// Logisim project 8位奇校验.circ as structural Verilog: 2 circuits, main circuit 8位奇校验编码电路
module \_8位奇校验编码电路  (
  input  [7:0] \原始数据 ,
  output [8:0] \奇校验编码 
);

  wire xor_1_out, xor_2_out, xor_3_out, xor_4_out, xor_5_out, xor_6_out, xor_7_out;

  xor xor_1 (xor_1_out, \原始数据 [0], \原始数据 [1]);
  xor xor_2 (xor_2_out, \原始数据 [2], \原始数据 [3]);
  xor xor_3 (xor_3_out, \原始数据 [4], \原始数据 [5]);
  xor xor_4 (xor_4_out, \原始数据 [6], \原始数据 [7]);
  xor xor_5 (xor_5_out, xor_1_out, xor_2_out);
  xor xor_6 (xor_6_out, xor_3_out, xor_4_out);
  xor xor_7 (xor_7_out, xor_5_out, xor_6_out);
  not not_1 (\奇校验编码 [8], xor_7_out);

  assign \奇校验编码 [7:0] = \原始数据 ;

  // Other names for the same wires on the sheet: D1 = \原始数据 [0]; Data[7:0] = \原始数据 ; 校验码[8:0] = {\奇校验编码 [8], \原始数据 };
  //   D2 = \原始数据 [1]; D3 = \原始数据 [2]; D4 = \原始数据 [3]; D5 = \原始数据 [4]; D6 = \原始数据 [5]; D7 = \原始数据 [6]; D8 = \原始数据 [7]

  // Notes on the sheet:
  //   输入引脚区
  //   请勿增改引脚，请勿修改子电路封装
  //   电路功能：实现8位数据位的奇校验编码，输入：8位数据；输出：9位校验码（数据位+校验位）
  //   8位奇校验编码电路
  //   请在下方利用上方输入输出引脚的隧道信号构建电路，ctrl+d复制选择部件
  //   输出引脚区
endmodule

module \_9位奇校验码检错电路  (
  input  [8:0] \奇校验编码 ,
  output \检错位 ,
  output [7:0] \数据位 
);

  wire not_1_out, xor_1_out, xor_2_out, xor_3_out, xor_4_out, xor_5_out, xor_6_out, xor_7_out;

  xor xor_1 (xor_1_out, \奇校验编码 [0], \奇校验编码 [1]);
  xor xor_2 (xor_2_out, \奇校验编码 [2], \奇校验编码 [3]);
  xor xor_3 (xor_3_out, \奇校验编码 [4], \奇校验编码 [5]);
  xor xor_4 (xor_4_out, \奇校验编码 [6], \奇校验编码 [7]);
  not not_1 (not_1_out, \奇校验编码 [8]);
  xor xor_5 (xor_5_out, xor_1_out, xor_2_out);
  xor xor_6 (xor_6_out, xor_3_out, xor_4_out);
  xor xor_7 (xor_7_out, xor_5_out, xor_6_out);
  xor xor_8 (\检错位 , xor_7_out, not_1_out);

  assign \数据位  = \奇校验编码 [7:0];

  // Other names for the same wires on the sheet: D1 = \奇校验编码 [0]; 奇校验码[8:0] = \奇校验编码 ; D2 = \奇校验编码 [1];
  //   D3 = \奇校验编码 [2]; D4 = \奇校验编码 [3]; D5 = \奇校验编码 [4]; D6 = \奇校验编码 [5]; D7 = \奇校验编码 [6]; D8 = \奇校验编码 [7];
  //   P1 = \奇校验编码 [8]

  // Notes on the sheet:
  //   输入引脚区
  //   请勿增改引脚，请勿修改子电路封装
  //   电路功能：实现9位奇校验编码的检错以及数据提取。输入：9位校验码；输出：检错位、数据位
  //   9位奇校验检错电路
  //   请在下方利用上方输入输出引脚的隧道信号构建电路，ctrl+d复制选择部件
  //   输出引脚区
endmodule
