// Logisim project Logisim使用.circ as structural Verilog: 9 circuits, main circuit 门电路
module \门电路  (
  input  in_1,
  input  in_2,
  input  in_3,
  input  in_4,
  input  in_5,
  input  \_2__门电路_6_异或门 ,
  input  in_7,
  input  in_8,
  input  in_9,
  input  in_10,
  input  in_11,
  input  in_12,
  input  in_13,
  output out_14,
  output out_15,
  output out_16,
  output out_17,
  output out_18,
  output out_19,
  output out_20
);

  and and_1 (out_14, in_1, in_3);
  or or_1 (out_16, in_5, in_7);
  not not_1 (out_18, in_9);
  nand nand_1 (out_20, in_12, in_13);
  nor nor_1 (out_15, in_2, in_4);
  xor xor_1 (out_17, \_2__门电路_6_异或门 , in_8);
  xnor xnor_1 (out_19, in_10, in_11);

  // Notes on the sheet:
  //   2. 门电路(1:与门)
  //   2. 门电路(2:或门)
  //   2. 门电路(3:非门)
  //   2. 门电路(4:与非门)
  //   2. 门电路(5:或非门)
  //   2. 门电路(7:同或门)
endmodule

module \隧道  (
  input  \_3__隧道 ,
  input  in_2,
  output out_3
);

  and and_1 (out_3, \_3__隧道 , in_2);

  // Other names for the same wires on the sheet: A = \_3__隧道 ; B = in_2; Y = out_3
endmodule

module \探针  (
  input  in_1,
  input  in_2,
  output out_3
);

  // Probe on in_1
  // Probe on in_2
  xor xor_1 (out_3, in_1, in_2);
  // Probe on out_3

  // Notes on the sheet:
  //   4. 探针
endmodule

module \常量  (
  output out_1
);

  and and_1 (out_1, 1'b0, 1'b1);

  // Notes on the sheet:
  //   5. 常量
endmodule

module \多位情况  (
  input  [7:0] A,
  input  [7:0] B,
  output [7:0] Y
);

  // Probe on A
  assign Y = A ^ B;  // XOR_Gate xor_1, 8 bits wide
  // Probe on B
  // Probe on Y

  // Notes on the sheet:
  //   6. 多位情况
endmodule

module \分线器  (
  input  [3:0] in_1,
  input  [7:0] in_2,
  input  in_3,
  input  in_4,
  input  in_5,
  input  in_6,
  output out_7,
  output [3:0] out_8,
  output out_9,
  output out_10,
  output [3:0] out_11,
  output out_12,
  output [3:0] out_13
);


  assign out_7 = in_1[0];
  assign out_8 = in_2[3:0];
  assign out_9 = in_1[1];
  assign out_10 = in_1[2];
  assign out_11 = in_2[7:4];
  assign out_12 = in_1[3];
  assign out_13 = {in_6, in_5, in_4, in_3};

  // Notes on the sheet:
  //   7. 分线器（输入）
  //   7. 分线器（输出）
  //   7. 分线器（拼接）
endmodule

module \输入输出  (
  input  \_1__输入输出 ,
  output out_2
);
endmodule

module \电路封装  (
  input  A,
  input  B,
  output Y
);

  wire and_1_out, and_2_out, not_1_out, not_2_out;

  not not_1 (not_1_out, B);
  and and_1 (and_1_out, not_1_out, A);
  not not_2 (not_2_out, A);
  and and_2 (and_2_out, not_2_out, B);
  or or_1 (Y, and_1_out, and_2_out);

  // Notes on the sheet:
  //   8、电路封装
  //   Y=A异或B=A与/B+/A与B
endmodule

module \电路封装应用  (
  input  \_9_电路封装的应用 ,
  input  in_2,
  output out_3
);

  \电路封装  \u_电路封装_1  (.A(\_9_电路封装的应用 ), .Y(out_3), .B(in_2));
endmodule
