// Logisim project 汉字编码实验.circ as structural Verilog: 1 circuit, main circuit 汉字编码实验
module \汉字编码实验  (
  input  \控制端 
);

  wire \时钟_out ;
  wire [6:0] \国标码转区位码电路_1_位号 , \国标码转区位码电路_1_区号 ;
  wire [7:0] counter_1_q;
  wire [15:0] rom_1_data;
  wire [31:0] \字库电路_1_out_3 , \字库电路_1_out_4 , \字库电路_1_out_5 , \字库电路_1_out_6 , \字库电路_1_out_7 , \字库电路_1_out_8 ,
       \字库电路_1_out_9 , \字库电路_1_out_10 , \字库电路_1_out_11 , \字库电路_1_out_12 , \字库电路_1_out_13 , \字库电路_1_out_14 ,
       \字库电路_1_out_15 , \字库电路_1_out_16 , \字库电路_1_out_17 , \字库电路_1_out_18 , \字库电路_1_out_19 , \字库电路_1_out_20 ,
       \字库电路_1_out_21 , \字库电路_1_out_22 , \字库电路_1_out_23 , \字库电路_1_out_24 , \字库电路_1_out_25 , \字库电路_1_out_26 ,
       \字库电路_1_out_27 , \字库电路_1_out_28 , \字库电路_1_out_29 , \字库电路_1_out_30 , \字库电路_1_out_31 , \字库电路_1_out_32 ,
       \字库电路_1_out_33 , \字库电路_1_out_34 ;

  Counter #(.behavior("old")) counter_1 (
    .load(1'b0), .D({8{1'b0}}), .count(1'b1), .Q(counter_1_q), .clk(\时钟_out ), .clr(\控制端 ), .preset(1'b0));  // open: carry
  Clock \u_时钟  (.out(\时钟_out ));
  ROM #(.dataWidth(16), .Select("high")) rom_1 (.addr(counter_1_q), .data(rom_1_data));
  \国标码转区位码电路  \u_国标码转区位码电路_1  (.\位号 (\国标码转区位码电路_1_位号 ), .\区号 (\国标码转区位码电路_1_区号 ), .GB2312(rom_1_data));
  \字库电路  \u_字库电路_1  (
    .out_3(\字库电路_1_out_3 ), .out_4(\字库电路_1_out_4 ), .out_5(\字库电路_1_out_5 ), .out_6(\字库电路_1_out_6 ),
    .out_7(\字库电路_1_out_7 ), .out_8(\字库电路_1_out_8 ), .out_9(\字库电路_1_out_9 ), .out_10(\字库电路_1_out_10 ),
    .out_11(\字库电路_1_out_11 ), .out_12(\字库电路_1_out_12 ), .out_13(\字库电路_1_out_13 ), .out_14(\字库电路_1_out_14 ),
    .out_15(\字库电路_1_out_15 ), .out_16(\字库电路_1_out_16 ), .out_17(\字库电路_1_out_17 ), .out_18(\字库电路_1_out_18 ),
    .out_19(\字库电路_1_out_19 ), .out_20(\字库电路_1_out_20 ), .out_21(\字库电路_1_out_21 ), .out_22(\字库电路_1_out_22 ),
    .out_23(\字库电路_1_out_23 ), .out_24(\字库电路_1_out_24 ), .out_25(\字库电路_1_out_25 ), .out_26(\字库电路_1_out_26 ),
    .out_27(\字库电路_1_out_27 ), .out_28(\字库电路_1_out_28 ), .out_29(\字库电路_1_out_29 ), .out_30(\字库电路_1_out_30 ),
    .out_31(\字库电路_1_out_31 ), .out_32(\字库电路_1_out_32 ), .out_33(\字库电路_1_out_33 ), .out_34(\字库电路_1_out_34 ),
    .\区号 (\国标码转区位码电路_1_区号 ), .\位号 (\国标码转区位码电路_1_位号 ));
  DotMatrix #(.inputtype("row"), .matrixcols(32), .matrixrows(32), .dotshape("circle")) dotmatrix_1 (
    .row0(\字库电路_1_out_3 ), .row1(\字库电路_1_out_4 ), .row2(\字库电路_1_out_5 ), .row3(\字库电路_1_out_6 ),
    .row4(\字库电路_1_out_7 ), .row5(\字库电路_1_out_8 ), .row6(\字库电路_1_out_9 ), .row7(\字库电路_1_out_10 ),
    .row8(\字库电路_1_out_11 ), .row9(\字库电路_1_out_12 ), .row10(\字库电路_1_out_13 ), .row11(\字库电路_1_out_14 ),
    .row12(\字库电路_1_out_15 ), .row13(\字库电路_1_out_16 ), .row14(\字库电路_1_out_17 ), .row15(\字库电路_1_out_18 ),
    .row16(\字库电路_1_out_19 ), .row17(\字库电路_1_out_20 ), .row18(\字库电路_1_out_21 ), .row19(\字库电路_1_out_22 ),
    .row20(\字库电路_1_out_23 ), .row21(\字库电路_1_out_24 ), .row22(\字库电路_1_out_25 ), .row23(\字库电路_1_out_26 ),
    .row24(\字库电路_1_out_27 ), .row25(\字库电路_1_out_28 ), .row26(\字库电路_1_out_29 ), .row27(\字库电路_1_out_30 ),
    .row28(\字库电路_1_out_31 ), .row29(\字库电路_1_out_32 ), .row30(\字库电路_1_out_33 ), .row31(\字库电路_1_out_34 ));

  // Notes on the sheet:
  //   计数器
  //   按2次时钟，计数器增加1
  //   GB2312
  //   ROM存储器中存放汉字的国标码(GB2312)
  //   contents of rom_1 (hex, n*v repeats v):
  //   b1b1 bea9 b6ac b0c2 bbe1 b6ac b2d0 b0c2 bbe1 b3c9 b9a6 bed9 d0d0
  //   先按计数器的控制端，使其变为1，则计数器清零；再按计数器的控制端，使其变为0，则计数器处于工作状态
  //   汉字GB2312编码实验
endmodule
