// Logisim project 第二次实验——运算器实验.circ as structural Verilog: 21 circuits, main circuit 8位原码一位乘法器
// CAS
module \_8位串行可控加减法器  (
  input  [7:0] X,
  input  [7:0] Y,
  input  Sub,
  output [7:0] S,
  output Cout,
  output out_6
);

  wire \n1位全加器fa封装1_1_cout , \n1位全加器fa封装1_3_cout , \n1位全加器fa封装1_4_cout , \n1位全加器fa封装1_5_cout ,
       \n1位全加器fa封装1_6_cout , \n1位全加器fa封装1_7_cout , \n1位全加器fa封装1_8_cout , xor_2_out, xor_3_out, xor_4_out,
       xor_5_out, xor_6_out, xor_7_out, xor_8_out, xor_9_out;
  wire [8:0] \运算指示 ;

  Multiplexer #(.width(9), .enable("false")) multiplexer_1 (.in0(9'hba), .in1(9'h92), .out(\运算指示 ), .sel(Sub));
  xor xor_1 (out_6, Cout, \n1位全加器fa封装1_1_cout );
  \_1位全加器FA封装1  \u_1位全加器fa封装1_1  (
    .Cout(\n1位全加器fa封装1_1_cout ), .Si(S[6]), .Cin(\n1位全加器fa封装1_3_cout ), .Xi(X[6]), .Yi(xor_3_out));
  \_1位全加器FA封装1  \u_1位全加器fa封装1_2  (.Cout(Cout), .Si(S[7]), .Cin(\n1位全加器fa封装1_1_cout ), .Xi(X[7]), .Yi(xor_2_out));
  xor xor_2 (xor_2_out, Sub, Y[7]);
  xor xor_3 (xor_3_out, Sub, Y[6]);
  \_1位全加器FA封装1  \u_1位全加器fa封装1_3  (
    .Cout(\n1位全加器fa封装1_3_cout ), .Si(S[5]), .Cin(\n1位全加器fa封装1_4_cout ), .Xi(X[5]), .Yi(xor_4_out));
  xor xor_4 (xor_4_out, Sub, Y[5]);
  \_1位全加器FA封装1  \u_1位全加器fa封装1_4  (
    .Cout(\n1位全加器fa封装1_4_cout ), .Si(S[4]), .Cin(\n1位全加器fa封装1_5_cout ), .Xi(X[4]), .Yi(xor_5_out));
  xor xor_5 (xor_5_out, Sub, Y[4]);
  \_1位全加器FA封装1  \u_1位全加器fa封装1_5  (
    .Cout(\n1位全加器fa封装1_5_cout ), .Si(S[3]), .Cin(\n1位全加器fa封装1_7_cout ), .Xi(X[3]), .Yi(xor_7_out));
  xor xor_6 (xor_6_out, Sub, Y[2]);
  xor xor_7 (xor_7_out, Sub, Y[3]);
  \_1位全加器FA封装1  \u_1位全加器fa封装1_6  (
    .Cout(\n1位全加器fa封装1_6_cout ), .Si(S[1]), .Cin(\n1位全加器fa封装1_8_cout ), .Xi(X[1]), .Yi(xor_8_out));
  \_1位全加器FA封装1  \u_1位全加器fa封装1_7  (
    .Cout(\n1位全加器fa封装1_7_cout ), .Si(S[2]), .Cin(\n1位全加器fa封装1_6_cout ), .Xi(X[2]), .Yi(xor_6_out));
  xor xor_8 (xor_8_out, Sub, Y[1]);
  // Probe on X
  // Probe on Y
  // Probe on S
  \_1位全加器FA封装1  \u_1位全加器fa封装1_8  (.Cout(\n1位全加器fa封装1_8_cout ), .Si(S[0]), .Cin(Sub), .Xi(X[0]), .Yi(xor_9_out));
  xor xor_9 (xor_9_out, Sub, Y[0]);
  DotMatrix #(.matrixcols(3), .matrixrows(3)) dotmatrix_1 (.col0(\运算指示 [8:6]), .col1(\运算指示 [5:3]), .col2(\运算指示 [2:0]));
  // Probe on X
  // Probe on Y
  // Probe on S

  // Other names for the same wires on the sheet: OF = out_6

  // Notes on the sheet:
  //   Y: pull=down
  //   S: pull=down
  //   Cout: pull=down
  //   out_6: pull=down
  //   Sub: pull=down
  //   X: pull=down
  //   8位可控加减法器
  //   输入引脚区
  //   输出引脚区
  //   功能说明：  8位可控加减法器    Sub=0: S = X＋Y  Sub=1:S = X－Y   Cout为最高位进位位，Overflow为有符号溢出标志
  //   8位串行可控加减法器
  //   有符号
  //   =
  //   无符号
endmodule

// CLA74182
module \_4位先行进位电路_CLA74182  (
  input  G4,
  input  P4,
  input  G3,
  input  P3,
  input  G2,
  input  P2,
  input  G1,
  input  P1,
  input  Cin,
  output C4,
  output C3,
  output C2,
  output C1,
  output G_star,
  output P_star
);

  wire and_2_out, and_3_out, and_4_out, and_5_out, and_6_out, and_7_out, and_8_out, and_9_out, and_10_out,
       and_11_out;

  and and_1 (P_star, P4, P3, P2, P1);
  or or_1 (G_star, G4, and_2_out, and_3_out, and_4_out);
  and and_2 (and_2_out, P4, G3);
  and and_3 (and_3_out, P4, P3, G2);
  or or_2 (C4, G4, and_2_out, and_3_out, and_4_out, and_5_out);
  and and_4 (and_4_out, P4, P3, P2, G1);
  and and_5 (and_5_out, P4, P3, P2, P1, Cin);
  or or_3 (C3, G3, and_6_out, and_8_out, and_7_out);
  and and_6 (and_6_out, P3, G2);
  and and_7 (and_7_out, P3, P2, P1, Cin);
  and and_8 (and_8_out, P3, P2, G1);
  or or_4 (C2, G2, and_9_out, and_10_out);
  and and_9 (and_9_out, P2, G1);
  and and_10 (and_10_out, P2, P1, Cin);
  or or_5 (C1, G1, and_11_out);
  and and_11 (and_11_out, P1, Cin);

  // Notes on the sheet:
  //   P2: pull=down
  //   P3: pull=down
  //   P4: pull=down
  //   Cin: pull=down
  //   G1: pull=down
  //   G3: pull=down
  //   G2: pull=down
  //   G4: pull=down
  //   P1: pull=down
  //   输入引脚区
  //   请根据以上引脚以及隧道信号设计完成74LS182先行进位电路，尽可能使用多输入逻辑门，并分析电路延迟
  //   4位先行进位电路（CLA74182）
  //   输出引脚区
endmodule

module \_4位快速加法器  (
  input  [3:0] X,
  input  [3:0] Y,
  input  C0,
  output [3:0] S,
  output C4,
  output C3,
  output G_star,
  output P_star
);

  wire and_1_out, and_2_out, and_3_out, and_4_out, \n4位先行进位电路_cla74182_1_c1 , \n4位先行进位电路_cla74182_1_c2 ,
       xor_2_out, xor_3_out, xor_5_out, xor_8_out;

  \_4位先行进位电路_CLA74182  \u_4位先行进位电路_cla74182_1  (
    .G4(and_1_out), .P4(xor_2_out), .G3(and_2_out), .P3(xor_3_out), .G2(and_3_out), .P2(xor_5_out),
    .G1(and_4_out), .P1(xor_8_out), .Cin(C0), .C4(C4), .C3(C3), .C2(\n4位先行进位电路_cla74182_1_c2 ),
    .C1(\n4位先行进位电路_cla74182_1_c1 ), .G_star(G_star), .P_star(P_star));
  and and_1 (and_1_out, X[3], Y[3]);
  xor xor_1 (S[3], C3, xor_2_out);
  xor xor_2 (xor_2_out, X[3], Y[3]);
  xor xor_3 (xor_3_out, X[2], Y[2]);
  and and_2 (and_2_out, X[2], Y[2]);
  xor xor_4 (S[2], \n4位先行进位电路_cla74182_1_c2 , xor_3_out);
  and and_3 (and_3_out, X[1], Y[1]);
  xor xor_5 (xor_5_out, X[1], Y[1]);
  xor xor_6 (S[1], \n4位先行进位电路_cla74182_1_c1 , xor_5_out);
  and and_4 (and_4_out, X[0], Y[0]);
  // Probe on X
  // Probe on Y
  // Probe on S
  xor xor_7 (S[0], xor_8_out, C0);
  xor xor_8 (xor_8_out, X[0], Y[0]);
  // Probe on X
  // Probe on Y
  // Probe on S

  // Notes on the sheet:
  //   C0: pull=down
  //   X: pull=down
  //   Y: pull=down
  //   输入引脚区
  //   4位快速加法器
  //   输出引脚区
  //   功能说明:4位Adder  S=X+Y，C4、C3分别为最高位、次高位进位位，C0为进位输入， G* P*为成组进位生成传递函数
  //   4位快速加法器
  //   +
  //   =
  //   有符号加法
  //   +
  //   =
  //   无符号加法
endmodule

// 32位加法器
module \_32位快速加法器  (
  input  C0,
  input  [31:0] X,
  input  [31:0] Y,
  output C32,
  output C31,
  output [31:0] S
);

  wire \n4位先行进位电路_cla74182_1_c1 , \n4位先行进位电路_cla74182_1_c2 , \n4位先行进位电路_cla74182_1_c3 ,
       \n4位先行进位电路_cla74182_2_c1 , \n4位先行进位电路_cla74182_2_c2 , \n4位先行进位电路_cla74182_2_c3 ,
       \n4位先行进位电路_cla74182_2_c4 , \n4位快速加法器_1_g_star , \n4位快速加法器_1_p_star , \n4位快速加法器_2_g_star ,
       \n4位快速加法器_2_p_star , \n4位快速加法器_3_g_star , \n4位快速加法器_3_p_star , \n4位快速加法器_4_g_star ,
       \n4位快速加法器_4_p_star , \n4位快速加法器_5_g_star , \n4位快速加法器_5_p_star , \n4位快速加法器_6_g_star ,
       \n4位快速加法器_6_p_star , \n4位快速加法器_7_g_star , \n4位快速加法器_7_p_star , \n4位快速加法器_8_g_star ,
       \n4位快速加法器_8_p_star ;

  \_4位先行进位电路_CLA74182  \u_4位先行进位电路_cla74182_1  (
    .G4(\n4位快速加法器_1_g_star ), .P4(\n4位快速加法器_1_p_star ), .G3(\n4位快速加法器_2_g_star ), .P3(\n4位快速加法器_2_p_star ),
    .G2(\n4位快速加法器_3_g_star ), .P2(\n4位快速加法器_3_p_star ), .G1(\n4位快速加法器_4_g_star ), .P1(\n4位快速加法器_4_p_star ),
    .Cin(\n4位先行进位电路_cla74182_2_c4 ), .C3(\n4位先行进位电路_cla74182_1_c3 ), .C2(\n4位先行进位电路_cla74182_1_c2 ),
    .C1(\n4位先行进位电路_cla74182_1_c1 ));  // open: C4, G_star, P_star
  \_4位快速加法器  \u_4位快速加法器_1  (
    .X(X[31:28]), .Y(Y[31:28]), .C0(\n4位先行进位电路_cla74182_1_c3 ), .S(S[31:28]), .C4(C32),
    .G_star(\n4位快速加法器_1_g_star ), .P_star(\n4位快速加法器_1_p_star ), .C3(C31));
  \_4位快速加法器  \u_4位快速加法器_2  (
    .X(X[27:24]), .Y(Y[27:24]), .C0(\n4位先行进位电路_cla74182_1_c2 ), .S(S[27:24]), .G_star(\n4位快速加法器_2_g_star ),
    .P_star(\n4位快速加法器_2_p_star ));  // open: C4, C3
  \_4位快速加法器  \u_4位快速加法器_3  (
    .X(X[23:20]), .Y(Y[23:20]), .C0(\n4位先行进位电路_cla74182_1_c1 ), .S(S[23:20]), .G_star(\n4位快速加法器_3_g_star ),
    .P_star(\n4位快速加法器_3_p_star ));  // open: C4, C3
  // Probe on X
  // Probe on Y
  // Probe on S
  \_4位快速加法器  \u_4位快速加法器_4  (
    .X(X[19:16]), .Y(Y[19:16]), .C0(\n4位先行进位电路_cla74182_2_c4 ), .S(S[19:16]), .G_star(\n4位快速加法器_4_g_star ),
    .P_star(\n4位快速加法器_4_p_star ));  // open: C4, C3
  \_4位先行进位电路_CLA74182  \u_4位先行进位电路_cla74182_2  (
    .G4(\n4位快速加法器_5_g_star ), .P4(\n4位快速加法器_5_p_star ), .G3(\n4位快速加法器_6_g_star ), .P3(\n4位快速加法器_6_p_star ),
    .G2(\n4位快速加法器_7_g_star ), .P2(\n4位快速加法器_7_p_star ), .G1(\n4位快速加法器_8_g_star ), .P1(\n4位快速加法器_8_p_star ),
    .C4(\n4位先行进位电路_cla74182_2_c4 ), .C3(\n4位先行进位电路_cla74182_2_c3 ), .C2(\n4位先行进位电路_cla74182_2_c2 ),
    .C1(\n4位先行进位电路_cla74182_2_c1 ));  // open: Cin, G_star, P_star
  // Probe on X
  // Probe on Y
  // Probe on S
  \_4位快速加法器  \u_4位快速加法器_5  (
    .X(X[15:12]), .Y(Y[15:12]), .C0(\n4位先行进位电路_cla74182_2_c3 ), .S(S[15:12]), .G_star(\n4位快速加法器_5_g_star ),
    .P_star(\n4位快速加法器_5_p_star ));  // open: C4, C3
  \_4位快速加法器  \u_4位快速加法器_6  (
    .X(X[11:8]), .Y(Y[11:8]), .C0(\n4位先行进位电路_cla74182_2_c2 ), .S(S[11:8]), .G_star(\n4位快速加法器_6_g_star ),
    .P_star(\n4位快速加法器_6_p_star ));  // open: C4, C3
  \_4位快速加法器  \u_4位快速加法器_7  (
    .X(X[7:4]), .Y(Y[7:4]), .C0(\n4位先行进位电路_cla74182_2_c1 ), .S(S[7:4]), .G_star(\n4位快速加法器_7_g_star ),
    .P_star(\n4位快速加法器_7_p_star ));  // open: C4, C3
  \_4位快速加法器  \u_4位快速加法器_8  (
    .X(X[3:0]), .Y(Y[3:0]), .C0(C0), .S(S[3:0]), .G_star(\n4位快速加法器_8_g_star ), .P_star(\n4位快速加法器_8_p_star ));  // open: C4, C3

  // Other names for the same wires on the sheet: S0[3:0] = S[3:0]; S1[3:0] = S[7:4]; S2[3:0] = S[11:8];
  //   S3[3:0] = S[15:12]; S4[3:0] = S[19:16]; S5[3:0] = S[23:20]; S6[3:0] = S[27:24]; S7[3:0] = S[31:28];
  //   X0[3:0] = X[3:0]; X1[3:0] = X[7:4]; X2[3:0] = X[11:8]; X3[3:0] = X[15:12]; X4[3:0] = X[19:16];
  //   X5[3:0] = X[23:20]; X6[3:0] = X[27:24]; X7[3:0] = X[31:28]; Y0[3:0] = Y[3:0]; Y1[3:0] = Y[7:4];
  //   Y2[3:0] = Y[11:8]; Y3[3:0] = Y[15:12]; Y4[3:0] = Y[19:16]; Y5[3:0] = Y[23:20]; Y6[3:0] = Y[27:24];
  //   Y7[3:0] = Y[31:28]

  // Notes on the sheet:
  //   C0: pull=down
  //   Y: pull=down
  //   X: pull=down
  //   输入引脚区
  //   功能说明：利用已完成的74182以及4位快速加法器构建速度最快的32位加法器 S = X ＋ Y，并分析电路延迟；
  //   输出引脚区
  //   +
  //   =
  //   有符号加法
  //   32位快速加法器
  //   +
  //   =
  //   无符号加法
  //   C32、C31分别为最高位、次高位进位位，C0为进位输入
endmodule

// 5位阵列乘法器
module \_5位无符号阵列乘法器__横向  (
  input  [4:0] X,
  input  [4:0] Y,
  output [9:0] \乘积 
);

  wire \n1位全加器fa封装2_2_cout , \n1位全加器fa封装2_2_si , \n1位全加器fa封装2_3_cout , \n1位全加器fa封装2_4_cout ,
       \n1位全加器fa封装2_4_si , \n1位全加器fa封装2_5_cout , \n1位全加器fa封装2_5_si , \n1位全加器fa封装2_6_cout ,
       \n1位全加器fa封装2_7_cout , \n1位全加器fa封装2_7_si , \n1位全加器fa封装2_8_cout , \n1位全加器fa封装2_8_si ,
       \n1位全加器fa封装2_9_cout , \n1位全加器fa封装2_9_si , \n1位全加器fa封装2_10_cout , \n1位全加器fa封装2_11_cout ,
       \n1位全加器fa封装2_11_si , \n1位全加器fa封装2_12_cout , \n1位全加器fa封装2_12_si , \n1位全加器fa封装2_13_cout ,
       \n1位全加器fa封装2_13_si , \n1位全加器fa封装2_14_cout , \n1位全加器fa封装2_15_cout , \n1位全加器fa封装2_15_si ,
       \n1位全加器fa封装2_16_cout , \n1位全加器fa封装2_16_si , \n1位全加器fa封装2_17_cout , \n1位全加器fa封装2_18_cout ,
       \n1位全加器fa封装2_18_si , \n1位全加器fa封装2_19_cout , \n1位全加器fa封装2_20_cout , X0Y1, X0Y2, X0Y3, X0Y4, X1Y0, X1Y1,
       X1Y2, X1Y3, X1Y4, X2Y0, X2Y1, X2Y2, X2Y3, X2Y4, X3Y0, X3Y1, X3Y2, X3Y3, X3Y4, X4Y0, X4Y1, X4Y2, X4Y3,
       X4Y4;

  \_1位全加器FA封装2  \u_1位全加器fa封装2_1  (
    .Cout(\乘积 [9]), .Si(\乘积 [8]), .Cin(X4Y4), .Xi(\n1位全加器fa封装2_3_cout ), .Yi(\n1位全加器fa封装2_2_cout ));
  \与门阵列  \u_与门阵列_1  (
    .X(X), .XY4({X4Y4, X3Y4, X2Y4, X1Y4, X0Y4}), .XY3({X4Y3, X3Y3, X2Y3, X1Y3, X0Y3}),
    .XY2({X4Y2, X3Y2, X2Y2, X1Y2, X0Y2}), .XY1({X4Y1, X3Y1, X2Y1, X1Y1, X0Y1}),
    .XY0({X4Y0, X3Y0, X2Y0, X1Y0, \乘积 [0]}), .Y(Y));
  // Probe on X
  \_1位全加器FA封装2  \u_1位全加器fa封装2_2  (
    .Cout(\n1位全加器fa封装2_2_cout ), .Si(\n1位全加器fa封装2_2_si ), .Cin(X4Y3), .Xi(\n1位全加器fa封装2_5_cout ),
    .Yi(\n1位全加器fa封装2_4_cout ));
  \_1位全加器FA封装2  \u_1位全加器fa封装2_3  (
    .Cout(\n1位全加器fa封装2_3_cout ), .Si(\乘积 [7]), .Cin(X3Y4), .Xi(\n1位全加器fa封装2_6_cout ), .Yi(\n1位全加器fa封装2_2_si ));
  \_1位全加器FA封装2  \u_1位全加器fa封装2_4  (
    .Cout(\n1位全加器fa封装2_4_cout ), .Si(\n1位全加器fa封装2_4_si ), .Cin(X4Y2), .Xi(\n1位全加器fa封装2_8_cout ),
    .Yi(\n1位全加器fa封装2_7_cout ));
  \_1位全加器FA封装2  \u_1位全加器fa封装2_5  (
    .Cout(\n1位全加器fa封装2_5_cout ), .Si(\n1位全加器fa封装2_5_si ), .Cin(X3Y3), .Xi(\n1位全加器fa封装2_9_cout ),
    .Yi(\n1位全加器fa封装2_4_si ));
  \_1位全加器FA封装2  \u_1位全加器fa封装2_6  (
    .Cout(\n1位全加器fa封装2_6_cout ), .Si(\乘积 [6]), .Cin(X2Y4), .Xi(\n1位全加器fa封装2_10_cout ), .Yi(\n1位全加器fa封装2_5_si ));
  // Probe on Y
  \_1位全加器FA封装2  \u_1位全加器fa封装2_7  (
    .Cout(\n1位全加器fa封装2_7_cout ), .Si(\n1位全加器fa封装2_7_si ), .Cin(X4Y1), .Xi(\n1位全加器fa封装2_11_cout ), .Yi(1'b0));
  \_1位全加器FA封装2  \u_1位全加器fa封装2_8  (
    .Cout(\n1位全加器fa封装2_8_cout ), .Si(\n1位全加器fa封装2_8_si ), .Cin(X3Y2), .Xi(\n1位全加器fa封装2_12_cout ),
    .Yi(\n1位全加器fa封装2_7_si ));
  \_1位全加器FA封装2  \u_1位全加器fa封装2_9  (
    .Cout(\n1位全加器fa封装2_9_cout ), .Si(\n1位全加器fa封装2_9_si ), .Cin(X2Y3), .Xi(\n1位全加器fa封装2_13_cout ),
    .Yi(\n1位全加器fa封装2_8_si ));
  \_1位全加器FA封装2  \u_1位全加器fa封装2_10  (
    .Cout(\n1位全加器fa封装2_10_cout ), .Si(\乘积 [5]), .Cin(X1Y4), .Xi(\n1位全加器fa封装2_14_cout ),
    .Yi(\n1位全加器fa封装2_9_si ));
  \_1位全加器FA封装2  \u_1位全加器fa封装2_11  (
    .Cout(\n1位全加器fa封装2_11_cout ), .Si(\n1位全加器fa封装2_11_si ), .Cin(X3Y1), .Xi(\n1位全加器fa封装2_15_cout ), .Yi(X4Y0));
  \_1位全加器FA封装2  \u_1位全加器fa封装2_12  (
    .Cout(\n1位全加器fa封装2_12_cout ), .Si(\n1位全加器fa封装2_12_si ), .Cin(X2Y2), .Xi(\n1位全加器fa封装2_16_cout ),
    .Yi(\n1位全加器fa封装2_11_si ));
  \_1位全加器FA封装2  \u_1位全加器fa封装2_13  (
    .Cout(\n1位全加器fa封装2_13_cout ), .Si(\n1位全加器fa封装2_13_si ), .Cin(X1Y3), .Xi(\n1位全加器fa封装2_17_cout ),
    .Yi(\n1位全加器fa封装2_12_si ));
  \_1位全加器FA封装2  \u_1位全加器fa封装2_14  (
    .Cout(\n1位全加器fa封装2_14_cout ), .Si(\乘积 [4]), .Cin(X0Y4), .Xi(1'b0), .Yi(\n1位全加器fa封装2_13_si ));
  \_1位全加器FA封装2  \u_1位全加器fa封装2_15  (
    .Cout(\n1位全加器fa封装2_15_cout ), .Si(\n1位全加器fa封装2_15_si ), .Cin(X2Y1), .Xi(\n1位全加器fa封装2_18_cout ), .Yi(X3Y0));
  \_1位全加器FA封装2  \u_1位全加器fa封装2_16  (
    .Cout(\n1位全加器fa封装2_16_cout ), .Si(\n1位全加器fa封装2_16_si ), .Cin(X1Y2), .Xi(\n1位全加器fa封装2_19_cout ),
    .Yi(\n1位全加器fa封装2_15_si ));
  \_1位全加器FA封装2  \u_1位全加器fa封装2_17  (
    .Cout(\n1位全加器fa封装2_17_cout ), .Si(\乘积 [3]), .Cin(X0Y3), .Xi(1'b0), .Yi(\n1位全加器fa封装2_16_si ));
  // Probe on \乘积 
  \_1位全加器FA封装2  \u_1位全加器fa封装2_18  (
    .Cout(\n1位全加器fa封装2_18_cout ), .Si(\n1位全加器fa封装2_18_si ), .Cin(X1Y1), .Xi(\n1位全加器fa封装2_20_cout ), .Yi(X2Y0));
  \_1位全加器FA封装2  \u_1位全加器fa封装2_19  (
    .Cout(\n1位全加器fa封装2_19_cout ), .Si(\乘积 [2]), .Cin(X0Y2), .Xi(1'b0), .Yi(\n1位全加器fa封装2_18_si ));
  // Probe on X
  // Probe on Y
  // Probe on \乘积 
  \_1位全加器FA封装2  \u_1位全加器fa封装2_20  (.Cout(\n1位全加器fa封装2_20_cout ), .Si(\乘积 [1]), .Cin(X0Y1), .Xi(1'b0), .Yi(X1Y0));

  // Other names for the same wires on the sheet: P[9:0] = \乘积 ; P0 = \乘积 [0]; X0Y0 = \乘积 [0];
  //   XY0[4:0] = {X4Y0, X3Y0, X2Y0, X1Y0, \乘积 [0]}; P1 = \乘积 [1]; P2 = \乘积 [2]; P3 = \乘积 [3]; P4 = \乘积 [4];
  //   P5 = \乘积 [5]; P6 = \乘积 [6]; P7 = \乘积 [7]; P8 = \乘积 [8]; P9 = \乘积 [9]; XY1[4:0] = {X4Y1, X3Y1, X2Y1, X1Y1, X0Y1};
  //   XY2[4:0] = {X4Y2, X3Y2, X2Y2, X1Y2, X0Y2}; XY3[4:0] = {X4Y3, X3Y3, X2Y3, X1Y3, X0Y3};
  //   XY4[4:0] = {X4Y4, X3Y4, X2Y4, X1Y4, X0Y4}

  // Notes on the sheet:
  //   Y: pull=down
  //   X: pull=down
  //   输入引脚区
  //   功能说明：利用一位全加器构成5位×5位的无符号数阵列乘法器，乘积=X×Y，并分析电路延迟；
  //   输出引脚区
  //   5位无符号阵列乘法器（横向）
  //   ×
  //   =
endmodule

module \_8位无符号数一位乘法器  (
  input  [7:0] X,
  input  [7:0] Y,
  output [15:0] \乘积 
);

  wire comparator_1_eq, d_ff_1_q, not_1_out, RST, \时钟_out ;
  wire [0:0] \n8位串行加法器_1_s ;
  wire [3:0] counter_1_q;
  wire [7:0] multiplexer_1_out, multiplexer_2_out, \n8位串行加法器_1_cout ;

  // Probe on X
  Clock \u_时钟  (.out(\时钟_out ));
  // Probe on Y
  // Probe on \乘积 [15:8]
  Register #(.Select("low")) register_1 (
    .D(\n8位串行加法器_1_cout ), .en(not_1_out), .Q(\乘积 [15:8]), .clk(\时钟_out ), .clr(RST));
  \_8位串行加法器  \u_8位串行加法器_1  (
    .X(\乘积 [15:8]), .Y(multiplexer_1_out), .Cin(1'b0), .S({\n8位串行加法器_1_cout [6:0], \n8位串行加法器_1_s [0]}),
    .Cout(\n8位串行加法器_1_cout [7]));  // open: out_6
  Multiplexer #(.width(8), .enable("false")) multiplexer_1 (
    .in0({8{1'b0}}), .in1(X), .out(multiplexer_1_out), .sel(\乘积 [0]));
  Button \u_复位  (.out(RST));
  Multiplexer #(.width(8), .enable("false")) multiplexer_2 (
    .in0(Y), .in1({\n8位串行加法器_1_s [0], \乘积 [7:1]}), .out(multiplexer_2_out), .sel(d_ff_1_q));
  // Probe on \乘积 [7:0]
  Register #(.Select("low")) Y_2 (.D(multiplexer_2_out), .en(not_1_out), .Q(\乘积 [7:0]), .clk(\时钟_out ), .clr(RST));
  Counter #(.width(4), .max('hf), .behavior("old")) counter_1 (
    .count(not_1_out), .Q(counter_1_q), .clk(\时钟_out ), .clr(RST));  // open: load, D, carry, preset
  D_Flip_Flop #(.Pre_Clr_Positions("LEGACY"), .enable("true"), .NewFFLayout("false")) d_ff_1 (
    .clk(\时钟_out ), .D(1'b1), .Q(d_ff_1_q), .reset(RST));  // open: Qn, preset, en
  // Probe on \乘积 
  not not_1 (not_1_out, comparator_1_eq);
  Comparator #(.width(4), .mode("unsigned")) comparator_1 (
    .a(counter_1_q), .b(4'b1001), .eq(comparator_1_eq));  // open: gt, lt
  // Probe on X
  // Probe on Y
  // Probe on \乘积 

  // Notes on the sheet:
  //   ∑
  //   功能说明: 无符号一位乘法器   乘积=X*Y，要求采用原码一位乘法实现，最终结果能输出在乘积引脚上
  //   输入输出引脚区
  //   计数及移位控制
  //   8位无符号数一位乘法器
  //   ×
  //   =
  //   核心算法：{ ∑ , Y } = { ∑ ＋ Y  |X|  , Y  } / 2
  //   n
endmodule

module \_8位补码一位乘法器  (
  input  [7:0] X,
  input  [7:0] Y,
  output [15:0] \乘积 
);

  wire and_1_out, clock_1_out, comparator_1_eq, d_ff_1_q, not_2_out, RST, XYZ, XZ, YZ;
  wire [0:0] \n8位串行加法器_1_s_2 ;
  wire [1:0] PS;
  wire [1:1] Yn_1_2_q;
  wire [3:0] counter_1_q;
  wire [7:0] multiplexer_1_out, multiplexer_2_out, \n8位串行加法器_1_s , not_1_out;
  wire [14:0] PX_star, PY_star;
  wire [15:0] multiplexer_3_out, \乘积_star ;
  wire [15:15] negator_1_out, negator_2_out, PX;

  // Probe on X
  Clock clock_1 (.out(clock_1_out));
  // Probe on Y
  Register #(.Select("low")) register (
    .D({{2{\n8位串行加法器_1_s [7]}}, \n8位串行加法器_1_s [5:0]}), .en(not_2_out), .Q(\乘积_star [15:8]),
    .clk(clock_1_out), .clr(RST));
  Button \u_复位  (.out(RST));
  // Probe on \乘积_star [15:8]
  Multiplexer #(.width(8), .enable("false")) multiplexer_1 (
    .in0(Y), .in1({\n8位串行加法器_1_s_2 [0], \乘积_star [7:1]}), .out(multiplexer_1_out), .sel(d_ff_1_q));
  \_8位串行加法器  \u_8位串行加法器_1  (
    .X(\乘积_star [15:8]), .Y(multiplexer_2_out), .Cin(and_1_out),
    .S({\n8位串行加法器_1_s [7], \n8位串行加法器_1_s [5:0], \n8位串行加法器_1_s_2 [0]}));  // open: Cout, out_6
  Multiplexer #(.select(2), .width(8), .enable("false")) multiplexer_2 (
    .in0({8{1'b0}}), .in1(not_1_out), .in2(X), .in3({8{1'b0}}), .out(multiplexer_2_out),
    .sel({Yn_1_2_q[1], \乘积_star [0]}));
  assign not_1_out = ~X;  // NOT_Gate not_1, 8 bits wide
  // Probe on \乘积_star [7:0]
  Register #(.Select("low")) Y_2 (
    .D(multiplexer_1_out), .en(not_2_out), .Q(\乘积_star [7:0]), .clk(clock_1_out), .clr(RST));
  and and_1 (and_1_out, ~Yn_1_2_q[1], \乘积_star [0]);  // AND_Gate
  Counter #(.width(4), .max('hf), .behavior("old")) counter_1 (
    .count(not_2_out), .Q(counter_1_q), .clk(clock_1_out), .clr(RST));  // open: load, D, carry, preset
  // Probe on \乘积 
  // Probe on Yn_1_2_q[1]
  Register #(.width(1), .Select("low")) Yn_1_2 (
    .D(\乘积_star [0]), .en(not_2_out), .Q(Yn_1_2_q[1]), .clk(clock_1_out), .clr(RST));
  Comparator #(.width(4), .mode("unsigned")) comparator_1 (
    .a(counter_1_q), .b(4'b1001), .eq(comparator_1_eq));  // open: gt, lt
  D_Flip_Flop #(.Pre_Clr_Positions("LEGACY"), .enable("true"), .NewFFLayout("false")) d_ff_1 (
    .clk(clock_1_out), .D(1'b1), .Q(d_ff_1_q), .reset(RST));  // open: Qn, preset, en
  not not_2 (not_2_out, comparator_1_eq);
  xor xor_1 (PX[15], X[7], Y[7]);
  // Probe on X
  // Probe on Y
  // Probe on \乘积 
  Comparator comparator_2 (.a(X), .b(8'h80), .eq(PS[0]));  // open: gt, lt
  Comparator comparator_3 (.a(Y), .b(8'h80), .eq(PS[1]));  // open: gt, lt
  or or_1 (XZ, X[0], X[1], X[2], X[3], X[4], X[5], X[6], X[7]);
  Multiplexer #(.select(2), .width(16), .enable("false")) multiplexer_3 (
    .in0(\乘积_star ), .in1({PX[15], PY_star}), .in2({PX[15], PX_star}), .in3(16'h4000),
    .out(multiplexer_3_out), .sel(PS));
  or or_2 (YZ, Y[0], Y[1], Y[2], Y[3], Y[4], Y[5], Y[6], Y[7]);
  xor xor_2 (XYZ, XZ, YZ);
  Negator #(.width(16)) negator_1 (.in({PX[15], X, {7{1'b0}}}), .out({negator_1_out[15], PX_star}));
  Negator #(.width(16)) negator_2 (.in({PX[15], Y, {7{1'b0}}}), .out({negator_2_out[15], PY_star}));
  Multiplexer #(.width(16), .enable("false")) multiplexer_4 (
    .in0(multiplexer_3_out), .in1({16{1'b0}}), .out(\乘积 ), .sel(XYZ));

  // Other names for the same wires on the sheet: PX[14:7] = X; SX = X[7]; PY[15:7] = {PX[15], Y}; SY = Y[7];
  //   PX_star[15] = PX[15]; PY_star[15] = PX[15]; SP = PX[15]

  // Notes on the sheet:
  //   功能说明: 补码一位乘法器   乘积=X×Y，要求采用补码一位乘法实现，最终结果能输出在乘积引脚上
  //   输入输出引脚区
  //   计数及移位控制
  //   核心算法：{ ∑,Y } = { ∑ ＋（Y      －  Y  ）[X]   , Y } / 2
  //   8位补码一位乘法器
  //   ×
  //   =
  //   n
  //   n+1
  //   补
endmodule

// ALU
module \_32位ALU__算术逻辑单元  (
  input  [31:0] X,
  input  [31:0] Y,
  input  [3:0] AluOP,
  output Signed_Overflow,
  output UnSigned_Overflow,
  output Equal,
  output [31:0] Result,
  output [31:0] Result_2
);

  wire \n32位快速加法器_1_c31 , \n32位快速加法器_1_c32 , \n32位快速加法器_2_c31 , \n32位快速加法器_2_c32 , not_2_out, xor_2_out,
       xor_3_out;
  wire [0:0] comparator_1_lt, comparator_2_lt;
  wire [31:0] AND_out, divider_1_out, divider_1_rem, multiplier_1_cout, multiplier_1_out, \n32位快速加法器_1_s ,
       \n32位快速加法器_2_s , NOR_out, not_1_out, OR_out, shifter_1_out, shifter_2_out, shifter_3_out, XOR_out;

  // Probe on X
  // Probe on X
  assign not_1_out = ~Y;  // NOT_Gate not_1, 32 bits wide
  // Probe on Y
  // Probe on Y
  Shifter #(.width(32)) shifter_1 (.in(X), .\dist (Y[4:0]), .out(shifter_1_out));
  Shifter #(.width(32), .shift("ar")) shifter_2 (.in(X), .\dist (Y[4:0]), .out(shifter_2_out));
  Shifter #(.width(32), .shift("lr")) shifter_3 (.in(X), .\dist (Y[4:0]), .out(shifter_3_out));
  Multiplier #(.width(32)) multiplier_1 (.a(X), .b(Y), .out(multiplier_1_out), .cout(multiplier_1_cout));  // open: cin
  Divider #(.width(32)) divider_1 (.a(X), .b(Y), .out(divider_1_out), .rem(divider_1_rem));  // open: upper
  \_32位快速加法器  \u_32位快速加法器_1  (
    .X(X), .Y(Y), .C0(1'b0), .S(\n32位快速加法器_1_s ), .C32(\n32位快速加法器_1_c32 ), .C31(\n32位快速加法器_1_c31 ));
  \_32位快速加法器  \u_32位快速加法器_2  (
    .X(X), .Y(not_1_out), .C0(1'b1), .S(\n32位快速加法器_2_s ), .C32(\n32位快速加法器_2_c32 ), .C31(\n32位快速加法器_2_c31 ));
  assign AND_out = X & Y;  // AND_Gate AND, 32 bits wide
  assign OR_out = X | Y;  // OR_Gate OR, 32 bits wide
  assign XOR_out = X ^ Y;  // XOR_Gate XOR, 32 bits wide
  assign NOR_out = ~(X | Y);  // NOR_Gate NOR, 32 bits wide
  Comparator #(.width(32)) comparator_1 (.a(X), .b(Y), .eq(Equal), .lt(comparator_1_lt[0]));  // open: gt
  Comparator #(.width(32), .mode("unsigned")) comparator_2 (.a(X), .b(Y), .lt(comparator_2_lt[0]));  // open: gt, eq
  xor xor_2 (xor_2_out, \n32位快速加法器_1_c31 , \n32位快速加法器_1_c32 );
  xor xor_3 (xor_3_out, \n32位快速加法器_2_c31 , \n32位快速加法器_2_c32 );
  not not_2 (not_2_out, \n32位快速加法器_2_c32 );
  // Probe on AluOP
  // Probe on Result
  // Probe on Result
  Multiplexer #(.select(4), .width(32), .enable("false")) multiplexer_1 (
    .in0(shifter_1_out), .in1(shifter_2_out), .in2(shifter_3_out), .in3(multiplier_1_out),
    .in4(divider_1_out), .in5(\n32位快速加法器_1_s ), .in6(\n32位快速加法器_2_s ), .in7(AND_out), .in8(OR_out),
    .in9(XOR_out), .in10(NOR_out), .in11({{31{1'b0}}, comparator_1_lt[0]}),
    .in12({{31{1'b0}}, comparator_2_lt[0]}), .in13({32{1'b0}}), .in14({32{1'b0}}), .in15({32{1'b0}}),
    .out(Result), .sel(AluOP));
  Multiplexer #(.select(4), .width(32), .enable("false")) multiplexer_2 (
    .in0({32{1'b0}}), .in1({32{1'b0}}), .in2({32{1'b0}}), .in3(multiplier_1_cout), .in4(divider_1_rem),
    .in5({32{1'b0}}), .in6({32{1'b0}}), .in7({32{1'b0}}), .in8({32{1'b0}}), .in9({32{1'b0}}),
    .in10({32{1'b0}}), .in11({32{1'b0}}), .in12({32{1'b0}}), .in13({32{1'b0}}), .in14({32{1'b0}}),
    .in15({32{1'b0}}), .out(Result_2), .sel(AluOP));
  Multiplexer #(.select(4), .enable("false")) multiplexer_3 (
    .in0(1'b0), .in1(1'b0), .in2(1'b0), .in3(1'b0), .in4(1'b0), .in5(\n32位快速加法器_1_c32 ), .in6(not_2_out),
    .in7(1'b0), .in8(1'b0), .in9(1'b0), .in10(1'b0), .in11(1'b0), .in12(1'b0), .in13(1'b0), .in14(1'b0),
    .in15(1'b0), .out(UnSigned_Overflow), .sel(AluOP));
  Multiplexer #(.select(4), .enable("false")) multiplexer_4 (
    .in0(1'b0), .in1(1'b0), .in2(1'b0), .in3(1'b0), .in4(1'b0), .in5(xor_2_out), .in6(xor_3_out), .in7(1'b0),
    .in8(1'b0), .in9(1'b0), .in10(1'b0), .in11(1'b0), .in12(1'b0), .in13(1'b0), .in14(1'b0), .in15(1'b0),
    .out(Signed_Overflow), .sel(AluOP));
  // Probe on Result_2

  // Other names for the same wires on the sheet: OF = Signed_Overflow; Result2[31:0] = Result_2; S[3:0] = AluOP;
  //   UOF = UnSigned_Overflow

  // Notes on the sheet:
  //   AluOP: pull=down
  //   X: pull=down
  //   Y: pull=down
  //   不要改变此引脚区域内容，也不要改变ALU封装形式
  //   输入引脚
  //   请在下方利用上方输入输出引脚的隧道信号构建ALU电路，ctrl+d复制选择部件
  //   输出引脚
  //   探测区域
  //   32位ALU（算术逻辑单元）
endmodule

module \与门阵列  (
  input  [4:0] X,
  input  [4:0] Y,
  output [4:0] XY0,
  output [4:0] XY1,
  output [4:0] XY2,
  output [4:0] XY3,
  output [4:0] XY4
);

  and and_1 (XY0[4], X[4], Y[0]);
  and and_2 (XY1[4], X[4], Y[1]);
  and and_3 (XY2[4], X[4], Y[2]);
  and and_4 (XY3[4], X[4], Y[3]);
  and and_5 (XY4[4], X[4], Y[4]);
  and and_6 (XY0[3], X[3], Y[0]);
  and and_7 (XY1[3], X[3], Y[1]);
  and and_8 (XY2[3], X[3], Y[2]);
  and and_9 (XY3[3], X[3], Y[3]);
  and and_10 (XY4[3], X[3], Y[4]);
  and and_11 (XY0[2], X[2], Y[0]);
  and and_12 (XY1[2], X[2], Y[1]);
  and and_13 (XY2[2], X[2], Y[2]);
  and and_14 (XY3[2], X[2], Y[3]);
  and and_15 (XY4[2], X[2], Y[4]);
  and and_16 (XY0[1], X[1], Y[0]);
  and and_17 (XY0[0], X[0], Y[0]);
  and and_18 (XY1[1], X[1], Y[1]);
  and and_19 (XY1[0], X[0], Y[1]);
  and and_20 (XY2[1], X[1], Y[2]);
  and and_21 (XY2[0], X[0], Y[2]);
  and and_22 (XY3[1], X[1], Y[3]);
  and and_23 (XY3[0], X[0], Y[3]);
  and and_24 (XY4[0], X[0], Y[4]);
  and and_25 (XY4[1], X[1], Y[4]);

  // Other names for the same wires on the sheet: X0Y0 = XY0[0]; X1Y0 = XY0[1]; X2Y0 = XY0[2]; X3Y0 = XY0[3];
  //   X4Y0 = XY0[4]; X0Y1 = XY1[0]; X1Y1 = XY1[1]; X2Y1 = XY1[2]; X3Y1 = XY1[3]; X4Y1 = XY1[4]; X0Y2 = XY2[0];
  //   X1Y2 = XY2[1]; X2Y2 = XY2[2]; X3Y2 = XY2[3]; X4Y2 = XY2[4]; X0Y3 = XY3[0]; X1Y3 = XY3[1]; X2Y3 = XY3[2];
  //   X3Y3 = XY3[3]; X4Y3 = XY3[4]; X0Y4 = XY4[0]; X1Y4 = XY4[1]; X2Y4 = XY4[2]; X3Y4 = XY4[3]; X4Y4 = XY4[4]

  // Notes on the sheet:
  //   5位乘法与门阵列
endmodule

// FA
module \_1位全加器FA封装1  (
  input  Cin,
  input  Xi,
  input  Yi,
  output Cout,
  output Si
);

  wire AND_2_out, AND_out, XOR_2_out;

  or OR (Cout, AND_out, AND_2_out);
  and AND (AND_out, Xi, Yi);
  and AND_2 (AND_2_out, Cin, XOR_2_out);
  xor XOR (Si, Cin, XOR_2_out);
  xor XOR_2 (XOR_2_out, Xi, Yi);

  // Notes on the sheet:
  //   Yi: pull=down
  //   Xi: pull=down
  //   Cin: pull=down
  //   1位全加器（FA）
  //   Si = Xi ^ Yi ^ Cin
  //   Cout = Xi Yi + Cin (Xi ^ Yi)
endmodule

module \_1位全加器FA封装2  (
  input  Cin,
  input  Xi,
  input  Yi,
  output Cout,
  output Si
);

  wire AND_2_out, AND_out, XOR_2_out;

  or OR (Cout, AND_out, AND_2_out);
  and AND (AND_out, Xi, Yi);
  and AND_2 (AND_2_out, Cin, XOR_2_out);
  xor XOR (Si, Cin, XOR_2_out);
  xor XOR_2 (XOR_2_out, Xi, Yi);

  // Notes on the sheet:
  //   1位全加器（FA）
  //   Si = Xi ^ Yi ^ Cin
  //   Cout = Xi Yi + Cin (Xi ^ Yi)
endmodule

module \_8位串行加法器  (
  input  [7:0] X,
  input  [7:0] Y,
  input  Cin,
  output [7:0] S,
  output Cout,
  output out_6
);

  wire \n1位全加器fa封装1_2_cout , \n1位全加器fa封装1_3_cout , \n1位全加器fa封装1_4_cout , \n1位全加器fa封装1_5_cout ,
       \n1位全加器fa封装1_6_cout , \n1位全加器fa封装1_7_cout , \n1位全加器fa封装1_8_cout ;

  xor xor_1 (out_6, Cout, \n1位全加器fa封装1_2_cout );
  \_1位全加器FA封装1  \u_1位全加器fa封装1_1  (.Cout(Cout), .Si(S[7]), .Cin(\n1位全加器fa封装1_2_cout ), .Xi(X[7]), .Yi(Y[7]));
  \_1位全加器FA封装1  \u_1位全加器fa封装1_2  (
    .Cout(\n1位全加器fa封装1_2_cout ), .Si(S[6]), .Cin(\n1位全加器fa封装1_3_cout ), .Xi(X[6]), .Yi(Y[6]));
  \_1位全加器FA封装1  \u_1位全加器fa封装1_3  (
    .Cout(\n1位全加器fa封装1_3_cout ), .Si(S[5]), .Cin(\n1位全加器fa封装1_4_cout ), .Xi(X[5]), .Yi(Y[5]));
  \_1位全加器FA封装1  \u_1位全加器fa封装1_4  (
    .Cout(\n1位全加器fa封装1_4_cout ), .Si(S[4]), .Cin(\n1位全加器fa封装1_5_cout ), .Xi(X[4]), .Yi(Y[4]));
  \_1位全加器FA封装1  \u_1位全加器fa封装1_5  (
    .Cout(\n1位全加器fa封装1_5_cout ), .Si(S[3]), .Cin(\n1位全加器fa封装1_6_cout ), .Xi(X[3]), .Yi(Y[3]));
  \_1位全加器FA封装1  \u_1位全加器fa封装1_6  (
    .Cout(\n1位全加器fa封装1_6_cout ), .Si(S[2]), .Cin(\n1位全加器fa封装1_7_cout ), .Xi(X[2]), .Yi(Y[2]));
  // Probe on X
  // Probe on Y
  // Probe on S
  \_1位全加器FA封装1  \u_1位全加器fa封装1_7  (
    .Cout(\n1位全加器fa封装1_7_cout ), .Si(S[1]), .Cin(\n1位全加器fa封装1_8_cout ), .Xi(X[1]), .Yi(Y[1]));
  // Probe on X
  // Probe on Y
  // Probe on S
  \_1位全加器FA封装1  \u_1位全加器fa封装1_8  (.Cout(\n1位全加器fa封装1_8_cout ), .Si(S[0]), .Cin(Cin), .Xi(X[0]), .Yi(Y[0]));

  // Other names for the same wires on the sheet: OF = out_6

  // Notes on the sheet:
  //   Cin: pull=down
  //   X: pull=down
  //   Y: pull=down
  //   输入引脚区
  //   符号位
  //   8位串行加法器
  //   输出引脚区
  //   Overflow
  //   +
  //   有符号加法
  //   +
  //   =
  //   无符号加法
endmodule

// 阵列乘法器
module \_5位无符号阵列乘法器__斜向  (
  input  [4:0] X,
  input  [4:0] Y,
  output [9:0] \乘积 
);

  wire \n1位全加器fa封装2_2_cout , \n1位全加器fa封装2_2_si , \n1位全加器fa封装2_3_cout , \n1位全加器fa封装2_4_cout ,
       \n1位全加器fa封装2_4_si , \n1位全加器fa封装2_5_cout , \n1位全加器fa封装2_5_si , \n1位全加器fa封装2_6_cout ,
       \n1位全加器fa封装2_7_cout , \n1位全加器fa封装2_7_si , \n1位全加器fa封装2_8_cout , \n1位全加器fa封装2_8_si ,
       \n1位全加器fa封装2_9_cout , \n1位全加器fa封装2_9_si , \n1位全加器fa封装2_10_cout , \n1位全加器fa封装2_11_cout ,
       \n1位全加器fa封装2_11_si , \n1位全加器fa封装2_12_cout , \n1位全加器fa封装2_12_si , \n1位全加器fa封装2_13_cout ,
       \n1位全加器fa封装2_13_si , \n1位全加器fa封装2_14_cout , \n1位全加器fa封装2_15_cout , \n1位全加器fa封装2_15_si ,
       \n1位全加器fa封装2_16_cout , \n1位全加器fa封装2_16_si , \n1位全加器fa封装2_17_cout , \n1位全加器fa封装2_18_cout ,
       \n1位全加器fa封装2_18_si , \n1位全加器fa封装2_19_cout , \n1位全加器fa封装2_20_cout , X0Y1, X0Y2, X0Y3, X0Y4, X1Y0, X1Y1,
       X1Y2, X1Y3, X1Y4, X2Y0, X2Y1, X2Y2, X2Y3, X2Y4, X3Y0, X3Y1, X3Y2, X3Y3, X3Y4, X4Y0, X4Y1, X4Y2, X4Y3,
       X4Y4;

  \_1位全加器FA封装2  \u_1位全加器fa封装2_1  (
    .Cout(\乘积 [9]), .Si(\乘积 [8]), .Cin(\n1位全加器fa封装2_2_cout ), .Xi(\n1位全加器fa封装2_3_cout ), .Yi(X4Y4));
  \与门阵列  \u_与门阵列_1  (
    .X(X), .XY4({X4Y4, X3Y4, X2Y4, X1Y4, X0Y4}), .XY3({X4Y3, X3Y3, X2Y3, X1Y3, X0Y3}),
    .XY2({X4Y2, X3Y2, X2Y2, X1Y2, X0Y2}), .XY1({X4Y1, X3Y1, X2Y1, X1Y1, X0Y1}),
    .XY0({X4Y0, X3Y0, X2Y0, X1Y0, \乘积 [0]}), .Y(Y));
  // Probe on X
  \_1位全加器FA封装2  \u_1位全加器fa封装2_2  (
    .Cout(\n1位全加器fa封装2_2_cout ), .Si(\n1位全加器fa封装2_2_si ), .Cin(\n1位全加器fa封装2_4_cout ), .Xi(X3Y4), .Yi(X4Y3));
  \_1位全加器FA封装2  \u_1位全加器fa封装2_3  (
    .Cout(\n1位全加器fa封装2_3_cout ), .Si(\乘积 [7]), .Cin(\n1位全加器fa封装2_5_cout ), .Xi(\n1位全加器fa封装2_6_cout ),
    .Yi(\n1位全加器fa封装2_2_si ));
  \_1位全加器FA封装2  \u_1位全加器fa封装2_4  (
    .Cout(\n1位全加器fa封装2_4_cout ), .Si(\n1位全加器fa封装2_4_si ), .Cin(\n1位全加器fa封装2_7_cout ), .Xi(X3Y3), .Yi(X4Y2));
  \_1位全加器FA封装2  \u_1位全加器fa封装2_5  (
    .Cout(\n1位全加器fa封装2_5_cout ), .Si(\n1位全加器fa封装2_5_si ), .Cin(\n1位全加器fa封装2_8_cout ), .Xi(X2Y4),
    .Yi(\n1位全加器fa封装2_4_si ));
  \_1位全加器FA封装2  \u_1位全加器fa封装2_6  (
    .Cout(\n1位全加器fa封装2_6_cout ), .Si(\乘积 [6]), .Cin(\n1位全加器fa封装2_9_cout ), .Xi(\n1位全加器fa封装2_10_cout ),
    .Yi(\n1位全加器fa封装2_5_si ));
  // Probe on Y
  \_1位全加器FA封装2  \u_1位全加器fa封装2_7  (
    .Cout(\n1位全加器fa封装2_7_cout ), .Si(\n1位全加器fa封装2_7_si ), .Cin(\n1位全加器fa封装2_11_cout ), .Xi(X3Y2), .Yi(X4Y1));
  \_1位全加器FA封装2  \u_1位全加器fa封装2_8  (
    .Cout(\n1位全加器fa封装2_8_cout ), .Si(\n1位全加器fa封装2_8_si ), .Cin(\n1位全加器fa封装2_12_cout ), .Xi(X2Y3),
    .Yi(\n1位全加器fa封装2_7_si ));
  \_1位全加器FA封装2  \u_1位全加器fa封装2_9  (
    .Cout(\n1位全加器fa封装2_9_cout ), .Si(\n1位全加器fa封装2_9_si ), .Cin(\n1位全加器fa封装2_13_cout ), .Xi(X1Y4),
    .Yi(\n1位全加器fa封装2_8_si ));
  \_1位全加器FA封装2  \u_1位全加器fa封装2_10  (
    .Cout(\n1位全加器fa封装2_10_cout ), .Si(\乘积 [5]), .Cin(\n1位全加器fa封装2_14_cout ), .Xi(1'b0),
    .Yi(\n1位全加器fa封装2_9_si ));
  \_1位全加器FA封装2  \u_1位全加器fa封装2_11  (
    .Cout(\n1位全加器fa封装2_11_cout ), .Si(\n1位全加器fa封装2_11_si ), .Cin(1'b0), .Xi(X3Y1), .Yi(X4Y0));
  \_1位全加器FA封装2  \u_1位全加器fa封装2_12  (
    .Cout(\n1位全加器fa封装2_12_cout ), .Si(\n1位全加器fa封装2_12_si ), .Cin(\n1位全加器fa封装2_15_cout ), .Xi(X2Y2),
    .Yi(\n1位全加器fa封装2_11_si ));
  \_1位全加器FA封装2  \u_1位全加器fa封装2_13  (
    .Cout(\n1位全加器fa封装2_13_cout ), .Si(\n1位全加器fa封装2_13_si ), .Cin(\n1位全加器fa封装2_16_cout ), .Xi(X1Y3),
    .Yi(\n1位全加器fa封装2_12_si ));
  \_1位全加器FA封装2  \u_1位全加器fa封装2_14  (
    .Cout(\n1位全加器fa封装2_14_cout ), .Si(\乘积 [4]), .Cin(\n1位全加器fa封装2_17_cout ), .Xi(X0Y4),
    .Yi(\n1位全加器fa封装2_13_si ));
  \_1位全加器FA封装2  \u_1位全加器fa封装2_15  (
    .Cout(\n1位全加器fa封装2_15_cout ), .Si(\n1位全加器fa封装2_15_si ), .Cin(1'b0), .Xi(X2Y1), .Yi(X3Y0));
  \_1位全加器FA封装2  \u_1位全加器fa封装2_16  (
    .Cout(\n1位全加器fa封装2_16_cout ), .Si(\n1位全加器fa封装2_16_si ), .Cin(\n1位全加器fa封装2_18_cout ), .Xi(X1Y2),
    .Yi(\n1位全加器fa封装2_15_si ));
  \_1位全加器FA封装2  \u_1位全加器fa封装2_17  (
    .Cout(\n1位全加器fa封装2_17_cout ), .Si(\乘积 [3]), .Cin(\n1位全加器fa封装2_19_cout ), .Xi(X0Y3),
    .Yi(\n1位全加器fa封装2_16_si ));
  // Probe on \乘积 
  \_1位全加器FA封装2  \u_1位全加器fa封装2_18  (
    .Cout(\n1位全加器fa封装2_18_cout ), .Si(\n1位全加器fa封装2_18_si ), .Cin(1'b0), .Xi(X1Y1), .Yi(X2Y0));
  \_1位全加器FA封装2  \u_1位全加器fa封装2_19  (
    .Cout(\n1位全加器fa封装2_19_cout ), .Si(\乘积 [2]), .Cin(\n1位全加器fa封装2_20_cout ), .Xi(X0Y2),
    .Yi(\n1位全加器fa封装2_18_si ));
  // Probe on X
  // Probe on Y
  // Probe on \乘积 
  \_1位全加器FA封装2  \u_1位全加器fa封装2_20  (.Cout(\n1位全加器fa封装2_20_cout ), .Si(\乘积 [1]), .Cin(1'b0), .Xi(X0Y1), .Yi(X1Y0));

  // Other names for the same wires on the sheet: P[9:0] = \乘积 ; P0 = \乘积 [0]; X0Y0 = \乘积 [0];
  //   XY0[4:0] = {X4Y0, X3Y0, X2Y0, X1Y0, \乘积 [0]}; P1 = \乘积 [1]; P2 = \乘积 [2]; P3 = \乘积 [3]; P4 = \乘积 [4];
  //   P5 = \乘积 [5]; P6 = \乘积 [6]; P7 = \乘积 [7]; P8 = \乘积 [8]; P9 = \乘积 [9]; XY1[4:0] = {X4Y1, X3Y1, X2Y1, X1Y1, X0Y1};
  //   XY2[4:0] = {X4Y2, X3Y2, X2Y2, X1Y2, X0Y2}; XY3[4:0] = {X4Y3, X3Y3, X2Y3, X1Y3, X0Y3};
  //   XY4[4:0] = {X4Y4, X3Y4, X2Y4, X1Y4, X0Y4}

  // Notes on the sheet:
  //   X: pull=down
  //   Y: pull=down
  //   输入引脚区
  //   功能说明：利用一位全加器构成5位×5位的无符号数阵列乘法器，乘积=X×Y，并分析电路延迟；
  //   输出引脚区
  //   5位无符号阵列乘法器（斜向）
  //   ×
  //   =
endmodule

module \乘法流水线接口  (
  input  [4:0] X,
  input  [4:0] Y,
  input  [4:0] XY0,
  input  [4:0] XY1,
  input  [4:0] XY2,
  input  [4:0] XY3,
  input  [4:0] XY4,
  input  [9:0] in_8,
  input  CLK,
  input  \同步清零_高电平有效 ,
  input  \使能端_低电平有效 ,
  output [4:0] X_prime,
  output [4:0] Y_prime,
  output [4:0] XY0_prime,
  output [4:0] XY1_prime,
  output [4:0] XY2_prime,
  output [4:0] XY3_2,
  output [4:0] XY4_2,
  output [9:0] out_19,
  output [9:0] EDU
);

  wire pull_resistor_2_node;
  wire [4:0] multiplexer_1_out, multiplexer_2_out, multiplexer_3_out, multiplexer_4_out, multiplexer_5_out,
       multiplexer_6_out, multiplexer_7_out;
  wire [9:0] multiplexer_8_out;

  Multiplexer #(.width(5), .enable("false")) multiplexer_1 (
    .in0(X), .in1({5{1'b0}}), .out(multiplexer_1_out), .sel(\同步清零_高电平有效 ));
  Multiplexer #(.width(5), .enable("false")) multiplexer_2 (
    .in0(Y), .in1({5{1'b0}}), .out(multiplexer_2_out), .sel(\同步清零_高电平有效 ));
  Multiplexer #(.width(5), .enable("false")) multiplexer_3 (
    .in0(XY0), .in1({5{1'b0}}), .out(multiplexer_3_out), .sel(\同步清零_高电平有效 ));
  Multiplexer #(.width(5), .enable("false")) multiplexer_4 (
    .in0(XY1), .in1({5{1'b0}}), .out(multiplexer_4_out), .sel(\同步清零_高电平有效 ));
  Multiplexer #(.width(5), .enable("false")) multiplexer_5 (
    .in0(XY2), .in1({5{1'b0}}), .out(multiplexer_5_out), .sel(\同步清零_高电平有效 ));
  Multiplexer #(.width(5), .enable("false")) multiplexer_6 (
    .in0(XY3), .in1({5{1'b0}}), .out(multiplexer_6_out), .sel(\同步清零_高电平有效 ));
  Multiplexer #(.width(5), .enable("false")) multiplexer_7 (
    .in0(XY4), .in1({5{1'b0}}), .out(multiplexer_7_out), .sel(\同步清零_高电平有效 ));
  Multiplexer #(.width(10), .enable("false")) multiplexer_8 (
    .in0(in_8), .in1({10{1'b0}}), .out(multiplexer_8_out), .sel(\同步清零_高电平有效 ));
  Pull_Resistor pull_resistor_1 (.node(\同步清零_高电平有效 ));
  Register #(.width(5), .Select("low")) register_1 (
    .D(multiplexer_1_out), .en(pull_resistor_2_node), .Q(X_prime), .clk(CLK));  // open: clr
  Register #(.width(5), .Select("low")) register_2 (
    .D(multiplexer_2_out), .en(pull_resistor_2_node), .Q(Y_prime), .clk(CLK));  // open: clr
  Register #(.width(5), .Select("low")) register_3 (
    .D(multiplexer_3_out), .en(pull_resistor_2_node), .Q(XY0_prime), .clk(CLK));  // open: clr
  Register #(.width(5), .Select("low")) register_4 (
    .D(multiplexer_4_out), .en(pull_resistor_2_node), .Q(XY1_prime), .clk(CLK));  // open: clr
  Register #(.width(5), .Select("low")) register_5 (
    .D(multiplexer_5_out), .en(pull_resistor_2_node), .Q(XY2_prime), .clk(CLK));  // open: clr
  Register #(.width(5), .Select("low")) register_6 (
    .D(multiplexer_6_out), .en(pull_resistor_2_node), .Q(XY3_2), .clk(CLK));  // open: clr
  Register #(.width(5), .Select("low")) register_7 (
    .D(multiplexer_7_out), .en(pull_resistor_2_node), .Q(XY4_2), .clk(CLK));  // open: clr
  Register #(.width(10), .Select("low")) register_8 (
    .D(multiplexer_8_out), .en(pull_resistor_2_node), .Q(EDU), .clk(CLK));  // open: clr
  Pull_Resistor pull_resistor_2 (.node(pull_resistor_2_node));
  not not_1 (pull_resistor_2_node, \使能端_低电平有效 );

  assign out_19 = EDU;

  // Notes on the sheet:
  //   使能端_低电平有效: pull=down
  //   同步清零_高电平有效: pull=down
  //   乘法流水线接口
endmodule

module \_5位无符号阵列乘法器流水线  (
  output [4:0] X,
  output [9:0] P2,
  output [9:0] P3,
  output [9:0] P4,
  output [9:0] P5,
  output [4:0] Y
);

  wire CLK, comparator_1_eq, not_1_out;
  wire [4:0] \与门阵列_1_xy0 , \与门阵列_1_xy1 , \与门阵列_1_xy2 , \与门阵列_1_xy3 , \与门阵列_1_xy4 , \乘数 , \乘法流水线接口_1_x_prime ,
       \乘法流水线接口_1_xy2_prime , \乘法流水线接口_1_xy3_2 , \乘法流水线接口_1_xy4_2 , \乘法流水线接口_1_y_prime , \乘法流水线接口_2_x_prime ,
       \乘法流水线接口_2_xy3_2 , \乘法流水线接口_2_xy4_2 , \乘法流水线接口_2_y_prime , \乘法流水线接口_3_x_prime , \乘法流水线接口_3_xy4_2 ,
       \乘法流水线接口_3_y_prime , \被乘数 ;
  wire [7:0] counter_1_q;
  wire [9:0] adder_1_out, adder_2_out, adder_3_out, adder_4_out, bit_extender_1_out, bit_extender_2_out,
       bit_extender_3_out, bit_extender_4_out, bit_extender_5_out, multiplier_1_out, shifter_1_out,
       shifter_2_out, shifter_3_out, shifter_4_out, \乘法流水线接口_1_out_19 , \乘法流水线接口_2_out_19 ,
       \乘法流水线接口_3_out_19 , \乘积 ;

  Clock clock_1 (.out(CLK));
  Counter #(.behavior("old")) counter_1 (.Q(counter_1_q), .clk(CLK));  // open: load, D, count, carry, clr, preset
  \与门阵列  \u_与门阵列_1  (
    .X(X), .XY4(\与门阵列_1_xy4 ), .XY3(\与门阵列_1_xy3 ), .XY2(\与门阵列_1_xy2 ), .XY1(\与门阵列_1_xy1 ),
    .XY0(\与门阵列_1_xy0 ), .Y(Y));
  // Probe on X
  assign bit_extender_1_out = {{5{1'b0}}, \与门阵列_1_xy1 };  // Bit_Extender bit_extender_1
  assign bit_extender_2_out = {{5{1'b0}}, \与门阵列_1_xy0 };  // Bit_Extender bit_extender_2
  ROM #(.dataWidth(10), .Select("low")) rom_1 (.addr(counter_1_q), .data({Y, X}));
  // Probe on Y
  Shifter #(.width(10)) shifter_1 (.in(bit_extender_1_out), .\dist (4'b0001), .out(shifter_1_out));
  Adder #(.width(10)) adder_1 (.a(shifter_1_out), .b(bit_extender_2_out), .out(adder_1_out));  // open: cin, cout
  \乘法流水线接口  \u_乘法流水线接口_1  (
    .X(X), .Y(Y), .XY2(\与门阵列_1_xy2 ), .XY3(\与门阵列_1_xy3 ), .XY4(\与门阵列_1_xy4 ), .in_8(adder_1_out), .CLK(CLK),
    .X_prime(\乘法流水线接口_1_x_prime ), .Y_prime(\乘法流水线接口_1_y_prime ), .XY2_prime(\乘法流水线接口_1_xy2_prime ),
    .XY3_2(\乘法流水线接口_1_xy3_2 ), .XY4_2(\乘法流水线接口_1_xy4_2 ), .out_19(\乘法流水线接口_1_out_19 ), .EDU(P2));  // open: XY0, XY1, XY0_prime, XY1_prime, 同步清零_高电平有效, 使能端_低电平有效
  // Probe on \乘法流水线接口_1_x_prime 
  assign bit_extender_3_out = {{5{1'b0}}, \乘法流水线接口_1_xy2_prime };  // Bit_Extender bit_extender_3
  // Probe on \乘法流水线接口_1_y_prime 
  Shifter #(.width(10)) shifter_2 (.in(bit_extender_3_out), .\dist (4'b0010), .out(shifter_2_out));
  // Probe on \被乘数 
  // Probe on \乘数 
  // Probe on \乘积 
  \乘法流水线接口  \u_乘法流水线接口_2  (
    .X(\乘法流水线接口_1_x_prime ), .Y(\乘法流水线接口_1_y_prime ), .XY3(\乘法流水线接口_1_xy3_2 ), .XY4(\乘法流水线接口_1_xy4_2 ),
    .in_8(adder_2_out), .CLK(CLK), .X_prime(\乘法流水线接口_2_x_prime ), .Y_prime(\乘法流水线接口_2_y_prime ),
    .XY3_2(\乘法流水线接口_2_xy3_2 ), .XY4_2(\乘法流水线接口_2_xy4_2 ), .out_19(\乘法流水线接口_2_out_19 ), .EDU(P3));  // open: XY0, XY1, XY2, XY0_prime, XY1_prime, XY2_prime, 同步清零_高电平有效, 使能端_低电平有效
  Adder #(.width(10)) adder_2 (.a(shifter_2_out), .b(\乘法流水线接口_1_out_19 ), .out(adder_2_out));  // open: cin, cout
  // Probe on \乘法流水线接口_2_x_prime 
  assign bit_extender_4_out = {{5{1'b0}}, \乘法流水线接口_2_xy3_2 };  // Bit_Extender bit_extender_4
  // Probe on \乘法流水线接口_2_y_prime 
  Shifter #(.width(10)) shifter_3 (.in(bit_extender_4_out), .\dist (4'b0011), .out(shifter_3_out));
  Adder #(.width(10)) adder_3 (.a(shifter_3_out), .b(\乘法流水线接口_2_out_19 ), .out(adder_3_out));  // open: cin, cout
  \乘法流水线接口  \u_乘法流水线接口_3  (
    .X(\乘法流水线接口_2_x_prime ), .Y(\乘法流水线接口_2_y_prime ), .XY4(\乘法流水线接口_2_xy4_2 ), .in_8(adder_3_out), .CLK(CLK),
    .X_prime(\乘法流水线接口_3_x_prime ), .Y_prime(\乘法流水线接口_3_y_prime ), .XY4_2(\乘法流水线接口_3_xy4_2 ),
    .out_19(\乘法流水线接口_3_out_19 ), .EDU(P4));  // open: XY0, XY1, XY2, XY3, XY0_prime, XY1_prime, XY2_prime, XY3_2, 同步清零_高电平有效, 使能端_低电平有效
  // Probe on \乘法流水线接口_3_x_prime 
  assign bit_extender_5_out = {{5{1'b0}}, \乘法流水线接口_3_xy4_2 };  // Bit_Extender bit_extender_5
  // Probe on \乘法流水线接口_3_y_prime 
  Shifter #(.width(10)) shifter_4 (.in(bit_extender_5_out), .\dist (4'b0100), .out(shifter_4_out));
  \乘法流水线接口  \u_乘法流水线接口_4  (
    .X(\乘法流水线接口_3_x_prime ), .Y(\乘法流水线接口_3_y_prime ), .in_8(adder_4_out), .CLK(CLK), .X_prime(\被乘数 ),
    .Y_prime(\乘数 ), .out_19(\乘积 ), .EDU(P5));  // open: XY0, XY1, XY2, XY3, XY4, XY0_prime, XY1_prime, XY2_prime, XY3_2, XY4_2, 同步清零_高电平有效, 使能端_低电平有效
  Adder #(.width(10)) adder_4 (.a(shifter_4_out), .b(\乘法流水线接口_3_out_19 ), .out(adder_4_out));  // open: cin, cout
  // Probe on \乘数 
  // Probe on \被乘数 
  // Probe on multiplier_1_out
  // Probe on \乘积 
  Multiplier #(.width(5)) multiplier_1 (
    .a(\被乘数 ), .b(\乘数 ), .out(multiplier_1_out[4:0]), .cout(multiplier_1_out[9:5]));  // open: cin
  Comparator #(.width(10)) comparator_1 (.a(multiplier_1_out), .b(\乘积 ), .eq(comparator_1_eq));  // open: gt, lt
  not not_1 (not_1_out, comparator_1_eq);
  LED \u_不正确  (.in(not_1_out));

  // Other names for the same wires on the sheet: 被乘数X[4:0] = X; 乘数Y[4:0] = Y

  // Notes on the sheet:
  //   contents of rom_1 (hex, n*v repeats v):
  //   3fe 58 23 1e 2c 34 66 380 3c0 55 3b3 12 18 3dc 390 390 3b9 45 1e 398 21 14 5c 6 3d2 3aa 41 28 394
  //   38c 5a 3f8 28 1c 48 3b4 3b2 45 3bc 0 399 3e0 26 44 69 55 8 3e0 8 4b 38a 0 3b4 1a 78 393 0 18 40 3b0
  //   390 3f0 7e 50
  //   第1步
  //   ×
  //   =
  //   第2步
  //   5位无符号阵列乘法器流水线
  //   第3步
  //   第4步
endmodule

module \_16位快速加法器__组内并行_组间串行  (
  input  [15:0] X,
  input  [15:0] Y,
  input  C0,
  output C15,
  output C16,
  output [15:0] S
);

  wire \n4位快速加法器_1_g_star , \n4位快速加法器_2_c4 , \n4位快速加法器_2_g_star , \n4位快速加法器_3_c4 , \n4位快速加法器_3_g_star ,
       \n4位快速加法器_4_c4 , \n4位快速加法器_4_g_star ;

  \_4位快速加法器  \u_4位快速加法器_1  (
    .X(X[15:12]), .Y(Y[15:12]), .C0(\n4位快速加法器_2_c4 ), .S(S[15:12]), .C4(C16), .G_star(\n4位快速加法器_1_g_star ),
    .C3(C15));  // open: P_star
  \_4位快速加法器  \u_4位快速加法器_2  (
    .X(X[11:8]), .Y(Y[11:8]), .C0(\n4位快速加法器_3_c4 ), .S(S[11:8]), .C4(\n4位快速加法器_2_c4 ),
    .G_star(\n4位快速加法器_2_g_star ));  // open: P_star, C3
  \_4位快速加法器  \u_4位快速加法器_3  (
    .X(X[7:4]), .Y(Y[7:4]), .C0(\n4位快速加法器_4_c4 ), .S(S[7:4]), .C4(\n4位快速加法器_3_c4 ),
    .G_star(\n4位快速加法器_3_g_star ));  // open: P_star, C3
  // Probe on X
  // Probe on Y
  // Probe on S
  // Probe on X
  // Probe on Y
  // Probe on S
  \_4位快速加法器  \u_4位快速加法器_4  (
    .X(X[3:0]), .Y(Y[3:0]), .C0(C0), .S(S[3:0]), .C4(\n4位快速加法器_4_c4 ), .G_star(\n4位快速加法器_4_g_star ));  // open: P_star, C3

  // Other names for the same wires on the sheet: S0[3:0] = S[3:0]; S1[3:0] = S[7:4]; S2[3:0] = S[11:8];
  //   S3[3:0] = S[15:12]; X0[3:0] = X[3:0]; X1[3:0] = X[7:4]; X2[3:0] = X[11:8]; X3[3:0] = X[15:12]; Y0[3:0] = Y[3:0];
  //   Y1[3:0] = Y[7:4]; Y2[3:0] = Y[11:8]; Y3[3:0] = Y[15:12]

  // Notes on the sheet:
  //   Y: pull=down
  //   C0: pull=down
  //   X: pull=down
  //   输入引脚区
  //   输出引脚区
  //   功能说明：16位Adder  S=X＋Y，C16为最高位进位，C15为次高位进位，C0为进位输入
  //   16位快速加法器（组内并行、组间串行）
  //   +
  //   =
  //   有符号加法
  //   +
  //   =
  //   无符号加法
endmodule

module \_16位快速加法器__组内并行_组间并行  (
  input  [15:0] X,
  input  [15:0] Y,
  input  C0,
  output C16,
  output C15,
  output G_star,
  output P_star,
  output [15:0] S
);

  wire \n4位先行进位电路_cla74182_1_c1 , \n4位先行进位电路_cla74182_1_c2 , \n4位先行进位电路_cla74182_1_c3 , \n4位快速加法器_1_g_star ,
       \n4位快速加法器_1_p_star , \n4位快速加法器_2_g_star , \n4位快速加法器_2_p_star , \n4位快速加法器_3_g_star ,
       \n4位快速加法器_3_p_star , \n4位快速加法器_4_g_star , \n4位快速加法器_4_p_star ;

  \_4位先行进位电路_CLA74182  \u_4位先行进位电路_cla74182_1  (
    .G4(\n4位快速加法器_1_g_star ), .P4(\n4位快速加法器_1_p_star ), .G3(\n4位快速加法器_2_g_star ), .P3(\n4位快速加法器_2_p_star ),
    .G2(\n4位快速加法器_3_g_star ), .P2(\n4位快速加法器_3_p_star ), .G1(\n4位快速加法器_4_g_star ), .P1(\n4位快速加法器_4_p_star ),
    .Cin(C0), .C3(\n4位先行进位电路_cla74182_1_c3 ), .C2(\n4位先行进位电路_cla74182_1_c2 ), .C1(\n4位先行进位电路_cla74182_1_c1 ),
    .G_star(G_star), .P_star(P_star));  // open: C4
  \_4位快速加法器  \u_4位快速加法器_1  (
    .X(X[15:12]), .Y(Y[15:12]), .C0(\n4位先行进位电路_cla74182_1_c3 ), .S(S[15:12]), .C4(C16),
    .G_star(\n4位快速加法器_1_g_star ), .P_star(\n4位快速加法器_1_p_star ), .C3(C15));
  \_4位快速加法器  \u_4位快速加法器_2  (
    .X(X[11:8]), .Y(Y[11:8]), .C0(\n4位先行进位电路_cla74182_1_c2 ), .S(S[11:8]), .G_star(\n4位快速加法器_2_g_star ),
    .P_star(\n4位快速加法器_2_p_star ));  // open: C4, C3
  \_4位快速加法器  \u_4位快速加法器_3  (
    .X(X[7:4]), .Y(Y[7:4]), .C0(\n4位先行进位电路_cla74182_1_c1 ), .S(S[7:4]), .G_star(\n4位快速加法器_3_g_star ),
    .P_star(\n4位快速加法器_3_p_star ));  // open: C4, C3
  // Probe on X
  // Probe on Y
  // Probe on S
  \_4位快速加法器  \u_4位快速加法器_4  (
    .X(X[3:0]), .Y(Y[3:0]), .C0(C0), .S(S[3:0]), .G_star(\n4位快速加法器_4_g_star ), .P_star(\n4位快速加法器_4_p_star ));  // open: C4, C3
  // Probe on X
  // Probe on Y
  // Probe on S

  // Other names for the same wires on the sheet: S0[3:0] = S[3:0]; S1[3:0] = S[7:4]; S2[3:0] = S[11:8];
  //   S3[3:0] = S[15:12]; X0[3:0] = X[3:0]; X1[3:0] = X[7:4]; X2[3:0] = X[11:8]; X3[3:0] = X[15:12]; Y0[3:0] = Y[3:0];
  //   Y1[3:0] = Y[7:4]; Y2[3:0] = Y[11:8]; Y3[3:0] = Y[15:12]

  // Notes on the sheet:
  //   Y: pull=down
  //   X: pull=down
  //   C0: pull=down
  //   输入引脚区
  //   输出引脚区
  //   功能说明：16位Adder  S=X＋Y，C16为最高位进位，C15为次高位进位，C0为进位输入， G* P*为成组进位生成传递函数
  //   16位快速加法器（组内并行、组间并行）
  //   +
  //   =
  //   有符号加法
  //   +
  //   =
  //   无符号加法
endmodule

module \_8位原码一位乘法器  (
  input  [7:0] X,
  input  [7:0] Y,
  output [15:0] \乘积 
);

  wire CLK, RST, \时钟_out ;
  wire [7:0] bit_extender_1_out, bit_extender_2_out;
  wire [8:0] \P符号指示 , \X符号指示 , \Y符号指示 ;
  wire [15:0] \n8位无符号一位乘法器_封装用_1_p5 ;

  // Probe on X[6:0]
  DotMatrix #(.matrixcols(3), .matrixrows(3)) dotmatrix_1 (
    .col0(\X符号指示 [8:6]), .col1(\X符号指示 [5:3]), .col2(\X符号指示 [2:0]));
  xor xor_1 (\乘积 [15], Y[7], X[7]);
  assign bit_extender_1_out = {{1{1'b0}}, X[6:0]};  // Bit_Extender bit_extender_1
  assign bit_extender_2_out = {{1{1'b0}}, Y[6:0]};  // Bit_Extender bit_extender_2
  Clock \u_时钟  (.out(\时钟_out ));
  Multiplexer #(.width(9), .enable("false")) multiplexer_1 (.in0(9'hba), .in1(9'h92), .out(\X符号指示 ), .sel(X[7]));
  // Probe on Y[6:0]
  DotMatrix #(.matrixcols(3), .matrixrows(3)) dotmatrix_2 (
    .col0(\Y符号指示 [8:6]), .col1(\Y符号指示 [5:3]), .col2(\Y符号指示 [2:0]));
  // Probe on \n8位无符号一位乘法器_封装用_1_p5 
  // _8位无符号一位乘法器_封装用 8位无符号一位乘法器_封装用_1: pin names not known; wires that end beside it: bit_extender_1_out, bit_extender_2_out, \时钟_out , RST, \n8位无符号一位乘法器_封装用_1_p5 
  BitSelector #(.width(16), .group(15)) bitselector_1 (.in(\n8位无符号一位乘法器_封装用_1_p5 ), .out(\乘积 [14:0]), .sel(1'b0));
  Button \u_复位  (.out(RST));
  Clock clock_1 (.out(CLK));
  Multiplexer #(.width(9), .enable("false")) multiplexer_2 (.in0(9'hba), .in1(9'h92), .out(\Y符号指示 ), .sel(Y[7]));
  // Probe on \乘积 [14:0]
  DotMatrix #(.matrixcols(3), .matrixrows(3)) dotmatrix_3 (
    .col0(\P符号指示 [8:6]), .col1(\P符号指示 [5:3]), .col2(\P符号指示 [2:0]));
  Multiplexer #(.width(9), .enable("false")) multiplexer_3 (.in0(9'hba), .in1(9'h92), .out(\P符号指示 ), .sel(\乘积 [15]));

  // Other names for the same wires on the sheet: P[15:0] = \乘积 ; P_star[14:0] = \乘积 [14:0]; P15 = \乘积 [15];
  //   X_star[6:0] = X[6:0]; Y_star[6:0] = Y[6:0]

  // Notes on the sheet:
  //   输入输出引脚区
  //   8位原码一位乘法器
endmodule

module \_6位原码阵列乘法器  (
  input  [5:0] X,
  input  [5:0] Y,
  output [10:0] P
);

  wire xor_1_out;
  wire [2:0] multiplexer_1_out, multiplexer_1_out_2, multiplexer_1_out_3, multiplexer_4_out,
       multiplexer_4_out_2, multiplexer_4_out_3, multiplexer_6_out, multiplexer_6_out_2, multiplexer_6_out_3;
  wire [4:0] negator_2_out;
  wire [5:0] negator_1_out, negator_3_out, X_t, Y_t;
  wire [9:0] \n5位阵列乘法器_1_p3 ;
  wire [11:0] P_t;

  DotMatrix #(.matrixcols(3), .matrixrows(3)) dotmatrix_1 (
    .col0(multiplexer_1_out_3), .col1(multiplexer_1_out_2), .col2(multiplexer_1_out));
  Multiplexer #(.width(9), .enable("false")) multiplexer_1 (
    .in0(9'hba), .in1(9'h92), .out({multiplexer_1_out_3, multiplexer_1_out_2, multiplexer_1_out}), .sel(X[5]));
  // Probe on X[4:0]
  // _5位阵列乘法器 5位阵列乘法器_1: pin names not known; wires that end beside it: X[5], X[4:0], \n5位阵列乘法器_1_p3 , Y[4:0], Y[5]
  Negator #(.width(6)) negator_1 (.in(X_t), .out(negator_1_out));
  xor xor_1 (xor_1_out, Y[5], X[5]);
  Multiplexer #(.width(5), .enable("false")) multiplexer_2 (
    .in0(X_t[4:0]), .in1(negator_1_out[4:0]), .out(X[4:0]), .sel(X_t[5]));
  Negator #(.width(5)) negator_2 (.in(\n5位阵列乘法器_1_p3 [4:0]), .out(negator_2_out));
  Multiplexer #(.width(6), .enable("false")) multiplexer_3 (
    .in0({6{1'b0}}), .in1({6{1'b1}}), .out(P_t[11:6]), .sel(xor_1_out));
  DotMatrix #(.matrixcols(3), .matrixrows(3)) dotmatrix_2 (
    .col0(multiplexer_4_out_3), .col1(multiplexer_4_out_2), .col2(multiplexer_4_out));
  // Probe on Y[4:0]
  Multiplexer #(.width(9), .enable("false")) multiplexer_4 (
    .in0(9'hba), .in1(9'h92), .out({multiplexer_4_out_3, multiplexer_4_out_2, multiplexer_4_out}), .sel(Y[5]));
  Multiplexer #(.width(5), .enable("false")) multiplexer_5 (
    .in0(\n5位阵列乘法器_1_p3 [4:0]), .in1(negator_2_out), .out(P_t[4:0]), .sel(xor_1_out));
  Negator #(.width(6)) negator_3 (.in(Y_t), .out(negator_3_out));
  DotMatrix #(.matrixcols(3), .matrixrows(3)) dotmatrix_3 (
    .col0(multiplexer_6_out_3), .col1(multiplexer_6_out_2), .col2(multiplexer_6_out));
  Multiplexer #(.width(9), .enable("false")) multiplexer_6 (
    .in0(9'hba), .in1(9'h92), .out({multiplexer_6_out_3, multiplexer_6_out_2, multiplexer_6_out}), .sel(P[10]));
  Multiplexer #(.width(5), .enable("false")) multiplexer_7 (
    .in0(Y_t[4:0]), .in1(negator_3_out[4:0]), .out(Y[4:0]), .sel(Y_t[5]));
  // Probe on X[4:0]
  // Probe on Y[4:0]
  // Probe on P[9:0]
  // Probe on P[9:0]
  // Pins of 5 and 6 bits meet at P_t[5:0]

  // Other names for the same wires on the sheet: P_t_t[9:0] = P[9:0]; X_t_t[4:0] = X[4:0]; Y_t_t[4:0] = Y[4:0]

  // Notes on the sheet:
  //   输入引脚区
  //   功能说明：利用5位无符号阵列乘法器完成6位×6位的原码阵列乘法器，乘积P = X × Y  
  //   6位原码阵列乘法器
  //   输出引脚区
  //   ×
  //   =
endmodule

module \_6位补码阵列乘法器  (
  input  [5:0] X,
  input  [5:0] Y,
  input  [11:0] in_3,
  output [11:0] P
);

  wire comparator_1_eq, comparator_2_eq, comparator_3_eq, comparator_4_eq, or_1_out, or_2_out, xor_1_out;
  wire [1:0] multiplexer_1_out;
  wire [4:0] X_t, Y_t;
  wire [5:0] negator_1_out, negator_3_out;
  wire [9:0] multiplexer_3_out, \n5位无符号阵列乘法器_横向_1_p2 , negator_2_out;
  wire [11:0] bit_extender_1_out, bit_extender_2_out, multiplexer_5_out, multiplier_1_out;

  // _5位无符号阵列乘法器__横向 5位无符号阵列乘法器_横向_1: pin names not known; wires that end beside it: X_t, \n5位无符号阵列乘法器_横向_1_p2 , Y_t
  // Probe on X
  xor xor_1 (xor_1_out, Y[5], X[5]);
  Comparator #(.width(6)) comparator_1 (.a(X), .b({6{1'b0}}), .eq(comparator_1_eq));  // open: gt, lt
  Comparator #(.width(6)) comparator_2 (.a(Y), .b({6{1'b0}}), .eq(comparator_2_eq));  // open: gt, lt
  Comparator #(.width(6)) comparator_3 (.a(X), .b(6'b100000), .eq(comparator_3_eq));  // open: gt, lt
  Comparator #(.width(6)) comparator_4 (.a(Y), .b(6'b100000), .eq(comparator_4_eq));  // open: gt, lt
  Negator #(.width(6)) negator_1 (.in(X), .out(negator_1_out));
  Negator #(.width(10)) negator_2 (.in(\n5位无符号阵列乘法器_横向_1_p2 ), .out(negator_2_out));
  Multiplexer #(.width(2), .enable("false")) multiplexer_1 (
    .in0(2'b00), .in1(2'b11), .out(multiplexer_1_out), .sel(xor_1_out));
  // Probe on or_1_out
  or or_1 (or_1_out, comparator_1_eq, comparator_2_eq);
  // Probe on or_2_out
  or or_2 (or_2_out, comparator_3_eq, comparator_4_eq);
  // Probe on Y
  Multiplexer #(.width(5), .enable("false")) multiplexer_2 (
    .in0(X[4:0]), .in1(negator_1_out[4:0]), .out(X_t), .sel(X[5]));
  Multiplexer #(.width(10), .enable("false")) multiplexer_3 (
    .in0(\n5位无符号阵列乘法器_横向_1_p2 ), .in1(negator_2_out), .out(multiplexer_3_out), .sel(xor_1_out));
  assign bit_extender_1_out = {{6{1'b0}}, X};  // Bit_Extender bit_extender_1
  assign bit_extender_2_out = {{6{Y[5]}}, Y};  // Bit_Extender bit_extender_2
  Negator #(.width(6)) negator_3 (.in(Y), .out(negator_3_out));
  Multiplier #(.width(12)) multiplier_1 (
    .a(bit_extender_1_out), .b(bit_extender_2_out), .out(multiplier_1_out));  // open: cin, cout
  Multiplexer #(.width(5), .enable("false")) multiplexer_4 (
    .in0(Y[4:0]), .in1(negator_3_out[4:0]), .out(Y_t), .sel(Y[5]));
  Multiplexer #(.width(12), .enable("false")) multiplexer_5 (
    .in0({multiplexer_1_out, multiplexer_3_out}), .in1(multiplier_1_out), .out(multiplexer_5_out),
    .sel(or_2_out));
  // Probe on X
  // Probe on Y
  // Probe on P
  Multiplexer #(.width(12), .enable("false")) multiplexer_6 (
    .in0(multiplexer_5_out), .in1(in_3), .out(P), .sel(or_1_out));

  // Other names for the same wires on the sheet: X4_0[4:0] = X[4:0]; Y4_0[4:0] = Y[4:0]

  // Notes on the sheet:
  //   输入引脚区
  //   功能说明：利用5位阵列乘法器6位×6位的补码阵列乘法器，乘积P = X × Y
  //   6位补码阵列乘法器
  //   输出引脚区
  //   ×
  //   =
endmodule

module \_8位无符号一位乘法器_封装用  (
  input  CLK,
  input  [7:0] X,
  input  [7:0] Y,
  input  RST,
  output [15:0] \乘积 
);

  wire comparator_1_eq, d_ff_1_q, not_1_out;
  wire [0:0] \n8位串行加法器_1_s ;
  wire [3:0] counter_1_q;
  wire [7:0] multiplexer_1_out, multiplexer_2_out, \n8位串行加法器_1_cout ;

  // Probe on X
  // Probe on Y
  // Probe on \乘积 [15:8]
  Register #(.Select("low")) register_1 (.D(\n8位串行加法器_1_cout ), .en(not_1_out), .Q(\乘积 [15:8]), .clk(CLK), .clr(RST));
  \_8位串行加法器  \u_8位串行加法器_1  (
    .X(\乘积 [15:8]), .Y(multiplexer_1_out), .Cin(1'b0), .S({\n8位串行加法器_1_cout [6:0], \n8位串行加法器_1_s [0]}),
    .Cout(\n8位串行加法器_1_cout [7]));  // open: out_6
  Multiplexer #(.width(8), .enable("false")) multiplexer_1 (
    .in0({8{1'b0}}), .in1(X), .out(multiplexer_1_out), .sel(\乘积 [0]));
  Multiplexer #(.width(8), .enable("false")) multiplexer_2 (
    .in0(Y), .in1({\n8位串行加法器_1_s [0], \乘积 [7:1]}), .out(multiplexer_2_out), .sel(d_ff_1_q));
  // Probe on \乘积 [7:0]
  Register #(.Select("low")) Y_2 (.D(multiplexer_2_out), .en(not_1_out), .Q(\乘积 [7:0]), .clk(CLK), .clr(RST));
  Counter #(.width(4), .max('hf), .behavior("old")) counter_1 (
    .count(not_1_out), .Q(counter_1_q), .clk(CLK), .clr(RST));  // open: load, D, carry, preset
  D_Flip_Flop #(.Pre_Clr_Positions("LEGACY"), .enable("true"), .NewFFLayout("false")) d_ff_1 (
    .clk(CLK), .D(1'b1), .Q(d_ff_1_q), .reset(RST));  // open: Qn, preset, en
  // Probe on \乘积 
  Comparator #(.width(4), .mode("unsigned")) comparator_1 (
    .a(counter_1_q), .b(4'b1001), .eq(comparator_1_eq));  // open: gt, lt
  not not_1 (not_1_out, comparator_1_eq);
  // Probe on X
  // Probe on Y
  // Probe on \乘积 

  // Notes on the sheet:
  //   输入输出引脚区
  //   ∑
  //   功能说明: 无符号一位乘法器   乘积=X*Y，要求采用原码一位乘法实现，最终结果能输出在乘积引脚上
  //   8位无符号一位乘法器（封装用）
  //   计数及移位控制
  //   ×
  //   =
  //   核心算法：{ ∑ , Y } = { ∑ ＋ Y  |X|  , Y  } / 2
  //   n
endmodule
