// Logisim project 20420192201952+庾晓萍-2.circ as structural Verilog: 4 circuits, main circuit 8位原码一位乘法器
// FA
module \_1位全加器FA封装1  (
  input  Cin,
  input  Xi,
  input  Yi,
  output Cout,
  output Si
);

  wire AND_2_out, AND_out, XOR_2_out;

  or OR (Cout, AND_out, AND_2_out);
  and AND (AND_out, Xi, Yi);
  and AND_2 (AND_2_out, Cin, XOR_2_out);
  xor XOR (Si, Cin, XOR_2_out);
  xor XOR_2 (XOR_2_out, Xi, Yi);

  // Notes on the sheet:
  //   Xi: pull=down
  //   Yi: pull=down
  //   Cin: pull=down
  //   1位全加器（FA）
  //   Si = Xi ^ Yi ^ Cin
  //   Cout = Xi Yi + Cin (Xi ^ Yi)
endmodule

module \_8位串行加法器  (
  input  [7:0] X,
  input  [7:0] Y,
  input  Cin,
  output [7:0] S,
  output Cout,
  output out_6
);

  wire \n1位全加器fa封装1_2_cout , \n1位全加器fa封装1_3_cout , \n1位全加器fa封装1_4_cout , \n1位全加器fa封装1_5_cout ,
       \n1位全加器fa封装1_6_cout , \n1位全加器fa封装1_7_cout , \n1位全加器fa封装1_8_cout ;

  xor xor_1 (out_6, Cout, \n1位全加器fa封装1_2_cout );
  \_1位全加器FA封装1  \u_1位全加器fa封装1_1  (.Cout(Cout), .Si(S[7]), .Cin(\n1位全加器fa封装1_2_cout ), .Xi(X[7]), .Yi(Y[7]));
  \_1位全加器FA封装1  \u_1位全加器fa封装1_2  (
    .Cout(\n1位全加器fa封装1_2_cout ), .Si(S[6]), .Cin(\n1位全加器fa封装1_3_cout ), .Xi(X[6]), .Yi(Y[6]));
  \_1位全加器FA封装1  \u_1位全加器fa封装1_3  (
    .Cout(\n1位全加器fa封装1_3_cout ), .Si(S[5]), .Cin(\n1位全加器fa封装1_4_cout ), .Xi(X[5]), .Yi(Y[5]));
  \_1位全加器FA封装1  \u_1位全加器fa封装1_4  (
    .Cout(\n1位全加器fa封装1_4_cout ), .Si(S[4]), .Cin(\n1位全加器fa封装1_5_cout ), .Xi(X[4]), .Yi(Y[4]));
  \_1位全加器FA封装1  \u_1位全加器fa封装1_5  (
    .Cout(\n1位全加器fa封装1_5_cout ), .Si(S[3]), .Cin(\n1位全加器fa封装1_6_cout ), .Xi(X[3]), .Yi(Y[3]));
  \_1位全加器FA封装1  \u_1位全加器fa封装1_6  (
    .Cout(\n1位全加器fa封装1_6_cout ), .Si(S[2]), .Cin(\n1位全加器fa封装1_7_cout ), .Xi(X[2]), .Yi(Y[2]));
  // Probe on X
  // Probe on Y
  // Probe on S
  \_1位全加器FA封装1  \u_1位全加器fa封装1_7  (
    .Cout(\n1位全加器fa封装1_7_cout ), .Si(S[1]), .Cin(\n1位全加器fa封装1_8_cout ), .Xi(X[1]), .Yi(Y[1]));
  // Probe on X
  // Probe on Y
  // Probe on S
  \_1位全加器FA封装1  \u_1位全加器fa封装1_8  (.Cout(\n1位全加器fa封装1_8_cout ), .Si(S[0]), .Cin(Cin), .Xi(X[0]), .Yi(Y[0]));

  // Other names for the same wires on the sheet: OF = out_6

  // Notes on the sheet:
  //   Y: pull=down
  //   X: pull=down
  //   Cin: pull=down
  //   输入引脚区
  //   符号位
  //   8位串行加法器
  //   输出引脚区
  //   Overflow
  //   +
  //   有符号加法
  //   +
  //   =
  //   无符号加法
endmodule

module \_8位原码一位乘法器  (
  input  [7:0] X,
  input  [7:0] Y,
  output [15:0] \乘积 
);

  wire CLK, RST, \时钟_out ;
  wire [7:0] bit_extender_1_out, bit_extender_2_out;
  wire [8:0] \P符号指示 , \X符号指示 , \Y符号指示 ;
  wire [15:0] \n8位无符号一位乘法器_封装用_1_乘积 ;

  // Probe on X[6:0]
  DotMatrix #(.matrixcols(3), .matrixrows(3)) dotmatrix_1 (
    .col0(\X符号指示 [8:6]), .col1(\X符号指示 [5:3]), .col2(\X符号指示 [2:0]));
  xor xor_1 (\乘积 [15], Y[7], X[7]);
  assign bit_extender_1_out = {{1{1'b0}}, X[6:0]};  // Bit_Extender bit_extender_1
  assign bit_extender_2_out = {{1{1'b0}}, Y[6:0]};  // Bit_Extender bit_extender_2
  Clock \u_时钟  (.out(\时钟_out ));
  Multiplexer #(.width(9), .enable("false")) multiplexer_1 (.in0(9'hba), .in1(9'h92), .out(\X符号指示 ), .sel(X[7]));
  // Probe on Y[6:0]
  DotMatrix #(.matrixcols(3), .matrixrows(3)) dotmatrix_2 (
    .col0(\Y符号指示 [8:6]), .col1(\Y符号指示 [5:3]), .col2(\Y符号指示 [2:0]));
  // Probe on \n8位无符号一位乘法器_封装用_1_乘积 
  \_8位无符号一位乘法器_封装用  \u_8位无符号一位乘法器_封装用_1  (
    .CLK(\时钟_out ), .X(bit_extender_1_out), .Y(bit_extender_2_out), .RST(RST), .\乘积 (\n8位无符号一位乘法器_封装用_1_乘积 ));
  BitSelector #(.width(16), .group(15)) bitselector_1 (.in(\n8位无符号一位乘法器_封装用_1_乘积 ), .out(\乘积 [14:0]), .sel(1'b0));
  Button \u_复位  (.out(RST));
  Clock clock_1 (.out(CLK));
  Multiplexer #(.width(9), .enable("false")) multiplexer_2 (.in0(9'hba), .in1(9'h92), .out(\Y符号指示 ), .sel(Y[7]));
  // Probe on \乘积 [14:0]
  DotMatrix #(.matrixcols(3), .matrixrows(3)) dotmatrix_3 (
    .col0(\P符号指示 [8:6]), .col1(\P符号指示 [5:3]), .col2(\P符号指示 [2:0]));
  Multiplexer #(.width(9), .enable("false")) multiplexer_3 (.in0(9'hba), .in1(9'h92), .out(\P符号指示 ), .sel(\乘积 [15]));

  // Other names for the same wires on the sheet: P[15:0] = \乘积 ; P_star[14:0] = \乘积 [14:0]; P15 = \乘积 [15];
  //   X_star[6:0] = X[6:0]; Y_star[6:0] = Y[6:0]

  // Notes on the sheet:
  //   输入输出引脚区
  //   8位原码一位乘法器
endmodule

module \_8位无符号一位乘法器_封装用  (
  input  CLK,
  input  [7:0] X,
  input  [7:0] Y,
  input  RST,
  output [15:0] \乘积 
);

  wire comparator_1_eq, d_ff_1_q, not_1_out;
  wire [0:0] \n8位串行加法器_1_s ;
  wire [3:0] counter_1_q;
  wire [7:0] multiplexer_1_out, multiplexer_2_out, \n8位串行加法器_1_cout ;

  // Probe on X
  // Probe on Y
  // Probe on \乘积 [15:8]
  Register #(.Select("low")) register_1 (.D(\n8位串行加法器_1_cout ), .en(not_1_out), .Q(\乘积 [15:8]), .clk(CLK), .clr(RST));
  \_8位串行加法器  \u_8位串行加法器_1  (
    .X(\乘积 [15:8]), .Y(multiplexer_1_out), .Cin(1'b0), .S({\n8位串行加法器_1_cout [6:0], \n8位串行加法器_1_s [0]}),
    .Cout(\n8位串行加法器_1_cout [7]));  // open: out_6
  Multiplexer #(.width(8), .enable("false")) multiplexer_1 (
    .in0({8{1'b0}}), .in1(X), .out(multiplexer_1_out), .sel(\乘积 [0]));
  Multiplexer #(.width(8), .enable("false")) multiplexer_2 (
    .in0(Y), .in1({\n8位串行加法器_1_s [0], \乘积 [7:1]}), .out(multiplexer_2_out), .sel(d_ff_1_q));
  // Probe on \乘积 [7:0]
  Register #(.Select("low")) Y_2 (.D(multiplexer_2_out), .en(not_1_out), .Q(\乘积 [7:0]), .clk(CLK), .clr(RST));
  Counter #(.width(4), .max('hf), .behavior("old")) counter_1 (
    .count(not_1_out), .Q(counter_1_q), .clk(CLK), .clr(RST));  // open: load, D, carry, preset
  D_Flip_Flop #(.Pre_Clr_Positions("LEGACY"), .enable("true"), .NewFFLayout("false")) d_ff_1 (
    .clk(CLK), .D(1'b1), .Q(d_ff_1_q), .reset(RST));  // open: Qn, preset, en
  // Probe on \乘积 
  Comparator #(.width(4), .mode("unsigned")) comparator_1 (
    .a(counter_1_q), .b(4'b1001), .eq(comparator_1_eq));  // open: gt, lt
  not not_1 (not_1_out, comparator_1_eq);
  // Probe on X
  // Probe on Y
  // Probe on \乘积 

  // Notes on the sheet:
  //   输入输出引脚区
  //   ∑
  //   功能说明: 无符号一位乘法器   乘积=X*Y，要求采用原码一位乘法实现，最终结果能输出在乘积引脚上
  //   8位无符号一位乘法器（封装用）
  //   计数及移位控制
  //   ×
  //   =
  //   核心算法：{ ∑ , Y } = { ∑ ＋ Y  |X|  , Y  } / 2
  //   n
endmodule
