// Logisim project 20420192201952+庾晓萍-2.circ as structural Verilog: 4 circuits, main circuit 6位补码阵列乘法器
// 5位阵列乘法器
module \_5位无符号阵列乘法器__横向  (
  input  [4:0] X,
  input  [4:0] Y,
  output [9:0] \乘积 
);

  wire \n1位全加器fa封装2_2_cout , \n1位全加器fa封装2_2_si , \n1位全加器fa封装2_3_cout , \n1位全加器fa封装2_4_cout ,
       \n1位全加器fa封装2_4_si , \n1位全加器fa封装2_5_cout , \n1位全加器fa封装2_5_si , \n1位全加器fa封装2_6_cout ,
       \n1位全加器fa封装2_7_cout , \n1位全加器fa封装2_7_si , \n1位全加器fa封装2_8_cout , \n1位全加器fa封装2_8_si ,
       \n1位全加器fa封装2_9_cout , \n1位全加器fa封装2_9_si , \n1位全加器fa封装2_10_cout , \n1位全加器fa封装2_11_cout ,
       \n1位全加器fa封装2_11_si , \n1位全加器fa封装2_12_cout , \n1位全加器fa封装2_12_si , \n1位全加器fa封装2_13_cout ,
       \n1位全加器fa封装2_13_si , \n1位全加器fa封装2_14_cout , \n1位全加器fa封装2_15_cout , \n1位全加器fa封装2_15_si ,
       \n1位全加器fa封装2_16_cout , \n1位全加器fa封装2_16_si , \n1位全加器fa封装2_17_cout , \n1位全加器fa封装2_18_cout ,
       \n1位全加器fa封装2_18_si , \n1位全加器fa封装2_19_cout , \n1位全加器fa封装2_20_cout , X0Y1, X0Y2, X0Y3, X0Y4, X1Y0, X1Y1,
       X1Y2, X1Y3, X1Y4, X2Y0, X2Y1, X2Y2, X2Y3, X2Y4, X3Y0, X3Y1, X3Y2, X3Y3, X3Y4, X4Y0, X4Y1, X4Y2, X4Y3,
       X4Y4;

  \_1位全加器FA封装2  \u_1位全加器fa封装2_1  (
    .Cout(\乘积 [9]), .Si(\乘积 [8]), .Cin(X4Y4), .Xi(\n1位全加器fa封装2_3_cout ), .Yi(\n1位全加器fa封装2_2_cout ));
  \与门阵列  \u_与门阵列_1  (
    .X(X), .XY4({X4Y4, X3Y4, X2Y4, X1Y4, X0Y4}), .XY3({X4Y3, X3Y3, X2Y3, X1Y3, X0Y3}),
    .XY2({X4Y2, X3Y2, X2Y2, X1Y2, X0Y2}), .XY1({X4Y1, X3Y1, X2Y1, X1Y1, X0Y1}),
    .XY0({X4Y0, X3Y0, X2Y0, X1Y0, \乘积 [0]}), .Y(Y));
  // Probe on X
  \_1位全加器FA封装2  \u_1位全加器fa封装2_2  (
    .Cout(\n1位全加器fa封装2_2_cout ), .Si(\n1位全加器fa封装2_2_si ), .Cin(X4Y3), .Xi(\n1位全加器fa封装2_5_cout ),
    .Yi(\n1位全加器fa封装2_4_cout ));
  \_1位全加器FA封装2  \u_1位全加器fa封装2_3  (
    .Cout(\n1位全加器fa封装2_3_cout ), .Si(\乘积 [7]), .Cin(X3Y4), .Xi(\n1位全加器fa封装2_6_cout ), .Yi(\n1位全加器fa封装2_2_si ));
  \_1位全加器FA封装2  \u_1位全加器fa封装2_4  (
    .Cout(\n1位全加器fa封装2_4_cout ), .Si(\n1位全加器fa封装2_4_si ), .Cin(X4Y2), .Xi(\n1位全加器fa封装2_8_cout ),
    .Yi(\n1位全加器fa封装2_7_cout ));
  \_1位全加器FA封装2  \u_1位全加器fa封装2_5  (
    .Cout(\n1位全加器fa封装2_5_cout ), .Si(\n1位全加器fa封装2_5_si ), .Cin(X3Y3), .Xi(\n1位全加器fa封装2_9_cout ),
    .Yi(\n1位全加器fa封装2_4_si ));
  \_1位全加器FA封装2  \u_1位全加器fa封装2_6  (
    .Cout(\n1位全加器fa封装2_6_cout ), .Si(\乘积 [6]), .Cin(X2Y4), .Xi(\n1位全加器fa封装2_10_cout ), .Yi(\n1位全加器fa封装2_5_si ));
  // Probe on Y
  \_1位全加器FA封装2  \u_1位全加器fa封装2_7  (
    .Cout(\n1位全加器fa封装2_7_cout ), .Si(\n1位全加器fa封装2_7_si ), .Cin(X4Y1), .Xi(\n1位全加器fa封装2_11_cout ), .Yi(1'b0));
  \_1位全加器FA封装2  \u_1位全加器fa封装2_8  (
    .Cout(\n1位全加器fa封装2_8_cout ), .Si(\n1位全加器fa封装2_8_si ), .Cin(X3Y2), .Xi(\n1位全加器fa封装2_12_cout ),
    .Yi(\n1位全加器fa封装2_7_si ));
  \_1位全加器FA封装2  \u_1位全加器fa封装2_9  (
    .Cout(\n1位全加器fa封装2_9_cout ), .Si(\n1位全加器fa封装2_9_si ), .Cin(X2Y3), .Xi(\n1位全加器fa封装2_13_cout ),
    .Yi(\n1位全加器fa封装2_8_si ));
  \_1位全加器FA封装2  \u_1位全加器fa封装2_10  (
    .Cout(\n1位全加器fa封装2_10_cout ), .Si(\乘积 [5]), .Cin(X1Y4), .Xi(\n1位全加器fa封装2_14_cout ),
    .Yi(\n1位全加器fa封装2_9_si ));
  \_1位全加器FA封装2  \u_1位全加器fa封装2_11  (
    .Cout(\n1位全加器fa封装2_11_cout ), .Si(\n1位全加器fa封装2_11_si ), .Cin(X3Y1), .Xi(\n1位全加器fa封装2_15_cout ), .Yi(X4Y0));
  \_1位全加器FA封装2  \u_1位全加器fa封装2_12  (
    .Cout(\n1位全加器fa封装2_12_cout ), .Si(\n1位全加器fa封装2_12_si ), .Cin(X2Y2), .Xi(\n1位全加器fa封装2_16_cout ),
    .Yi(\n1位全加器fa封装2_11_si ));
  \_1位全加器FA封装2  \u_1位全加器fa封装2_13  (
    .Cout(\n1位全加器fa封装2_13_cout ), .Si(\n1位全加器fa封装2_13_si ), .Cin(X1Y3), .Xi(\n1位全加器fa封装2_17_cout ),
    .Yi(\n1位全加器fa封装2_12_si ));
  \_1位全加器FA封装2  \u_1位全加器fa封装2_14  (
    .Cout(\n1位全加器fa封装2_14_cout ), .Si(\乘积 [4]), .Cin(X0Y4), .Xi(1'b0), .Yi(\n1位全加器fa封装2_13_si ));
  \_1位全加器FA封装2  \u_1位全加器fa封装2_15  (
    .Cout(\n1位全加器fa封装2_15_cout ), .Si(\n1位全加器fa封装2_15_si ), .Cin(X2Y1), .Xi(\n1位全加器fa封装2_18_cout ), .Yi(X3Y0));
  \_1位全加器FA封装2  \u_1位全加器fa封装2_16  (
    .Cout(\n1位全加器fa封装2_16_cout ), .Si(\n1位全加器fa封装2_16_si ), .Cin(X1Y2), .Xi(\n1位全加器fa封装2_19_cout ),
    .Yi(\n1位全加器fa封装2_15_si ));
  \_1位全加器FA封装2  \u_1位全加器fa封装2_17  (
    .Cout(\n1位全加器fa封装2_17_cout ), .Si(\乘积 [3]), .Cin(X0Y3), .Xi(1'b0), .Yi(\n1位全加器fa封装2_16_si ));
  // Probe on \乘积 
  \_1位全加器FA封装2  \u_1位全加器fa封装2_18  (
    .Cout(\n1位全加器fa封装2_18_cout ), .Si(\n1位全加器fa封装2_18_si ), .Cin(X1Y1), .Xi(\n1位全加器fa封装2_20_cout ), .Yi(X2Y0));
  \_1位全加器FA封装2  \u_1位全加器fa封装2_19  (
    .Cout(\n1位全加器fa封装2_19_cout ), .Si(\乘积 [2]), .Cin(X0Y2), .Xi(1'b0), .Yi(\n1位全加器fa封装2_18_si ));
  // Probe on X
  // Probe on Y
  // Probe on \乘积 
  \_1位全加器FA封装2  \u_1位全加器fa封装2_20  (.Cout(\n1位全加器fa封装2_20_cout ), .Si(\乘积 [1]), .Cin(X0Y1), .Xi(1'b0), .Yi(X1Y0));

  // Other names for the same wires on the sheet: P[9:0] = \乘积 ; P0 = \乘积 [0]; X0Y0 = \乘积 [0];
  //   XY0[4:0] = {X4Y0, X3Y0, X2Y0, X1Y0, \乘积 [0]}; P1 = \乘积 [1]; P2 = \乘积 [2]; P3 = \乘积 [3]; P4 = \乘积 [4];
  //   P5 = \乘积 [5]; P6 = \乘积 [6]; P7 = \乘积 [7]; P8 = \乘积 [8]; P9 = \乘积 [9]; XY1[4:0] = {X4Y1, X3Y1, X2Y1, X1Y1, X0Y1};
  //   XY2[4:0] = {X4Y2, X3Y2, X2Y2, X1Y2, X0Y2}; XY3[4:0] = {X4Y3, X3Y3, X2Y3, X1Y3, X0Y3};
  //   XY4[4:0] = {X4Y4, X3Y4, X2Y4, X1Y4, X0Y4}

  // Notes on the sheet:
  //   X: pull=down
  //   Y: pull=down
  //   输入引脚区
  //   功能说明：利用一位全加器构成5位×5位的无符号数阵列乘法器，乘积=X×Y，并分析电路延迟；
  //   输出引脚区
  //   5位无符号阵列乘法器（横向）
  //   ×
  //   =
endmodule

module \与门阵列  (
  input  [4:0] X,
  input  [4:0] Y,
  output [4:0] XY0,
  output [4:0] XY1,
  output [4:0] XY2,
  output [4:0] XY3,
  output [4:0] XY4
);

  and and_1 (XY0[4], X[4], Y[0]);
  and and_2 (XY1[4], X[4], Y[1]);
  and and_3 (XY2[4], X[4], Y[2]);
  and and_4 (XY3[4], X[4], Y[3]);
  and and_5 (XY4[4], X[4], Y[4]);
  and and_6 (XY0[3], X[3], Y[0]);
  and and_7 (XY1[3], X[3], Y[1]);
  and and_8 (XY2[3], X[3], Y[2]);
  and and_9 (XY3[3], X[3], Y[3]);
  and and_10 (XY4[3], X[3], Y[4]);
  and and_11 (XY0[2], X[2], Y[0]);
  and and_12 (XY1[2], X[2], Y[1]);
  and and_13 (XY2[2], X[2], Y[2]);
  and and_14 (XY3[2], X[2], Y[3]);
  and and_15 (XY4[2], X[2], Y[4]);
  and and_16 (XY0[1], X[1], Y[0]);
  and and_17 (XY0[0], X[0], Y[0]);
  and and_18 (XY1[1], X[1], Y[1]);
  and and_19 (XY1[0], X[0], Y[1]);
  and and_20 (XY2[0], X[0], Y[2]);
  and and_21 (XY2[1], X[1], Y[2]);
  and and_22 (XY3[0], X[0], Y[3]);
  and and_23 (XY3[1], X[1], Y[3]);
  and and_24 (XY4[0], X[0], Y[4]);
  and and_25 (XY4[1], X[1], Y[4]);

  // Other names for the same wires on the sheet: X0Y0 = XY0[0]; X1Y0 = XY0[1]; X2Y0 = XY0[2]; X3Y0 = XY0[3];
  //   X4Y0 = XY0[4]; X0Y1 = XY1[0]; X1Y1 = XY1[1]; X2Y1 = XY1[2]; X3Y1 = XY1[3]; X4Y1 = XY1[4]; X0Y2 = XY2[0];
  //   X1Y2 = XY2[1]; X2Y2 = XY2[2]; X3Y2 = XY2[3]; X4Y2 = XY2[4]; X0Y3 = XY3[0]; X1Y3 = XY3[1]; X2Y3 = XY3[2];
  //   X3Y3 = XY3[3]; X4Y3 = XY3[4]; X0Y4 = XY4[0]; X1Y4 = XY4[1]; X2Y4 = XY4[2]; X3Y4 = XY4[3]; X4Y4 = XY4[4]

  // Notes on the sheet:
  //   5位乘法与门阵列
endmodule

module \_1位全加器FA封装2  (
  input  Cin,
  input  Xi,
  input  Yi,
  output Cout,
  output Si
);

  wire AND_2_out, AND_out, XOR_2_out;

  or OR (Cout, AND_out, AND_2_out);
  and AND (AND_out, Xi, Yi);
  and AND_2 (AND_2_out, Cin, XOR_2_out);
  xor XOR (Si, Cin, XOR_2_out);
  xor XOR_2 (XOR_2_out, Xi, Yi);

  // Notes on the sheet:
  //   1位全加器（FA）
  //   Si = Xi ^ Yi ^ Cin
  //   Cout = Xi Yi + Cin (Xi ^ Yi)
endmodule

module \_6位补码阵列乘法器  (
  input  [5:0] X,
  input  [5:0] Y,
  input  [11:0] in_3,
  output [11:0] P
);

  wire comparator_1_eq, comparator_2_eq, comparator_3_eq, comparator_4_eq, or_1_out, or_2_out, xor_1_out;
  wire [1:0] multiplexer_1_out;
  wire [4:0] X_t, Y_t;
  wire [5:0] negator_1_out, negator_3_out;
  wire [9:0] multiplexer_3_out, \n5位无符号阵列乘法器_横向_1_p2 , negator_2_out;
  wire [11:0] bit_extender_1_out, bit_extender_2_out, multiplexer_5_out, multiplier_1_out;

  // _5位无符号阵列乘法器__横向 5位无符号阵列乘法器_横向_1: pin names not known; wires that end beside it: X_t, \n5位无符号阵列乘法器_横向_1_p2 , Y_t
  // Probe on X
  xor xor_1 (xor_1_out, Y[5], X[5]);
  Comparator #(.width(6)) comparator_1 (.a(X), .b({6{1'b0}}), .eq(comparator_1_eq));  // open: gt, lt
  Comparator #(.width(6)) comparator_2 (.a(Y), .b({6{1'b0}}), .eq(comparator_2_eq));  // open: gt, lt
  Comparator #(.width(6)) comparator_3 (.a(X), .b(6'b100000), .eq(comparator_3_eq));  // open: gt, lt
  Comparator #(.width(6)) comparator_4 (.a(Y), .b(6'b100000), .eq(comparator_4_eq));  // open: gt, lt
  Negator #(.width(6)) negator_1 (.in(X), .out(negator_1_out));
  Negator #(.width(10)) negator_2 (.in(\n5位无符号阵列乘法器_横向_1_p2 ), .out(negator_2_out));
  Multiplexer #(.width(2), .enable("false")) multiplexer_1 (
    .in0(2'b00), .in1(2'b11), .out(multiplexer_1_out), .sel(xor_1_out));
  // Probe on or_1_out
  or or_1 (or_1_out, comparator_1_eq, comparator_2_eq);
  // Probe on or_2_out
  or or_2 (or_2_out, comparator_3_eq, comparator_4_eq);
  // Probe on Y
  Multiplexer #(.width(5), .enable("false")) multiplexer_2 (
    .in0(X[4:0]), .in1(negator_1_out[4:0]), .out(X_t), .sel(X[5]));
  Multiplexer #(.width(10), .enable("false")) multiplexer_3 (
    .in0(\n5位无符号阵列乘法器_横向_1_p2 ), .in1(negator_2_out), .out(multiplexer_3_out), .sel(xor_1_out));
  assign bit_extender_1_out = {{6{1'b0}}, X};  // Bit_Extender bit_extender_1
  assign bit_extender_2_out = {{6{Y[5]}}, Y};  // Bit_Extender bit_extender_2
  Negator #(.width(6)) negator_3 (.in(Y), .out(negator_3_out));
  Multiplier #(.width(12)) multiplier_1 (
    .a(bit_extender_1_out), .b(bit_extender_2_out), .out(multiplier_1_out));  // open: cin, cout
  // Probe on P
  Multiplexer #(.width(5), .enable("false")) multiplexer_4 (
    .in0(Y[4:0]), .in1(negator_3_out[4:0]), .out(Y_t), .sel(Y[5]));
  Multiplexer #(.width(12), .enable("false")) multiplexer_5 (
    .in0({multiplexer_1_out, multiplexer_3_out}), .in1(multiplier_1_out), .out(multiplexer_5_out),
    .sel(or_2_out));
  // Probe on X
  // Probe on Y
  // Probe on P
  Multiplexer #(.width(12), .enable("false")) multiplexer_6 (
    .in0(multiplexer_5_out), .in1(in_3), .out(P), .sel(or_1_out));

  // Other names for the same wires on the sheet: X4_0[4:0] = X[4:0]; Y4_0[4:0] = Y[4:0]

  // Notes on the sheet:
  //   输入引脚区
  //   功能说明：利用5位无符号阵列乘法器完成6位×6位的原码阵列乘法器，乘积P = X × Y  
  //   6位补码阵列乘法器
  //   输出引脚区
  //   ×
  //   =
endmodule
