// Logisim project 挑战性设计实验.circ as structural Verilog: 7 circuits, main circuit 硬布线控制器（变长指令周期）
module \MIPS单总线处理器数据通路  (
  output [21:0] out_1
);

  wire alu_1_equal, and_1_out, CLK, comparator_1_eq, equal, Mcal, Mex, Mif, not_1_out, RST, T1, T2, T3, T4;
  wire [4:0] registerfile_1_p4, registerfile_1_p5;
  wire [11:0] Clks, \指令数 ;
  wire [31:0] alu_1_result, AR_q, bit_extender_1_out, controlled_buffer_1_out, controlled_buffer_2_out, DR_q,
       IR, PC_q, ram_1_data, registerfile_1_p6, shifter_1_out, X_q, Z_q, \内部总线 ;

  // Probe on \指令数 
  LED led_1 (.in(Mcal));
  LED led_2 (.in(Mif));
  Button u_RST (.out(RST));
  Register #(.width(32), .Select("low")) AR (.D(\内部总线 ), .en(out_1[13]), .Q(AR_q), .clk(CLK));  // open: clr
  // Digital_Oscilloscope #(.nState(35)) digital_oscilloscope_1: pin names not known; wires that end beside it: CLK, Mif, Mcal, Mex, T1, T2, T3, T4, out_1[2]
  LED led_3 (.in(Mex));
  LED led_4 (.in(T1));
  Register #(.width(32), .Select("low")) X (.D(\内部总线 ), .en(out_1[10]), .Q(X_q), .clk(CLK));  // open: clr
  // Probe on Clks
  LED led_5 (.in(T3));
  LED led_6 (.in(T2));
  Clock u_CLK (.out(CLK));
  LED led_7 (.in(T4));
  RAM #(.addrWidth(10), .dataWidth(32), .bus("separate"), .Select("high"), .simpleMode("false")) ram_1 (
    .addr(AR_q[11:2]), .din(controlled_buffer_1_out), .data(ram_1_data), .str(out_1[0]), .clk(CLK),
    .ld(out_1[1]));  // open: sel, clr
  assign controlled_buffer_1_out = out_1[15] ? DR_q : 32'bz;  // Controlled_Buffer controlled_buffer_1
  ALU alu_1 (
    .X(X_q), .Y(\内部总线 ), .Equal(alu_1_equal), .Result(alu_1_result), .ADD(out_1[4]), .ADD4(out_1[3]),
    .SLT(out_1[2]));  // open: SUB
  assign controlled_buffer_2_out = out_1[11] ? \内部总线  : 32'bz;  // Controlled_Buffer controlled_buffer_2
  assign controlled_buffer_2_out = out_1[12] ? ram_1_data : 32'bz;  // Controlled_Buffer controlled_buffer_3
  Register #(.width(32), .Select("low")) PC (.D(\内部总线 ), .en(out_1[14]), .Q(PC_q), .clk(CLK), .clr(RST));
  assign \内部总线  = out_1[21] ? PC_q : 32'bz;  // Controlled_Buffer controlled_buffer_4
  assign \内部总线  = out_1[20] ? DR_q : 32'bz;  // Controlled_Buffer controlled_buffer_5
  Register #(.width(32), .Select("low")) DR (.D(controlled_buffer_2_out), .Q(DR_q), .clk(CLK));  // open: en, clr
  Register #(.width(1), .Select("low")) PSW (.D(alu_1_equal), .en(out_1[7]), .Q(equal), .clk(CLK));  // open: clr
  assign \内部总线  = out_1[19] ? Z_q : 32'bz;  // Controlled_Buffer controlled_buffer_6
  Register #(.width(32), .Select("low")) Z (.D(alu_1_result), .Q(Z_q), .clk(CLK));  // open: en, clr
  Register #(.width(32), .Select("low")) u_IR (.D(\内部总线 ), .en(out_1[8]), .Q(IR), .clk(CLK));  // open: clr
  assign \内部总线  = out_1[17] ? bit_extender_1_out : 32'bz;  // Controlled_Buffer controlled_buffer_7
  assign \内部总线  = out_1[16] ? shifter_1_out : 32'bz;  // Controlled_Buffer controlled_buffer_8
  \硬布线控制器_变长指令周期  \u_硬布线控制器_变长指令周期_1  (
    .\状态节拍信号 ({T4, T3, T2, T1, Mex, Mcal, Mif}), .CLK(CLK), .IR(IR), .ControlBus(out_1), .EQUAL(equal));
  // RegisterFile registerfile_1: pin names not known; wires that end beside it: \内部总线 , CLK, out_1[9], registerfile_1_p4, registerfile_1_p5, registerfile_1_p6
  assign bit_extender_1_out = {{16{IR[15]}}, IR[15:0]};  // Bit_Extender bit_extender_1
  assign \内部总线  = out_1[18] ? registerfile_1_p6 : 32'bz;  // Controlled_Buffer controlled_buffer_9
  Multiplexer #(.width(5), .enable("false")) multiplexer_1 (
    .in0(IR[25:21]), .in1(IR[20:16]), .out(registerfile_1_p5), .sel(out_1[6]));
  Multiplexer #(.width(5), .enable("false")) multiplexer_2 (
    .in0(IR[20:16]), .in1(IR[15:11]), .out(registerfile_1_p4), .sel(out_1[5]));
  not not_1 (not_1_out, comparator_1_eq);
  Comparator #(.width(32)) comparator_1 (.a(IR), .b(32'h1000ffff), .eq(comparator_1_eq));  // open: gt, lt
  Shifter #(.width(32)) shifter_1 (.in(bit_extender_1_out), .\dist (5'b00010), .out(shifter_1_out));
  Counter #(.width(12), .max('hfff), .trigger("falling")) counter_1 (
    .count(not_1_out), .Q(Clks), .clk(CLK));  // open: load, D, carry, clr, preset, down
  and and_1 (and_1_out, not_1_out, Mif, T1);
  Counter #(.width(12), .max('hfff), .trigger("falling"), .behavior("old")) counter_2 (
    .count(and_1_out), .Q(\指令数 ), .clk(CLK));  // open: load, D, carry, clr, preset

  // Other names for the same wires on the sheet: rd[4:0] = IR[15:11]; rt[4:0] = IR[20:16]; rs[4:0] = IR[25:21];
  //   Write = out_1[0]; 控制信号[21:0] = out_1; READ = out_1[1]; Slt = out_1[2]; Add4 = out_1[3]; Add = out_1[4];
  //   RegDst = out_1[5]; RegTgt = out_1[6]; PSWin = out_1[7]; IRin = out_1[8]; Rin = out_1[9]; Xin = out_1[10];
  //   DRin = out_1[11]; DREin = out_1[12]; ARin = out_1[13]; PCin = out_1[14]; DREout = out_1[15];
  //   IR_A_out = out_1[16]; IR_I_out = out_1[17]; Rout = out_1[18]; Zout = out_1[19]; DRout = out_1[20];
  //   PCout = out_1[21]; 状态节拍信号[6:0] = {T4, T3, T2, T1, Mex, Mcal, Mif}

  // Notes on the sheet:
  //   指令数
  //   RAM
  //   外部总线
  //   时钟周期数
  //   内部总线
  //   支持LW、SW、BEQ、SLT、ADDI、ADD等6条指令
  //   三级时序
  //   单总线结构 MIPS 处理器数据通路（硬布线控制器、三级时序、变长指令周期）        支持6条指令
  //   Immidate32
  //   BranchAddress32
endmodule

// 硬布线
module \硬布线控制器_变长指令周期  (
  input  CLK,
  input  [31:0] IR,
  input  EQUAL,
  output [6:0] \状态节拍信号 ,
  output [21:0] ControlBus
);

  wire ADD, ADDI, BEQ, LW, not_1_out, Other;
  wire [3:0] OCInput, register_1_q, \状态机_变长指令周期_1_n0 ;

  Register #(.width(4), .Select("low")) register_1 (
    .D(\状态机_变长指令周期_1_n0 ), .Q(register_1_q), .clk(not_1_out));  // open: en, clr
  not not_1 (not_1_out, CLK);
  \状态机_变长指令周期  \u_状态机_变长指令周期_1  (
    .LW(LW), .SW(OCInput[3]), .BEQ(BEQ), .SLT(OCInput[0]), .ADDI(ADDI), .ADD(ADD), .S3(register_1_q[3]),
    .S2(register_1_q[2]), .S1(register_1_q[1]), .S0(register_1_q[0]), .N3(\状态机_变长指令周期_1_n0 [3]),
    .N2(\状态机_变长指令周期_1_n0 [2]), .N1(\状态机_变长指令周期_1_n0 [1]), .N0(\状态机_变长指令周期_1_n0 [0]));
  // Probe on register_1_q
  // Probe on \状态机_变长指令周期_1_n0 
  \输出函数_变长指令周期  \u_输出函数_变长指令周期_1  (
    .S3(register_1_q[3]), .S2(register_1_q[2]), .S1(register_1_q[1]), .S0(register_1_q[0]),
    .Mif(\状态节拍信号 [0]), .Mcal(\状态节拍信号 [1]), .Mex(\状态节拍信号 [2]), .T1(\状态节拍信号 [3]), .T2(\状态节拍信号 [4]),
    .T3(\状态节拍信号 [5]), .T4(\状态节拍信号 [6]));
  \指令译码器  \u_指令译码器_1  (
    .IR(IR), .LW(LW), .SW(OCInput[3]), .BEQ(BEQ), .ADDI(ADDI), .SLT(OCInput[0]), .OtherInstr(Other), .ADD(ADD));
  \硬布线控制器组合逻辑单元  \u_硬布线控制器组合逻辑单元_1  (
    .SLT(OCInput[0]), .ADDI(ADDI), .LW(LW), .SW(OCInput[3]), .BEQ(BEQ), .Mif(\状态节拍信号 [0]),
    .Mcal(\状态节拍信号 [1]), .Mex(\状态节拍信号 [2]), .T1(\状态节拍信号 [3]), .T2(\状态节拍信号 [4]), .T3(\状态节拍信号 [5]),
    .T4(\状态节拍信号 [6]), .EQUAL(EQUAL), .ADD(ADD), .Pcout(ControlBus[21]), .DRout(ControlBus[20]),
    .Zout(ControlBus[19]), .Rout(ControlBus[18]), .IRiout(ControlBus[17]), .IRaout(ControlBus[16]),
    .DREout(ControlBus[15]), .Pcin(ControlBus[14]), .ARin(ControlBus[13]), .DREin(ControlBus[12]),
    .DRin(ControlBus[11]), .Xin(ControlBus[10]), .Rin(ControlBus[9]), .IRin(ControlBus[8]),
    .PSWin(ControlBus[7]), .RegTgt(ControlBus[6]), .RegDst(ControlBus[5]), .Add_2(ControlBus[4]),
    .Add4(ControlBus[3]), .Slt_2(ControlBus[2]), .READ(ControlBus[1]), .WRITE(ControlBus[0]));

  // Other names for the same wires on the sheet: Write = ControlBus[0]; READ = ControlBus[1]; Slt_t = ControlBus[2];
  //   Add4 = ControlBus[3]; Add_t = ControlBus[4]; RegDst = ControlBus[5]; RegTgt = ControlBus[6];
  //   PSWin = ControlBus[7]; IRin = ControlBus[8]; Rin = ControlBus[9]; Xin = ControlBus[10]; DRin = ControlBus[11];
  //   DREin = ControlBus[12]; ARin = ControlBus[13]; PCin = ControlBus[14]; DREout = ControlBus[15];
  //   IR_A_out = ControlBus[16]; IR_I_out = ControlBus[17]; Rout = ControlBus[18]; Zout = ControlBus[19];
  //   DRout = ControlBus[20]; PCout = ControlBus[21]; SLT = OCInput[0];
  //   OCInput (some bits) = {ADD, EQUAL, \状态节拍信号 , BEQ, LW, ADDI}; SW = OCInput[3]; Mif = \状态节拍信号 [0];
  //   Mcal = \状态节拍信号 [1]; Mex = \状态节拍信号 [2]; T1 = \状态节拍信号 [3]; T2 = \状态节拍信号 [4]; T3 = \状态节拍信号 [5]; T4 = \状态节拍信号 [6];
  //   指令字[31:0] = IR

  // Notes on the sheet:
  //   次态
  //   输入引脚
  //   指令译码信号
  //   现态
  //   状态寄存器
  //   状态机
  //   现态
  //   次态
  //   硬布线控制器（三级时序，变长指令周期）
  //   输出函数
  //   输出引脚
  //   时序发生器
  //   指令译码器
  //   指令译码信号
  //   硬布线控制器组合逻辑单元
  //   硬布线控制器组合逻辑单元
  //   指令译码
endmodule

module \指令译码器  (
  input  [31:0] IR,
  output LW,
  output SW,
  output BEQ,
  output ADDI,
  output SLT,
  output ADD,
  output OtherInstr
);

  wire comparator_5_eq, comparator_6_eq, comparator_7_eq;

  Comparator #(.width(6)) comparator_1 (.a(IR[31:26]), .b(6'b100011), .eq(LW));  // open: gt, lt
  Comparator #(.width(6)) comparator_2 (.a(IR[31:26]), .b(6'b101011), .eq(SW));  // open: gt, lt
  Comparator #(.width(6)) comparator_3 (.a(IR[31:26]), .b(6'b000100), .eq(BEQ));  // open: gt, lt
  Comparator #(.width(6)) comparator_4 (.a(IR[31:26]), .b(6'b001000), .eq(ADDI));  // open: gt, lt
  Comparator #(.width(6)) comparator_5 (.a(IR[31:26]), .b({6{1'b0}}), .eq(comparator_5_eq));  // open: gt, lt
  Comparator #(.width(6)) comparator_6 (.a(IR[5:0]), .b(6'b101010), .eq(comparator_6_eq));  // open: gt, lt
  Comparator #(.width(6)) comparator_7 (.a(IR[5:0]), .b(6'b100000), .eq(comparator_7_eq));  // open: gt, lt
  and and_1 (SLT, comparator_6_eq, comparator_5_eq);
  and and_2 (ADD, comparator_5_eq, comparator_7_eq);
  nor nor_1 (OtherInstr, BEQ, SW, LW, ADDI, SLT, ADD);

  // Other names for the same wires on the sheet: FUNCT[5:0] = IR[5:0]; OP[5:0] = IR[31:26]

  // Notes on the sheet:
  //   输入引脚
  //   指令译码器（ID）
  //   输出引脚
endmodule

// 状态机
module \状态机_变长指令周期  (
  input  LW,
  input  SW,
  input  BEQ,
  input  SLT,
  input  ADDI,
  input  ADD,
  input  S3,
  input  S2,
  input  S1,
  input  S0,
  output N3,
  output N2,
  output N1,
  output N0
);

  wire and_2_out, and_3_out, and_4_out, and_5_out, and_6_out, and_7_out, not_1_out, not_2_out, not_3_out,
       not_4_out, not_5_out, not_6_out, not_7_out, not_8_out, not_9_out, not_10_out, not_11_out, not_12_out,
       not_13_out, not_14_out, not_15_out, not_16_out, not_17_out, not_18_out;

  not not_1 (not_1_out, S3);
  not not_2 (not_2_out, S3);
  not not_3 (not_3_out, S2);
  not not_4 (not_4_out, S3);
  not not_5 (not_5_out, S1);
  not not_6 (not_6_out, S3);
  not not_7 (not_7_out, S0);
  not not_8 (not_8_out, S3);
  not not_9 (not_9_out, S1);
  not not_10 (not_10_out, LW);
  not not_11 (not_11_out, SW);
  not not_12 (not_12_out, BEQ);
  not not_13 (not_13_out, S3);
  not not_14 (not_14_out, S2);
  not not_15 (not_15_out, S3);
  not not_16 (not_16_out, S0);
  not not_17 (not_17_out, S3);
  not not_18 (not_18_out, S0);
  and and_1 (N3, not_1_out, S2, S1, S0);
  and and_2 (and_2_out, not_2_out, not_3_out, S1, S0);
  and and_3 (and_3_out, not_4_out, S2, not_5_out);
  and and_4 (and_4_out, not_6_out, S2, not_7_out);
  and and_5 (and_5_out, not_8_out, not_9_out, S0);
  and and_6 (and_6_out, not_10_out, not_11_out, not_12_out, not_13_out, not_14_out, S1);
  and and_7 (and_7_out, not_15_out, S1, not_16_out);
  and and_8 (N0, not_17_out, not_18_out);
  or or_1 (N2, and_2_out, and_3_out, and_4_out);
  or or_2 (N1, and_5_out, and_6_out, and_7_out);
endmodule

// 输出函数
module \输出函数_变长指令周期  (
  input  S3,
  input  S2,
  input  S1,
  input  S0,
  output Mif,
  output Mcal,
  output Mex,
  output T1,
  output T2,
  output T3,
  output T4
);

  wire and_3_out, and_4_out, and_5_out, and_6_out, and_7_out, and_8_out, and_9_out, and_10_out, and_11_out,
       and_12_out, not_1_out, not_2_out, not_3_out, not_4_out, not_5_out, not_6_out, not_7_out, not_8_out,
       not_9_out, not_10_out, not_11_out, not_12_out, not_13_out, not_14_out, not_15_out, not_16_out,
       not_17_out, not_18_out, not_19_out, not_20_out, not_21_out, not_22_out, not_23_out, not_24_out,
       not_25_out, not_26_out, not_27_out, not_28_out;

  not not_1 (not_1_out, S3);
  and and_1 (Mif, not_1_out, not_2_out);
  not not_2 (not_2_out, S2);
  not not_3 (not_3_out, S3);
  and and_2 (Mcal, not_3_out, S2, not_4_out);
  not not_4 (not_4_out, S1);
  not not_5 (not_5_out, S3);
  not not_6 (not_6_out, S2);
  not not_7 (not_7_out, S1);
  not not_8 (not_8_out, S0);
  not not_9 (not_9_out, S3);
  not not_10 (not_10_out, S1);
  not not_11 (not_11_out, S0);
  not not_12 (not_12_out, S3);
  not not_13 (not_13_out, S0);
  not not_14 (not_14_out, S2);
  not not_15 (not_15_out, S1);
  not not_16 (not_16_out, S3);
  not not_17 (not_17_out, S1);
  not not_18 (not_18_out, S3);
  not not_19 (not_19_out, S2);
  not not_20 (not_20_out, S0);
  not not_21 (not_21_out, S3);
  not not_22 (not_22_out, S2);
  not not_23 (not_23_out, S0);
  not not_24 (not_24_out, S2);
  not not_25 (not_25_out, S1);
  not not_26 (not_26_out, S0);
  not not_27 (not_27_out, S3);
  not not_28 (not_28_out, S2);
  and and_3 (and_3_out, not_5_out, S2, S1);
  or or_1 (Mex, and_3_out, and_4_out);
  and and_4 (and_4_out, S3, not_6_out, not_7_out, not_8_out);
  and and_5 (and_5_out, not_9_out, not_10_out, not_11_out);
  or or_2 (T1, and_5_out, and_6_out, and_7_out);
  and and_6 (and_6_out, not_12_out, S2, not_13_out);
  and and_7 (and_7_out, S3, not_14_out, not_15_out, S0);
  and and_8 (and_8_out, not_16_out, not_17_out, S0);
  or or_3 (T2, and_8_out, and_9_out, and_10_out);
  and and_9 (and_9_out, not_18_out, S2, S0);
  and and_10 (and_10_out, S3, not_19_out, S1, not_20_out);
  and and_11 (and_11_out, not_21_out, not_22_out, S1, not_23_out);
  or or_4 (T3, and_11_out, and_12_out);
  and and_12 (and_12_out, S3, not_24_out, not_25_out, not_26_out);
  and and_13 (T4, not_27_out, not_28_out, S1, S0);

  // Notes on the sheet:
  //   输出函数（变长指令周期）
endmodule

module \硬布线控制器组合逻辑单元  (
  input  SLT,
  input  ADDI,
  input  LW,
  input  SW,
  input  BEQ,
  input  Mif,
  input  Mcal,
  input  Mex,
  input  T1,
  input  T2,
  input  T3,
  input  T4,
  input  EQUAL,
  input  ADD,
  output Pcout,
  output DRout,
  output Zout,
  output Rout,
  output IRiout,
  output IRaout,
  output DREout,
  output Pcin,
  output ARin,
  output DREin,
  output DRin,
  output Xin,
  output Rin,
  output IRin,
  output PSWin,
  output RegTgt,
  output RegDst,
  output Add_2,
  output Add4,
  output Slt_2,
  output READ,
  output WRITE
);

  wire and_1_out, and_2_out, and_3_out, and_4_out, and_5_out, and_6_out, and_7_out, and_8_out, and_9_out,
       and_10_out, and_11_out, and_12_out, and_13_out, and_14_out, and_15_out, and_16_out, and_17_out,
       and_18_out, and_19_out, and_20_out, and_21_out, and_24_out, and_25_out, and_26_out, and_27_out,
       and_28_out, and_29_out, and_30_out, and_32_out, and_33_out, and_34_out, and_35_out, and_36_out,
       and_37_out, and_38_out, and_39_out, and_40_out, and_41_out, and_44_out, and_45_out, and_46_out,
       and_47_out, and_48_out, and_49_out, and_50_out, and_51_out, and_54_out, and_55_out, and_57_out,
       and_58_out, and_59_out, and_60_out, and_61_out, and_62_out, and_63_out, and_64_out;

  and and_1 (and_1_out, Mif, T1);
  and and_2 (and_2_out, BEQ, Mex, T1);
  and and_3 (and_3_out, Mif, T4);
  and and_4 (and_4_out, LW, Mex, T3);
  and and_5 (and_5_out, Mif, T3);
  and and_6 (and_6_out, BEQ, Mex, T3, EQUAL);
  and and_7 (and_7_out, SW, Mex, T1);
  and and_8 (and_8_out, LW, Mex, T1);
  and and_9 (and_9_out, ADDI, Mex, T3);
  and and_10 (and_10_out, SLT, Mex, T3);
  and and_11 (and_11_out, BEQ, Mcal, T2);
  and and_12 (and_12_out, BEQ, Mcal, T1);
  and and_13 (and_13_out, SW, Mex, T2);
  and and_14 (and_14_out, SW, Mcal, T1);
  and and_15 (and_15_out, LW, Mcal, T1);
  and and_16 (and_16_out, ADDI, Mex, T1);
  and and_17 (and_17_out, SLT, Mex, T2);
  and and_18 (and_18_out, SLT, Mex, T1);
  and and_19 (and_19_out, SW, Mcal, T2);
  and and_20 (and_20_out, LW, Mcal, T2);
  and and_21 (and_21_out, ADDI, Mex, T2);
  and and_22 (IRaout, BEQ, Mex, T2);
  and and_23 (DREout, SW, Mex, T3);
  and and_24 (and_24_out, Mif, T3);
  and and_25 (and_25_out, BEQ, Mex, T3, EQUAL);
  and and_26 (and_26_out, Mif, T1);
  and and_27 (and_27_out, SW, Mex, T1);
  and and_28 (and_28_out, LW, Mex, T1);
  and and_29 (and_29_out, Mif, T3);
  and and_30 (and_30_out, LW, Mex, T2);
  and and_31 (DRin, SW, Mex, T2);
  and and_32 (and_32_out, Mif, T1);
  and and_33 (and_33_out, Mcal, T1, LW);
  and and_34 (and_34_out, Mcal, T1, SW);
  and and_35 (and_35_out, Mcal, T1, BEQ);
  and and_36 (and_36_out, Mex, T1, BEQ);
  and and_37 (and_37_out, Mex, T1, SLT);
  and and_38 (and_38_out, Mex, T1, ADDI);
  and and_39 (and_39_out, LW, Mex, T3);
  and and_40 (and_40_out, ADDI, Mex, T3);
  and and_41 (and_41_out, SLT, Mex, T3);
  and and_42 (IRin, Mif, T4);
  and and_43 (PSWin, BEQ, Mcal, T2);
  and and_44 (and_44_out, BEQ, Mcal, T2);
  and and_45 (and_45_out, SW, Mex, T2);
  and and_46 (and_46_out, SLT, Mex, T2);
  and and_47 (and_47_out, SLT, Mex, T3);
  and and_48 (and_48_out, BEQ, Mex, T2);
  and and_49 (and_49_out, SW, Mcal, T2);
  and and_50 (and_50_out, LW, Mcal, T2);
  and and_51 (and_51_out, ADDI, Mex, T2);
  and and_52 (Add4, Mif, T2);
  and and_53 (Slt_2, SLT, Mex, T2);
  and and_54 (and_54_out, Mif, T3);
  and and_55 (and_55_out, LW, Mex, T2);
  and and_56 (WRITE, SW, Mex, T3);
  or or_1 (Pcout, and_1_out, and_2_out);
  or or_2 (DRout, and_3_out, and_4_out);
  or or_3 (Zout, and_5_out, and_6_out, and_7_out, and_8_out, and_9_out, and_10_out, and_57_out);
  and and_57 (and_57_out, Mex, T3, ADD);
  and and_58 (and_58_out, Mex, ADD, T1);
  or or_4 (Rout, and_58_out, and_11_out, and_12_out, and_13_out, and_14_out, and_15_out, and_16_out, and_17_out, and_18_out, and_59_out);
  and and_59 (and_59_out, Mex, ADD, T2);
  or or_5 (IRiout, and_19_out, and_20_out, and_21_out);
  or or_6 (Pcin, and_24_out, and_25_out);
  or or_7 (ARin, and_26_out, and_27_out, and_28_out);
  or or_8 (DREin, and_29_out, and_30_out);
  or or_9 (Xin, and_32_out, and_33_out, and_34_out, and_35_out, and_36_out, and_37_out, and_38_out, and_60_out);
  and and_60 (and_60_out, ADD, T1, Mex);
  or or_10 (Rin, and_39_out, and_40_out, and_41_out, and_61_out);
  and and_61 (and_61_out, ADD, Mex, T3);
  or or_11 (RegTgt, and_44_out, and_45_out, and_46_out, and_62_out);
  and and_62 (and_62_out, Mex, T2, ADD);
  or or_12 (RegDst, and_47_out, and_63_out);
  and and_63 (and_63_out, ADD, T3, Mex);
  or or_13 (Add_2, and_48_out, and_49_out, and_50_out, and_51_out, and_64_out);
  and and_64 (and_64_out, ADD, T2, Mex);
  or or_14 (READ, and_54_out, and_55_out);

  // Notes on the sheet:
  //   硬布线控制器组合逻辑单元
endmodule

module ALU (
  input  ADD,
  input  ADD4,
  input  [31:0] X,
  input  [31:0] Y,
  input  SUB,
  input  SLT,
  output Equal,
  output [31:0] Result
);

  wire [0:0] comparator_1_lt;
  wire [1:0] priority_encoder_1_out;
  wire [31:0] adder_1_out, adder_2_out, subtractor_1_out;

  Pull_Resistor pull_resistor_1 (.node(Y));
  Adder #(.width(32)) adder_1 (.a(X), .b(Y), .out(adder_1_out));  // open: cin, cout
  Adder #(.width(32)) adder_2 (.a(X), .b(32'h4), .out(adder_2_out));  // open: cin, cout
  Subtractor #(.width(32)) subtractor_1 (.a(X), .b(Y), .out(subtractor_1_out));  // open: bin, bout
  Comparator #(.width(32)) comparator_1 (.a(X), .b(Y), .eq(Equal), .lt(comparator_1_lt[0]));  // open: gt
  Priority_Encoder #(.select(2)) priority_encoder_1 (
    .in0(ADD), .in1(ADD4), .in2(SUB), .in3(SLT), .out(priority_encoder_1_out));  // open: gs, en_out, en_in
  Pull_Resistor pull_resistor_2 (.node(priority_encoder_1_out));
  Multiplexer #(.select(2), .width(32), .enable("false")) multiplexer_1 (
    .in0(adder_1_out), .in1(adder_2_out), .in2(subtractor_1_out), .in3({{31{1'b0}}, comparator_1_lt[0]}),
    .out(Result), .sel(priority_encoder_1_out));

  // Notes on the sheet:
  //   输入引脚
  //   算术逻辑单元（ALU）
  //   输出引脚
endmodule
