// Logisim project 单总线结构MIPS处理器（微程序控制器+6条指令）（请同学们在此电路上进行修改）.circ as structural Verilog: 6 circuits, main circuit 单总线MIPS处理器（微程序控制器）
module \单总线MIPS处理器_微程序控制器  (
);

  wire Add, Add4, Addrout, alu_1_equal, and_1_out, ARin, CLK, comparator_1_eq, comparator_2_eq, d_ff_1_qn,
       DREin, DREout, DRin, DRout, EPCin, EPCout, equal, IR_A_out, IR_I_out, IRin, IRQ0, IRQ1, IRQ2, IRQ3,
       not_1_out, PCin, PCout, PSWin, READ, RegDst, RegTgt, Rin, Rout, RST, Slt, Write, Xin, Zout,
       \中断控制器_1_intr , \中断控制器_1_ir0w , \中断控制器_1_ir1w , \中断控制器_1_ir2w , \中断控制器_1_ir3w , \中断请求 ;
  wire [1:0] \中断控制信号 , \中断控制器_1_intno ;
  wire [4:0] registerfile_1_p4, registerfile_1_p5, \微地址_状态 ;
  wire [11:0] \指令数 , \时钟周期数 ;
  wire [31:0] alu_1_result, AR_q, bit_extender_1_out, controlled_buffer_1_out, controlled_buffer_3_out, DR_q,
       EPC_q, IR, multiplexer_3_out, PC_q, ram_1_data, registerfile_1_p6, shifter_1_out, X_q, Z_q, \内部总线 ;

  Button u_RST (.out(RST));
  // Probe on IR
  // Probe on \时钟周期数 
  Register #(.width(32), .Select("low")) AR (.D(\内部总线 ), .en(ARin), .Q(AR_q), .clk(CLK), .clr(RST));
  Clock u_CLK (.out(CLK));
  Register #(.width(32), .Select("low")) X (.D(\内部总线 ), .en(Xin), .Q(X_q), .clk(CLK), .clr(RST));
  // Probe on \微地址_状态 
  // Probe on \指令数 
  RAM #(.addrWidth(10), .dataWidth(32), .bus("separate"), .Select("high")) ram_1 (
    .addr(AR_q[11:2]), .din(controlled_buffer_3_out), .data(ram_1_data), .str(Write), .clk(CLK), .ld(READ));  // open: sel, clr
  ALU alu_1 (
    .X(X_q), .Y(\内部总线 ), .Equal(alu_1_equal), .Result(alu_1_result), .ADD(Add), .ADD4(Add4), .SLT(Slt));  // open: SUB
  assign controlled_buffer_1_out = DRin ? \内部总线  : 32'bz;  // Controlled_Buffer controlled_buffer_1
  assign controlled_buffer_1_out = DREin ? ram_1_data : 32'bz;  // Controlled_Buffer controlled_buffer_2
  assign controlled_buffer_3_out = DREout ? DR_q : 32'bz;  // Controlled_Buffer controlled_buffer_3
  Register #(.width(32), .Select("low")) PC (.D(\内部总线 ), .en(PCin), .Q(PC_q), .clk(CLK), .clr(RST));
  Register #(.width(32), .Select("low")) DR (.D(controlled_buffer_1_out), .Q(DR_q), .clk(CLK), .clr(RST));  // open: en
  Register #(.width(1), .Select("low")) PSW (.D(alu_1_equal), .en(PSWin), .Q(equal), .clk(CLK), .clr(RST));
  Register #(.width(32), .Select("low")) Z (.D(alu_1_result), .Q(Z_q), .clk(CLK), .clr(RST));  // open: en
  assign \内部总线  = PCout ? PC_q : 32'bz;  // Controlled_Buffer controlled_buffer_4
  assign \内部总线  = DRout ? DR_q : 32'bz;  // Controlled_Buffer controlled_buffer_5
  assign \内部总线  = Zout ? Z_q : 32'bz;  // Controlled_Buffer controlled_buffer_6
  assign \内部总线  = IR_I_out ? bit_extender_1_out : 32'bz;  // Controlled_Buffer controlled_buffer_7
  assign \内部总线  = IR_A_out ? shifter_1_out : 32'bz;  // Controlled_Buffer controlled_buffer_8
  Register #(.width(32), .Select("low")) u_IR (.D(\内部总线 ), .en(IRin), .Q(IR), .clk(CLK), .clr(RST));
  Comparator #(.width(32)) comparator_1 (.a(IR), .b(32'h1000ffff), .eq(comparator_1_eq));  // open: gt, lt
  \微程序控制器  \u_微程序控制器_1  (
    .CLK(CLK), .EQUAL(equal), .mAddr(\微地址_状态 ),
    .ControlBus({PCout, DRout, Zout, Rout, IR_I_out, IR_A_out, DREout, PCin, ARin, DREin, DRin, Xin, Rin, IRin, PSWin, RegTgt, RegDst, Add, Add4, Slt, READ, Write}),
    .\指令字 (IR), .RST(RST), .IntR(\中断请求 ), .IntSignals({EPCout, EPCin, Addrout, \中断控制信号 }));
  // RegisterFile registerfile_1: pin names not known; wires that end beside it: \内部总线 , CLK, Rin, registerfile_1_p4, registerfile_1_p5, registerfile_1_p6
  not not_1 (not_1_out, comparator_1_eq);
  Counter #(.width(12), .max('hfff)) counter_1 (
    .count(not_1_out), .Q(\时钟周期数 ), .clk(CLK), .clr(RST));  // open: load, D, carry, preset, down
  assign bit_extender_1_out = {{16{IR[15]}}, IR[15:0]};  // Bit_Extender bit_extender_1
  assign \内部总线  = Rout ? registerfile_1_p6 : 32'bz;  // Controlled_Buffer controlled_buffer_9
  Multiplexer #(.width(5), .enable("false")) multiplexer_1 (
    .in0(IR[25:21]), .in1(IR[20:16]), .out(registerfile_1_p5), .sel(RegTgt));
  Multiplexer #(.width(5), .enable("false")) multiplexer_2 (
    .in0(IR[20:16]), .in1(IR[15:11]), .out(registerfile_1_p4), .sel(RegDst));
  and and_1 (and_1_out, not_1_out, comparator_2_eq);
  Comparator #(.width(5)) comparator_2 (.a(5'b00011), .b(\微地址_状态 ), .eq(comparator_2_eq));  // open: gt, lt
  Shifter #(.width(32)) shifter_1 (.in(bit_extender_1_out), .\dist (5'b00010), .out(shifter_1_out));
  Counter #(.width(12), .max('hfff), .behavior("old")) counter_2 (
    .count(and_1_out), .Q(\指令数 ), .clk(CLK), .clr(RST));  // open: load, D, carry, preset
  D_Flip_Flop #(.Pre_Clr_Positions("LEGACY"), .enable("true"), .NewFFLayout("false")) d_ff_1 (
    .Qn(d_ff_1_qn), .preset(\中断控制信号 [0]), .reset(\中断控制信号 [1]));  // open: clk, D, Q, en
  Button u_IRQ0 (.out(IRQ0));
  Button u_IRQ2 (.out(IRQ2));
  Register #(.width(32), .Select("low")) EPC (.D(\内部总线 ), .en(EPCin), .Q(EPC_q), .clk(CLK), .clr(RST));
  and and_2 (\中断请求 , d_ff_1_qn, \中断控制器_1_intr );
  LED IRQ0_2 (.in(\中断控制器_1_ir0w ));
  \中断控制器  \u_中断控制器_1  (
    .CLK(CLK), .Clr(\中断控制信号 [1]), .Key0(IRQ0), .EDU_TEST(4'b0000), .Key1(IRQ1), .Key2(IRQ2), .Key3(IRQ3),
    .IR0W(\中断控制器_1_ir0w ), .IR1W(\中断控制器_1_ir1w ), .IntNo(\中断控制器_1_intno ), .IntR(\中断控制器_1_intr ),
    .IR2W(\中断控制器_1_ir2w ), .IR3W(\中断控制器_1_ir3w ));
  LED u_IRQ1 (.in(\中断控制器_1_ir1w ));
  LED IRQ2_2 (.in(\中断控制器_1_ir2w ));
  LED u_IRQ3 (.in(\中断控制器_1_ir3w ));
  Button IRQ1_2 (.out(IRQ1));
  Button IRQ3_2 (.out(IRQ3));
  assign \内部总线  = EPCout ? EPC_q : 32'bz;  // Controlled_Buffer controlled_buffer_10
  Multiplexer #(.select(2), .width(32), .enable("false")) multiplexer_3 (
    .in0(32'h400), .in1(32'h600), .in2(32'h800), .in3(32'ha00), .out(multiplexer_3_out), .sel(\中断控制器_1_intno ));
  // Probe on \中断控制器_1_intno 
  assign \内部总线  = Addrout ? multiplexer_3_out : 32'bz;  // Controlled_Buffer controlled_buffer_11

  // Other names for the same wires on the sheet: rd[4:0] = IR[15:11]; rt[4:0] = IR[20:16]; rs[4:0] = IR[25:21];
  //   关中断 = \中断控制信号 [0]; 开中断 = \中断控制信号 [1]; 中断控制信号[4:2] = {EPCout, EPCin, Addrout};
  //   控制总线[21:0] = {PCout, DRout, Zout, Rout, IR_I_out, IR_A_out, DREout, PCin, ARin, DREin, DRin, Xin, Rin, IRin, PSWin, RegTgt, RegDst, Add, Add4, Slt, READ, Write}

  // Notes on the sheet:
  //   MEM
  //   外部总线
  //   内部总线
  //   单总线结构 MIPS 处理器（微程序控制器）数据通路（6条指令）
  //   请将此电路改造成支持中断的数据通路
  //   微程序控制器
  //   Immediate32
  //   AddressOffset32
  //   IRQ0
  //   IRQ1
  //   中断使能寄存器 IE
  //   IRQ3
  //   IRQ2
  //   EPC用于保存断点
  //   送控制器
  //   中断请求信号
  //   执行ERET时开中断，同时清除中断源
  //   中断逻辑
endmodule

// 控制器
module \微程序控制器  (
  input  EQUAL,
  input  [31:0] \指令字 ,
  input  RST,
  input  CLK,
  input  IntR,
  output [4:0] mAddr,
  output [21:0] ControlBus,
  output [4:0] IntSignals
);

  wire ADD, ADDI, BEQ, ERET, LW, not_1_out, Other, P0, P1, P2, SLT, SW;
  wire [1:0] \判别测试逻辑_1_m0 ;
  wire [4:0] adder_1_out, multiplexer_1_out, \微程序入口查找逻辑_1_s0 ;

  \微程序入口查找逻辑  \u_微程序入口查找逻辑_1  (
    .LW(LW), .SW(SW), .BEQ(BEQ), .SLT(SLT), .ADDI(ADDI), .ADD(ADD), .ERET(ERET), .S4(\微程序入口查找逻辑_1_s0 [4]),
    .S3(\微程序入口查找逻辑_1_s0 [3]), .S2(\微程序入口查找逻辑_1_s0 [2]), .S1(\微程序入口查找逻辑_1_s0 [1]), .S0(\微程序入口查找逻辑_1_s0 [0]));
  \判别测试逻辑  \u_判别测试逻辑_1  (
    .P0(P0), .P1(P1), .EQUAL(EQUAL), .IntR(IntR), .P2(P2), .M1(\判别测试逻辑_1_m0 [1]), .M0(\判别测试逻辑_1_m0 [0]));
  Multiplexer #(.select(2), .width(5), .enable("false")) multiplexer_1 (
    .in0(adder_1_out), .in1(\微程序入口查找逻辑_1_s0 ), .in2(5'b11101), .in3({5{1'b0}}), .out(multiplexer_1_out),
    .sel(\判别测试逻辑_1_m0 ));
  Register #(.width(5), .Select("low")) register_1 (
    .D(multiplexer_1_out), .Q(mAddr), .clk(not_1_out), .clr(RST));  // open: en
  not not_1 (not_1_out, CLK);
  Adder #(.width(5)) adder_1 (.a(5'b00001), .b(mAddr), .out(adder_1_out));  // open: cin, cout
  \指令译码器  \u_指令译码器_1  (
    .IR(\指令字 ), .LW(LW), .SW(SW), .BEQ(BEQ), .SLT(SLT), .ADDI(ADDI), .ADD(ADD), .OtherInstr(Other),
    .ERET(ERET));
  ROM #(.addrWidth(5), .dataWidth(30), .Select("high")) rom_1 (
    .addr(mAddr), .data({ControlBus, IntSignals, P0, P1, P2}));

  // Notes on the sheet:
  //   输入引脚
  //   微程序入口查找逻辑
  //   判别测试逻辑
  //   微程序入口
  //   输出引脚
  //   顺序地址
  //   取址入口
  //   中断入口
  //   μAR
  //   中断控制信号
  //   微程序控制器（下址字段法）
  //   请将此电路改造成支持中断的微程序控制器
  //   微地址
  //   控制存储器
  //   指令译码器
  //   contents of rom_1 (hex, n*v repeats v):
  //   20240000 800 8500200 10010004 4040000 2001000 8200000 100200 10020001 4040000 2001000 8200000
  //   4084000 800101 4040000 400c003 20040000 1001000 8400001 4040000 4004400 8022001 4040000 2001000
  //   8020001 4040000 4005000 8022001 400091 20000048 400021
  //   指令译码信号
  //   控制信号
  //   微指令
  //   中断控制信号
  //   指令译码逻辑ID
  //   判断逻辑
endmodule

module \微程序入口查找逻辑  (
  input  LW,
  input  SW,
  input  BEQ,
  input  SLT,
  input  ADDI,
  input  ADD,
  input  ERET,
  output S4,
  output S3,
  output S2,
  output S1,
  output S0
);

  or or_1 (S4, SLT, ADDI, ADD, ERET);
  or or_2 (S3, SW, BEQ, ADD, ERET);
  or or_3 (S2, LW, BEQ, ADDI, ERET);
  or or_4 (S1, BEQ, SLT, ADDI);
  or or_5 (S0, SW, SLT, ADD);
endmodule

module \判别测试逻辑  (
  input  P0,
  input  P1,
  input  EQUAL,
  input  IntR,
  input  P2,
  output M1,
  output M0
);

  wire and_1_out, and_2_out, and_3_out, and_4_out, and_5_out, and_6_out, not_1_out, not_2_out, not_3_out,
       not_4_out, not_5_out, not_6_out, not_7_out, not_8_out, not_9_out, not_10_out, not_11_out, not_12_out,
       not_13_out, not_14_out, not_15_out, not_16_out;

  not not_1 (not_1_out, P0);
  not not_2 (not_2_out, P1);
  not not_3 (not_3_out, P0);
  not not_4 (not_4_out, P1);
  not not_5 (not_5_out, IntR);
  not not_6 (not_6_out, P0);
  not not_7 (not_7_out, EQUAL);
  not not_8 (not_8_out, P0);
  not not_9 (not_9_out, EQUAL);
  not not_10 (not_10_out, IntR);
  not not_11 (not_11_out, P0);
  not not_12 (not_12_out, P1);
  not not_13 (not_13_out, IntR);
  not not_14 (not_14_out, P0);
  not not_15 (not_15_out, EQUAL);
  not not_16 (not_16_out, IntR);
  and and_1 (and_1_out, not_1_out, not_2_out, P2, IntR);
  and and_2 (and_2_out, not_3_out, not_4_out, P2, not_5_out);
  and and_3 (and_3_out, not_6_out, P1, P2, not_7_out, IntR);
  and and_4 (and_4_out, not_8_out, P1, P2, not_9_out, not_10_out);
  and and_5 (and_5_out, not_11_out, not_12_out, P2, not_13_out);
  and and_6 (and_6_out, not_14_out, P1, P2, not_15_out, not_16_out);
  or or_1 (M1, and_1_out, and_2_out, and_3_out, and_4_out);
  or or_2 (M0, P0, and_5_out, and_6_out);
endmodule

module ALU (
  input  ADD,
  input  ADD4,
  input  [31:0] X,
  input  [31:0] Y,
  input  SUB,
  input  SLT,
  output Equal,
  output [31:0] Result
);

  wire [0:0] comparator_1_lt;
  wire [1:0] priority_encoder_1_out;
  wire [31:0] adder_1_out, adder_2_out, subtractor_1_out;

  Pull_Resistor pull_resistor_1 (.node(Y));
  Adder #(.width(32)) adder_1 (.a(X), .b(Y), .out(adder_1_out));  // open: cin, cout
  Adder #(.width(32)) adder_2 (.a(X), .b(32'h4), .out(adder_2_out));  // open: cin, cout
  Subtractor #(.width(32)) subtractor_1 (.a(X), .b(Y), .out(subtractor_1_out));  // open: bin, bout
  Comparator #(.width(32)) comparator_1 (.a(X), .b(Y), .eq(Equal), .lt(comparator_1_lt[0]));  // open: gt
  Priority_Encoder #(.select(2)) priority_encoder_1 (
    .in0(ADD), .in1(ADD4), .in2(SUB), .in3(SLT), .out(priority_encoder_1_out));  // open: gs, en_out, en_in
  Pull_Resistor pull_resistor_2 (.node(priority_encoder_1_out));
  Multiplexer #(.select(2), .width(32), .enable("false")) multiplexer_1 (
    .in0(adder_1_out), .in1(adder_2_out), .in2(subtractor_1_out), .in3({{31{1'b0}}, comparator_1_lt[0]}),
    .out(Result), .sel(priority_encoder_1_out));

  // Notes on the sheet:
  //   算术逻辑运算单元ALU
  //   输入引脚
  //   输出引脚
endmodule

module \指令译码器  (
  input  [31:0] IR,
  output LW,
  output SW,
  output BEQ,
  output SLT,
  output ADDI,
  output ADD,
  output OtherInstr,
  output ERET
);

  wire comparator_6_eq, comparator_7_eq, comparator_8_eq;

  Comparator #(.width(6)) comparator_1 (.a(IR[31:26]), .b(6'b100011), .eq(LW));  // open: gt, lt
  Comparator #(.width(6)) comparator_2 (.a(IR[31:26]), .b(6'b101011), .eq(SW));  // open: gt, lt
  Comparator #(.width(6)) comparator_3 (.a(IR[31:26]), .b(6'b010000), .eq(ERET));  // open: gt, lt
  Comparator #(.width(6)) comparator_4 (.a(IR[31:26]), .b(6'b000100), .eq(BEQ));  // open: gt, lt
  Comparator #(.width(6)) comparator_5 (.a(IR[31:26]), .b(6'b001000), .eq(ADDI));  // open: gt, lt
  Comparator #(.width(6)) comparator_6 (.a(IR[31:26]), .b({6{1'b0}}), .eq(comparator_6_eq));  // open: gt, lt
  Comparator #(.width(6)) comparator_7 (.a(IR[5:0]), .b(6'b101010), .eq(comparator_7_eq));  // open: gt, lt
  Comparator #(.width(6)) comparator_8 (.a(IR[5:0]), .b(6'b100000), .eq(comparator_8_eq));  // open: gt, lt
  and and_1 (SLT, comparator_7_eq, comparator_6_eq);
  and and_2 (ADD, comparator_6_eq, comparator_8_eq);
  nor nor_1 (OtherInstr, LW, SW, BEQ, ERET, SLT, ADDI, ADD);

  // Other names for the same wires on the sheet: FUNCT[5:0] = IR[5:0]; OP[5:0] = IR[31:26]

  // Notes on the sheet:
  //   输入引脚
  //   指令译码器（ID）
  //   请将此电路改造成支持中断的指令译码器
  //   输出引脚
endmodule
