// Logisim project 单总线结构MIPS处理器（微程序控制器+中断+5条指令）.circ as structural Verilog: 8 circuits, main circuit 微程序入口查找逻辑
module \单总线结构MIPS处理器数据通路_微程序_中断  (
);

  wire Add, Add4, Addrout, alu_1_equal, and_2_out, ARin, CLK, comparator_1_eq, comparator_2_eq, d_ff_1_qn,
       DREin, DREout, DRin, DRout, EPCin, EPCout, equal, IR_A_out, IR_I_out, IRin, IRQ0, IRQ1, IRQ2, IRQ3,
       not_1_out, PCin, PCout, PSWin, READ, RegDst, RegTgt, Rin, Rout, RST, Slt, Write, Xin, Zout,
       \中断控制器_1_intr , \中断控制器_1_ir0w , \中断控制器_1_ir1w , \中断控制器_1_ir2w , \中断控制器_1_ir3w , \中断请求 ;
  wire [1:0] \中断控制信号 , \中断控制器_1_intno ;
  wire [4:0] registerfile_1_p5, registerfile_1_p6, \微地址 ;
  wire [11:0] \指令数 , \时钟数 ;
  wire [31:0] alu_1_result, AR_q, bit_extender_1_out, controlled_buffer_1_out, controlled_buffer_3_out, DR_q,
       EPC_q, IR, multiplexer_3_out, PC_q, ram_1_data, registerfile_1_p7, shifter_1_out, X_q, Z_q, \内部总线 ;

  Button u_IRQ0 (.out(IRQ0));
  Button u_IRQ2 (.out(IRQ2));
  // Probe on \微地址 
  // Probe on \时钟数 
  Register #(.width(32), .trigger("rising"), .Select("low")) AR (.D(\内部总线 ), .en(ARin), .Q(AR_q), .clk(CLK), .clr(RST));
  // Probe on IR
  // Probe on \指令数 
  Button u_IRQ1 (.out(IRQ1));
  Button u_IRQ3 (.out(IRQ3));
  Register #(.width(32), .trigger("rising"), .Select("low")) X (.D(\内部总线 ), .en(Xin), .Q(X_q), .clk(CLK), .clr(RST));
  Clock #(.highDuration(1), .lowDuration(1)) clock_1 (.out(CLK));
  Button u_RST (.out(RST));
  RAM #(.addrWidth(10), .dataWidth(32), .bus("separate"), .Select("high")) ram_1 (
    .addr(AR_q[11:2]), .din(controlled_buffer_3_out), .data(ram_1_data), .str(Write), .clk(CLK), .ld(READ));  // open: sel, clr
  ALU alu_1 (
    .X(X_q), .Y(\内部总线 ), .Equal(alu_1_equal), .Result(alu_1_result), .ADD(Add), .ADD4(Add4), .SLT(Slt));  // open: SUB
  assign controlled_buffer_1_out = DRin ? \内部总线  : 32'bz;  // Controlled_Buffer controlled_buffer_1
  assign controlled_buffer_1_out = DREin ? ram_1_data : 32'bz;  // Controlled_Buffer controlled_buffer_2
  assign controlled_buffer_3_out = DREout ? DR_q : 32'bz;  // Controlled_Buffer controlled_buffer_3
  Register #(.width(32), .trigger("rising"), .Select("low")) PC (.D(\内部总线 ), .en(PCin), .Q(PC_q), .clk(CLK), .clr(RST));
  Register #(.width(32), .trigger("rising"), .Select("low")) DR (
    .D(controlled_buffer_1_out), .Q(DR_q), .clk(CLK), .clr(RST));  // open: en
  Register #(.width(1), .trigger("rising"), .Select("low")) PSW (
    .D(alu_1_equal), .en(PSWin), .Q(equal), .clk(CLK), .clr(RST));
  Register #(.width(32), .trigger("rising"), .Select("low")) Z (
    .D(alu_1_result), .Q(Z_q), .clk(CLK), .clr(RST));  // open: en
  assign \内部总线  = PCout ? PC_q : 32'bz;  // Controlled_Buffer controlled_buffer_4
  assign \内部总线  = DRout ? DR_q : 32'bz;  // Controlled_Buffer controlled_buffer_5
  assign \内部总线  = Zout ? Z_q : 32'bz;  // Controlled_Buffer controlled_buffer_6
  assign \内部总线  = IR_I_out ? bit_extender_1_out : 32'bz;  // Controlled_Buffer controlled_buffer_7
  assign \内部总线  = IR_A_out ? shifter_1_out : 32'bz;  // Controlled_Buffer controlled_buffer_8
  Register #(.width(32), .trigger("rising"), .Select("low")) u_IR (.D(\内部总线 ), .en(IRin), .Q(IR), .clk(CLK), .clr(RST));
  \微程序控制器_中断  \u_微程序控制器_中断_1  (
    .EQUAL(equal), .\指令字 (IR), .IntR(\中断请求 ), .CLK(CLK), .RST(RST), .mAddr(\微地址 ),
    .ControlBus({PCout, DRout, Zout, Rout, IR_I_out, IR_A_out, DREout, PCin, ARin, DREin, DRin, Xin, Rin, IRin, PSWin, RegTgt, RegDst, Add, Add4, Slt, READ, Write}),
    .IntSignals({EPCout, EPCin, Addrout, \中断控制信号 }));
  // RegisterFile registerfile_1: pin names not known; wires that end beside it: \内部总线 , CLK, DREout, Rin, registerfile_1_p5, registerfile_1_p6, registerfile_1_p7
  assign bit_extender_1_out = {{16{IR[15]}}, IR[15:0]};  // Bit_Extender bit_extender_1
  assign \内部总线  = Rout ? registerfile_1_p7 : 32'bz;  // Controlled_Buffer controlled_buffer_9
  Multiplexer #(.select(1), .width(5), .disabled("Z"), .enable("false")) multiplexer_1 (
    .in0(IR[25:21]), .in1(IR[20:16]), .out(registerfile_1_p6), .sel(RegTgt));
  Multiplexer #(.select(1), .width(5), .disabled("Z"), .enable("false")) multiplexer_2 (
    .in0(IR[20:16]), .in1(IR[15:11]), .out(registerfile_1_p5), .sel(RegDst));
  Shifter #(.width(32), .shift("ll")) shifter_1 (.in(bit_extender_1_out), .\dist (5'b00010), .out(shifter_1_out));
  Comparator #(.width(32), .mode("twosComplement")) comparator_1 (
    .a(IR), .b(32'h1000ffff), .eq(comparator_1_eq));  // open: gt, lt
  not not_1 (not_1_out, comparator_1_eq);
  D_Flip_Flop #(.trigger("rising"), .Pre_Clr_Positions("LEGACY"), .NegatePresetClear("false"), .enable("true"), .NewFFLayout("false")) d_ff_1 (
    .Qn(d_ff_1_qn), .preset(\中断控制信号 [0]), .reset(\中断控制信号 [1]));  // open: clk, D, Q, en
  Counter #(.width(12), .max('hfff), .ongoal("wrap"), .trigger("falling"), .behavior("new")) counter_1 (
    .count(not_1_out), .Q(\时钟数 ), .clk(CLK), .clr(RST));  // open: load, D, carry, preset, down
  Register #(.width(32), .trigger("rising"), .Select("low")) EPC (
    .D(\内部总线 ), .en(EPCin), .Q(EPC_q), .clk(CLK), .clr(RST));
  and and_1 (\中断请求 , d_ff_1_qn, \中断控制器_1_intr );
  \中断控制器  \u_中断控制器_1  (
    .CLK(CLK), .Clr(\中断控制信号 [1]), .Key0(IRQ0), .EDU_TEST(4'b0000), .Key1(IRQ1), .Key2(IRQ2), .Key3(IRQ3),
    .IR0W(\中断控制器_1_ir0w ), .IR1W(\中断控制器_1_ir1w ), .IntNo(\中断控制器_1_intno ), .IntR(\中断控制器_1_intr ),
    .IR2W(\中断控制器_1_ir2w ), .IR3W(\中断控制器_1_ir3w ));
  LED #(.active("true")) IRQ0_2 (.in(\中断控制器_1_ir0w ));
  LED #(.active("true")) IRQ1_2 (.in(\中断控制器_1_ir1w ));
  LED #(.active("true")) IRQ2_2 (.in(\中断控制器_1_ir2w ));
  LED #(.active("true")) IRQ3_2 (.in(\中断控制器_1_ir3w ));
  assign \内部总线  = EPCout ? EPC_q : 32'bz;  // Controlled_Buffer controlled_buffer_10
  Multiplexer #(.select(2), .width(32), .disabled("Z"), .enable("false")) multiplexer_3 (
    .in0(32'h400), .in1(32'h600), .in2(32'h800), .in3(32'ha00), .out(multiplexer_3_out), .sel(\中断控制器_1_intno ));
  // Probe on \中断控制器_1_intno 
  assign \内部总线  = Addrout ? multiplexer_3_out : 32'bz;  // Controlled_Buffer controlled_buffer_11
  Comparator #(.width(5), .mode("twosComplement")) comparator_2 (
    .a(5'b00011), .b(\微地址 ), .eq(comparator_2_eq));  // open: gt, lt
  Counter #(.width(12), .max('hfff), .ongoal("wrap"), .trigger("falling"), .behavior("old")) counter_2 (
    .count(and_2_out), .Q(\指令数 ), .clk(CLK), .clr(RST));  // open: load, D, carry, preset
  and and_2 (and_2_out, not_1_out, comparator_2_eq);

  // Other names for the same wires on the sheet: rd[4:0] = IR[15:11]; rt[4:0] = IR[20:16]; rs[4:0] = IR[25:21];
  //   关中断 = \中断控制信号 [0]; 开中断 = \中断控制信号 [1]; 中断控制信号[4:2] = {EPCout, EPCin, Addrout};
  //   控制总线[21:0] = {PCout, DRout, Zout, Rout, IR_I_out, IR_A_out, DREout, PCin, ARin, DREin, DRin, Xin, Rin, IRin, PSWin, RegTgt, RegDst, Add, Add4, Slt, READ, Write}

  // Notes on the sheet:
  //   RAM
  //   外部总线
  //   内部总线
  //   单总线结构 MIPS 处理器数据通路（微程序+中断）
  //   微程序+中断
  //   Immidate32
  //   BranchAddress32
  //   IRQ1
  //   IRQ0
  //   中断使能寄存器 IE
  //   IRQ3
  //   IRQ2
  //   EPC用于保存断点
  //   送控制器
  //   中断请求信号
  //   执行ERET时开中断，同时清除中断源
  //   中断逻辑
endmodule

// 控制器
module \微程序控制器_中断  (
  input  EQUAL,
  input  [31:0] \指令字 ,
  input  IntR,
  input  CLK,
  input  RST,
  output [4:0] mAddr,
  output [21:0] ControlBus,
  output [4:0] IntSignals
);

  wire ADDI, BEQ, ERET, LW, Other, P0, P1, P2, SLT, SW;
  wire [1:0] \判别测试_1_m0 ;
  wire [4:0] adder_1_out, multiplexer_1_out, \微程序入口查找逻辑_1_s0 ;

  \微程序入口查找逻辑  \u_微程序入口查找逻辑_1  (
    .LW(LW), .S4(\微程序入口查找逻辑_1_s0 [4]), .SW(SW), .S3(\微程序入口查找逻辑_1_s0 [3]), .BEQ(BEQ),
    .S2(\微程序入口查找逻辑_1_s0 [2]), .SLT(SLT), .S1(\微程序入口查找逻辑_1_s0 [1]), .S0(\微程序入口查找逻辑_1_s0 [0]), .ADDI(ADDI),
    .ERET(ERET));
  \判别测试  \u_判别测试_1  (.P0(P0), .P1(P1), .P2(P2), .EQUAL(EQUAL), .M1(\判别测试_1_m0 [1]), .IntR(IntR), .M0(\判别测试_1_m0 [0]));
  Multiplexer #(.select(2), .width(5), .disabled("Z"), .enable("false")) multiplexer_1 (
    .in0(adder_1_out), .in1(\微程序入口查找逻辑_1_s0 ), .in2(5'b11010), .in3({5{1'b0}}), .out(multiplexer_1_out),
    .sel(\判别测试_1_m0 ));
  Register #(.width(5), .trigger("falling"), .Select("low")) register_1 (
    .D(multiplexer_1_out), .Q(mAddr), .clk(CLK), .clr(RST));  // open: en
  Adder #(.width(5)) adder_1 (.a(5'b00001), .b(mAddr), .out(adder_1_out));  // open: cin, cout
  \指令译码器  \u_指令译码器_1  (
    .IR(\指令字 ), .LW(LW), .SW(SW), .BEQ(BEQ), .ADDI(ADDI), .SLT(SLT), .ERET(ERET), .OtherInstr(Other));
  ROM #(.addrWidth(5), .dataWidth(30), .Select("high")) rom_1 (
    .addr(mAddr), .data({ControlBus, IntSignals, P0, P1, P2}));

  // Notes on the sheet:
  //   输入引脚
  //   微程序入口查找逻辑
  //   执行阶段微程序入口地址
  //   中断响应入口地址
  //   顺序地址
  //   取指阶段微程序入口地址
  //   判别测试逻辑
  //   微地址
  //   μAR
  //   输出引脚
  //   控制信号
  //   中断控制信号
  //   支持中断的微程序控制器（计数器法）
  //   微地址
  //   指令译码器
  //   控制存储器
  //   contents of rom_1 (hex, n*v repeats v):
  //   20240000 800 8500200 10010004 4040000 2001000 8200000 100200 10020001 4040000 2001000 8200000
  //   4084000 800101 4040000 400c003 20040000 1001000 8400001 4040000 4004400 8022001 4040000 2001000
  //   8020001 400091 20000048 400021
  //   指令译码信号
  //   控制信号
  //   微指令
  //   指令译码逻辑ID
  //   中断控制信号
  //   判断逻辑
endmodule

module \指令译码器  (
  input  [31:0] IR,
  output LW,
  output SW,
  output BEQ,
  output SLT,
  output ADDI,
  output ERET,
  output OtherInstr
);

  wire comparator_6_eq, comparator_7_eq;

  Comparator #(.width(6), .mode("twosComplement")) comparator_1 (
    .a(IR[31:26]), .b(6'b100011), .eq(LW));  // open: gt, lt
  Comparator #(.width(6), .mode("twosComplement")) comparator_2 (
    .a(IR[31:26]), .b(6'b101011), .eq(SW));  // open: gt, lt
  Comparator #(.width(6), .mode("twosComplement")) comparator_3 (
    .a(IR[31:26]), .b(6'b010000), .eq(ERET));  // open: gt, lt
  Comparator #(.width(6), .mode("twosComplement")) comparator_4 (
    .a(IR[31:26]), .b(6'b000100), .eq(BEQ));  // open: gt, lt
  Comparator #(.width(6), .mode("twosComplement")) comparator_5 (
    .a(IR[31:26]), .b(6'b001000), .eq(ADDI));  // open: gt, lt
  Comparator #(.width(6), .mode("twosComplement")) comparator_6 (
    .a(IR[31:26]), .b({6{1'b0}}), .eq(comparator_6_eq));  // open: gt, lt
  Comparator #(.width(6), .mode("twosComplement")) comparator_7 (
    .a(IR[5:0]), .b(6'b101010), .eq(comparator_7_eq));  // open: gt, lt
  and and_1 (SLT, comparator_7_eq, comparator_6_eq);
  nor nor_1 (OtherInstr, LW, SW, BEQ, SLT, ADDI, ERET);

  // Other names for the same wires on the sheet: FUNCT[5:0] = IR[5:0]; OP[5:0] = IR[31:26]
endmodule

// 入口查找
module \微程序入口查找逻辑  (
  input  LW,
  input  SW,
  input  BEQ,
  input  SLT,
  input  ADDI,
  input  ERET,
  output S4,
  output S3,
  output S2,
  output S1,
  output S0
);

  or or_1 (S4, SLT, ADDI, ERET);
  or or_2 (S3, SW, BEQ, ERET);
  or or_3 (S2, LW, BEQ, ADDI);
  or or_4 (S1, BEQ, SLT, ADDI);
  or or_5 (S0, SW, SLT, ERET);
endmodule

module \判别测试  (
  input  P0,
  input  P1,
  input  P2,
  input  EQUAL,
  input  IntR,
  output M1,
  output M0
);

  wire and_1_out, and_2_out, and_3_out, and_4_out, and_5_out, and_6_out, not_1_out, not_2_out, not_3_out,
       not_4_out, not_5_out, not_6_out, not_7_out, not_8_out, not_9_out, not_10_out, not_11_out, not_12_out,
       not_13_out, not_14_out, not_15_out, not_16_out;

  not not_1 (not_1_out, P0);
  not not_2 (not_2_out, P1);
  not not_3 (not_3_out, P0);
  not not_4 (not_4_out, P1);
  not not_5 (not_5_out, IntR);
  not not_6 (not_6_out, P0);
  not not_7 (not_7_out, EQUAL);
  not not_8 (not_8_out, P0);
  not not_9 (not_9_out, EQUAL);
  not not_10 (not_10_out, IntR);
  not not_11 (not_11_out, P0);
  not not_12 (not_12_out, P1);
  not not_13 (not_13_out, IntR);
  not not_14 (not_14_out, P0);
  not not_15 (not_15_out, EQUAL);
  not not_16 (not_16_out, IntR);
  and and_1 (and_1_out, not_1_out, not_2_out, P2, IntR);
  and and_2 (and_2_out, not_3_out, not_4_out, P2, not_5_out);
  and and_3 (and_3_out, not_6_out, P1, P2, not_7_out, IntR);
  and and_4 (and_4_out, not_8_out, P1, P2, not_9_out, not_10_out);
  and and_5 (and_5_out, not_11_out, not_12_out, P2, not_13_out);
  and and_6 (and_6_out, not_14_out, P1, P2, not_15_out, not_16_out);
  or or_1 (M1, and_1_out, and_2_out, and_3_out, and_4_out);
  or or_2 (M0, P0, and_5_out, and_6_out);
endmodule

module ALU (
  input  ADD,
  input  ADD4,
  input  [31:0] X,
  input  [31:0] Y,
  input  SUB,
  input  SLT,
  output Equal,
  output [31:0] Result
);

  wire [0:0] comparator_1_lt;
  wire [1:0] priority_encoder_1_out;
  wire [31:0] adder_1_out, adder_2_out, subtractor_1_out;

  Pull_Resistor #(.pull(0)) pull_resistor_1 (.node(Y));
  Adder #(.width(32)) adder_1 (.a(X), .b(Y), .out(adder_1_out));  // open: cin, cout
  Adder #(.width(32)) adder_2 (.a(X), .b(32'h4), .out(adder_2_out));  // open: cin, cout
  Subtractor #(.width(32)) subtractor_1 (.a(X), .b(Y), .out(subtractor_1_out));  // open: bin, bout
  Comparator #(.width(32), .mode("twosComplement")) comparator_1 (
    .a(X), .b(Y), .eq(Equal), .lt(comparator_1_lt[0]));  // open: gt
  Priority_Encoder #(.select(2), .disabled("Z")) priority_encoder_1 (
    .in0(ADD), .in1(ADD4), .in2(SUB), .in3(SLT), .out(priority_encoder_1_out));  // open: gs, en_out, en_in
  Pull_Resistor #(.pull(0)) pull_resistor_2 (.node(priority_encoder_1_out));
  Multiplexer #(.select(2), .width(32), .disabled("Z"), .enable("false")) multiplexer_1 (
    .in0(adder_1_out), .in1(adder_2_out), .in2(subtractor_1_out), .in3({{31{1'b0}}, comparator_1_lt[0]}),
    .out(Result), .sel(priority_encoder_1_out));

  // Notes on the sheet:
  //   算术逻辑运算单元ALU
  //   输入引脚
  //   输出引脚
endmodule

module \中断控制器  (
  input  CLK,
  input  Clr,
  input  Key0,
  input  [3:0] EDU_TEST,
  input  Key1,
  input  Key2,
  input  Key3,
  output IR0W,
  output IR1W,
  output [1:0] IntNo,
  output IntR,
  output IR2W,
  output IR3W
);

  wire and_1_out, and_2_out, and_3_out, and_4_out, Clr0, Clr1, Clr2, Clr3, d_ff_1_q, d_ff_2_q, d_ff_3_q,
       d_ff_4_q, IR0_q, IR1_q, IR2_q, IR3_q, or_1_out, or_3_out, or_5_out, or_7_out, or_9_out, or_10_out,
       or_11_out, or_12_out;

  or or_1 (or_1_out, Key0, EDU_TEST[3]);
  or or_2 (IR0W, IR0_q, d_ff_2_q);
  or or_3 (or_3_out, Key1, EDU_TEST[2]);
  or or_4 (IR1W, IR1_q, d_ff_3_q);
  D_Flip_Flop #(.trigger("rising"), .Pre_Clr_Positions("LEGACY"), .NegatePresetClear("false"), .enable("true"), .NewFFLayout("false")) d_ff_1 (
    .clk(or_5_out), .D(1'b1), .Q(d_ff_1_q), .reset(IR2_q));  // open: Qn, preset, en
  or or_5 (or_5_out, Key2, EDU_TEST[1]);
  or or_6 (IR2W, IR2_q, d_ff_1_q);
  or or_7 (or_7_out, Key3, EDU_TEST[0]);
  or or_8 (IR3W, IR3_q, d_ff_4_q);
  D_Flip_Flop #(.trigger("rising"), .Pre_Clr_Positions("LEGACY"), .NegatePresetClear("false"), .enable("true"), .NewFFLayout("false")) d_ff_2 (
    .clk(or_1_out), .D(1'b1), .Q(d_ff_2_q), .reset(IR0_q));  // open: Qn, preset, en
  D_Flip_Flop #(.trigger("rising"), .Pre_Clr_Positions("LEGACY"), .NegatePresetClear("false"), .enable("true"), .NewFFLayout("false")) d_ff_3 (
    .clk(or_3_out), .D(1'b1), .Q(d_ff_3_q), .reset(IR1_q));  // open: Qn, preset, en
  D_Flip_Flop #(.trigger("rising"), .Pre_Clr_Positions("LEGACY"), .NegatePresetClear("false"), .enable("true"), .NewFFLayout("false")) d_ff_4 (
    .clk(or_7_out), .D(1'b1), .Q(d_ff_4_q), .reset(IR3_q));  // open: Qn, preset, en
  Pull_Resistor #(.pull(0)) pull_resistor_1 (.node(EDU_TEST));
  or or_9 (or_9_out, d_ff_2_q, IR0_q);
  and and_1 (and_1_out, or_9_out, ~Clr0);  // AND_Gate
  or or_10 (or_10_out, d_ff_3_q, IR1_q);
  and and_2 (and_2_out, or_10_out, ~Clr1);  // AND_Gate
  or or_11 (or_11_out, d_ff_1_q, IR2_q);
  and and_3 (and_3_out, or_11_out, ~Clr2);  // AND_Gate
  or or_12 (or_12_out, d_ff_4_q, IR3_q);
  and and_4 (and_4_out, or_12_out, ~Clr3);  // AND_Gate
  D_Flip_Flop #(.trigger("rising"), .Pre_Clr_Positions("LEGACY"), .NegatePresetClear("false"), .enable("true"), .NewFFLayout("false")) IR0 (
    .clk(CLK), .D(and_1_out), .Q(IR0_q));  // open: Qn, preset, en, reset
  D_Flip_Flop #(.trigger("rising"), .Pre_Clr_Positions("LEGACY"), .NegatePresetClear("false"), .enable("true"), .NewFFLayout("false")) IR1 (
    .clk(CLK), .D(and_2_out), .Q(IR1_q));  // open: Qn, preset, en, reset
  D_Flip_Flop #(.trigger("rising"), .Pre_Clr_Positions("LEGACY"), .NegatePresetClear("false"), .enable("true"), .NewFFLayout("false")) IR2 (
    .clk(CLK), .D(and_3_out), .Q(IR2_q));  // open: Qn, preset, en, reset
  D_Flip_Flop #(.trigger("rising"), .Pre_Clr_Positions("LEGACY"), .NegatePresetClear("false"), .enable("true"), .NewFFLayout("false")) IR3 (
    .clk(CLK), .D(and_4_out), .Q(IR3_q));  // open: Qn, preset, en, reset
  Priority_Encoder #(.select(2), .disabled("Z")) priority_encoder_1 (
    .in0(IR0_q), .in1(IR1_q), .in2(IR2_q), .in3(IR3_q), .out(IntNo), .gs(IntR));  // open: en_out, en_in
  Decoder #(.select(2), .tristate("false"), .disabled(0), .enable("true")) decoder_1 (
    .out0(Clr0), .out1(Clr1), .out2(Clr2), .out3(Clr3), .sel(IntNo), .en(Clr));

  // Other names for the same wires on the sheet: EDU_INT3 = EDU_TEST[0]; EDU_INT2 = EDU_TEST[1];
  //   EDU_INT1 = EDU_TEST[2]; EDU_INT0 = EDU_TEST[3]

  // Notes on the sheet:
  //   中断等待
  //   中断等待
  //   中断等待
  //   中断等待
  //   Reset 
  //   Reset 
  //   Reset 
  //   Reset 
  //   中断优先编码器
  //   中断控制器
endmodule

module Test (
  input  [5:0] in_1,
  input  [4:0] in_2,
  input  [2:0] in_3,
  input  in_4,
  input  in_5,
  input  in_6,
  input  in_7,
  input  in_8,
  input  [3:0] in_9,
  output [4:0] out_10,
  output [1:0] out_11,
  output [5:0] out_12,
  output [1:0] out_13
);

  wire clock_1_out;
  wire [31:0] multiplexer_1_out;

  \微程序入口查找逻辑  \u_微程序入口查找逻辑_1  (
    .LW(in_1[5]), .S4(out_10[4]), .SW(in_1[4]), .S3(out_10[3]), .BEQ(in_1[3]), .S2(out_10[2]), .SLT(in_1[2]),
    .S1(out_10[1]), .S0(out_10[0]), .ADDI(in_1[1]), .ERET(in_1[0]));
  // Probe on out_10
  Clock #(.highDuration(1), .lowDuration(1)) clock_1 (.out(clock_1_out));
  \中断控制器  \u_中断控制器_1  (
    .CLK(clock_1_out), .Clr(in_8), .Key0(in_4), .EDU_TEST(in_9), .Key1(in_5), .Key2(in_6), .Key3(in_7),
    .IntNo(out_13));  // open: IR0W, IR1W, IntR, IR2W, IR3W
  \判别测试  \u_判别测试_1  (
    .P0(in_2[4]), .P1(in_2[3]), .P2(in_2[2]), .EQUAL(in_2[1]), .M1(out_11[1]), .IntR(in_2[0]), .M0(out_11[0]));
  Multiplexer #(.select(3), .width(32), .disabled("Z"), .enable("false")) multiplexer_1 (
    .in0({32{1'b0}}), .in1({32{1'b0}}), .in2({32{1'b0}}), .in3({32{1'b0}}), .in4({32{1'b0}}),
    .in5({32{1'b0}}), .out(multiplexer_1_out), .sel(in_3));  // open: in6, in7
  \指令译码器  \u_指令译码器_1  (
    .IR(multiplexer_1_out), .LW(out_12[5]), .SW(out_12[4]), .BEQ(out_12[3]), .ADDI(out_12[1]),
    .SLT(out_12[2]), .ERET(out_12[0]));  // open: OtherInstr
endmodule
